// Logisim project 第4关：多级嵌套中断(EPC内存堆栈保存).circ as structural Verilog: 23 circuits, main circuit ◇单周期MIPS
module \单周期MIPS  (
  output RegWrite,
  output MemWrite,
  output [31:0] PC,
  output [31:0] IR,
  output [31:0] RDin,
  output [31:0] MDin,
  output [31:0] LedData
);

  wire and_1_out, and_2_out, and_3_out, and_4_out, and_5_out, BranchJump, CLK, comparator_1_eq,
       demultiplexer_1_out0, demultiplexer_1_out1, Go, IR1, IR2, IR3, JAL, JALJMPJump, mips_alu_1_equal,
       multiplexer_6_out, NormalJump, not_1_out, not_2_out, or_2_out, or_4_out, PCEnable, register_2_q,
       RegJump, RST, SignedExt, Syscall, W1, W2, W3, \单周期硬布线控制器_1_alu_src , \单周期硬布线控制器_1_beq ,
       \单周期硬布线控制器_1_blez , \单周期硬布线控制器_1_bne , \单周期硬布线控制器_1_eret , \单周期硬布线控制器_1_jmp , \单周期硬布线控制器_1_mfc0 ,
       \单周期硬布线控制器_1_mtc0 , \单周期硬布线控制器_1_readmode , \单周期硬布线控制器_1_regdst ;
  wire [0:0] IE_q;
  wire [1:0] \单周期硬布线控制器_1_memtoreg ;
  wire [2:0] IMW_q;
  wire [3:0] \单周期硬布线控制器_1_alu_op ;
  wire [4:0] multiplexer_1_out, multiplexer_3_out;
  wire [7:0] multiplexer_8_out, ram_1_data, ram_2_data, ram_3_data, ram_4_data;
  wire [9:0] multiplexer_2_out;
  wire [15:0] adder_2_out, \总周期数 ;
  wire [27:0] NextPC;
  wire [31:0] bit_extender_1_out, bit_extender_2_out, bit_extender_3_out, bit_extender_4_out, BranchAddr,
       controlled_buffer_1_out, JMPJALAddress, mips_alu_1_result, multiplexer_4_out, multiplexer_5_out,
       multiplexer_7_out, multiplexer_9_out, multiplexer_10_out, R1, shifter_2_out;
  wire [31:28] shifter_1_out;

  Clock clock_1 (.out(CLK));
  Button _1 (.out(IR1));
  Button _2 (.out(IR2));
  Button _3 (.out(IR3));
  Button \u_继续运行  (.out(Go));
  LED led_1 (.in(W1));
  LED led_2 (.in(W2));
  LED led_3 (.in(W3));
  Button button_1 (.out(RST));
  Hex_Digit_Display hex_digit_display_1 (.value(LedData[31:28]));  // open: dp
  assign controlled_buffer_1_out = JALJMPJump ? JMPJALAddress : 32'bz;  // Controlled_Buffer controlled_buffer_1
  assign controlled_buffer_1_out = RegJump ? R1 : 32'bz;  // Controlled_Buffer controlled_buffer_2
  assign controlled_buffer_1_out = BranchJump ? BranchAddr : 32'bz;  // Controlled_Buffer controlled_buffer_3
  assign controlled_buffer_1_out = NormalJump ? {JMPJALAddress[31:28], NextPC} : 32'bz;  // Controlled_Buffer controlled_buffer_4
  Register #(.width(32)) u_PC (.D(controlled_buffer_1_out), .en(PCEnable), .Q(PC), .clk(CLK), .clr(RST));
  Hex_Digit_Display hex_digit_display_2 (.value(LedData[23:20]));  // open: dp
  Hex_Digit_Display hex_digit_display_3 (.value(LedData[27:24]));  // open: dp
  Adder #(.width(32)) adder_1 (.a(PC), .b(32'h4), .out({JMPJALAddress[31:28], NextPC}));  // open: cin, cout
  Register #(.width(16)) register_1 (.D(adder_2_out), .en(PCEnable), .Q(\总周期数 ), .clk(CLK), .clr(RST));
  Hex_Digit_Display hex_digit_display_4 (.value(LedData[15:12]));  // open: dp
  Hex_Digit_Display hex_digit_display_5 (.value(LedData[19:16]));  // open: dp
  ROM #(.addrWidth(10), .dataWidth(32)) rom_1 (.addr(PC[11:2]), .data(IR));  // open: sel
  Adder #(.width(16)) adder_2 (.a(16'h1), .b(\总周期数 ), .out(adder_2_out));  // open: cin, cout
  Hex_Digit_Display hex_digit_display_6 (.value(LedData[11:8]));  // open: dp
  Hex_Digit_Display hex_digit_display_7 (.value(LedData[7:4]));  // open: dp
  // Probe on \总周期数 
  nor nor_1 (NormalJump, RegJump, JALJMPJump, BranchJump);
  or or_1 (JALJMPJump, JAL, \单周期硬布线控制器_1_jmp );
  Hex_Digit_Display hex_digit_display_8 (.value(LedData[3:0]));  // open: dp
  not not_1 (not_1_out, PCEnable);
  Multiplexer #(.width(5), .enable("false")) multiplexer_1 (
    .in0(IR[20:16]), .in1(IR[15:11]), .out(multiplexer_1_out), .sel(\单周期硬布线控制器_1_regdst ));
  assign bit_extender_1_out = {{16{1'b0}}, IR[15:0]};  // Bit_Extender bit_extender_1
  assign bit_extender_2_out = {{16{IR[15]}}, IR[15:0]};  // Bit_Extender bit_extender_2
  assign bit_extender_3_out = {{6{IR[25]}}, IR[25:0]};  // Bit_Extender bit_extender_3
  \单周期硬布线控制器  \u_单周期硬布线控制器_1  (
    .Func(IR[5:0]), .OP(IR[31:26]), .ALU_OP(\单周期硬布线控制器_1_alu_op ), .MemToReg(\单周期硬布线控制器_1_memtoreg [0]),
    .MemWrite(MemWrite), .ALU_SRC(\单周期硬布线控制器_1_alu_src ), .RegWrite(RegWrite), .SysCALL(Syscall),
    .SignedExt(SignedExt), .RegDst(\单周期硬布线控制器_1_regdst ), .JR(RegJump), .JMP(\单周期硬布线控制器_1_jmp ),
    .Beq(\单周期硬布线控制器_1_beq ), .JAL(JAL), .Bne(\单周期硬布线控制器_1_bne ), .\使能端 (not_1_out), .MF(IR[25:21]),
    .MFC0(\单周期硬布线控制器_1_mfc0 ), .MTC0(\单周期硬布线控制器_1_mtc0 ), .ERET(\单周期硬布线控制器_1_eret ),
    .BLEZ(\单周期硬布线控制器_1_blez ), .ReadMode(\单周期硬布线控制器_1_readmode ));
  Multiplexer #(.width(10), .enable("false")) multiplexer_2 (
    .in0({IR[20:16], IR[25:21]}), .in1(10'h44), .out(multiplexer_2_out), .sel(Syscall));
  Multiplexer #(.width(5), .enable("false")) multiplexer_3 (
    .in0(multiplexer_1_out), .in1({5{1'b1}}), .out(multiplexer_3_out), .sel(JAL));
  Multiplexer #(.width(32), .enable("false")) multiplexer_4 (
    .in0(bit_extender_1_out), .in1(bit_extender_2_out), .out(multiplexer_4_out), .sel(SignedExt));
  Shifter #(.width(32)) shifter_1 (
    .in(bit_extender_3_out), .\dist (5'b00010), .out({shifter_1_out, JMPJALAddress[27:0]}));
  or or_2 (or_2_out, mips_alu_1_result[0], mips_alu_1_equal);
  and and_1 (and_1_out, or_2_out, \单周期硬布线控制器_1_blez );
  and and_2 (and_2_out, mips_alu_1_equal, \单周期硬布线控制器_1_beq );
  and and_3 (and_3_out, ~mips_alu_1_equal, \单周期硬布线控制器_1_bne );  // AND_Gate
  Shifter #(.width(32)) shifter_2 (.in(bit_extender_2_out), .\dist (5'b00010), .out(shifter_2_out));
  or or_3 (BranchJump, and_1_out, and_2_out, and_3_out);
  MIPS_Regifile mips_regifile_1 (
    .Din(RDin), .Clk(CLK), .R1(R1), .R2(MDin), .WE(RegWrite), .W_num(multiplexer_3_out),
    .R1_num(multiplexer_2_out[4:0]), .R2_num(multiplexer_2_out[9:5]));
  Adder #(.width(32)) adder_3 (
    .a({JMPJALAddress[31:28], NextPC}), .b(shifter_2_out), .out(BranchAddr));  // open: cin, cout
  Multiplexer #(.width(32), .enable("false")) multiplexer_5 (
    .in0(MDin), .in1(multiplexer_4_out), .out(multiplexer_5_out), .sel(\单周期硬布线控制器_1_alu_src ));
  MIPS_ALU mips_alu_1 (
    .X(R1), .Y(multiplexer_5_out), .AluOP(\单周期硬布线控制器_1_alu_op ), .Equal(mips_alu_1_equal),
    .Result(mips_alu_1_result), .shamt(IR[10:6]));  // open: Result_2
  Demultiplexer #(.enable("false")) demultiplexer_1 (
    .out0(demultiplexer_1_out0), .out1(demultiplexer_1_out1), .in(\单周期硬布线控制器_1_mtc0 ), .sel(IR[11]));
  not not_2 (not_2_out, \单周期硬布线控制器_1_eret );
  Multiplexer #(.enable("false")) multiplexer_6 (.in0(1'b0), .in1(MDin[0]), .out(multiplexer_6_out), .sel(not_2_out));
  Comparator #(.width(32)) comparator_1 (.a(MDin), .b(32'h22), .eq(comparator_1_eq));  // open: gt, lt
  D_Flip_Flop IE (.clk(CLK), .D(multiplexer_6_out), .Q(IE_q[0]), .en(demultiplexer_1_out0));  // open: Qn, preset, reset
  RAM #(.addrWidth(10), .bus("separate")) ram_1 (
    .addr(mips_alu_1_result[11:2]), .din(MDin[7:0]), .data(ram_1_data), .str(MemWrite), .clk(CLK), .clr(RST));  // open: sel, ld
  RAM #(.addrWidth(10), .bus("separate")) ram_2 (
    .addr(mips_alu_1_result[11:2]), .din(MDin[15:8]), .data(ram_2_data), .str(MemWrite), .clk(CLK), .clr(RST));  // open: sel, ld
  and and_4 (and_4_out, Syscall, comparator_1_eq);
  and and_5 (and_5_out, Syscall, ~comparator_1_eq);  // AND_Gate
  Register #(.width(3)) IMW (.D(MDin[2:0]), .en(demultiplexer_1_out1), .Q(IMW_q), .clk(CLK));  // open: clr
  Register #(.width(1)) register_2 (.D(and_5_out), .en(PCEnable), .Q(register_2_q), .clk(CLK), .clr(or_4_out));
  Multiplexer #(.width(32), .enable("false")) multiplexer_7 (
    .in0({{31{1'b0}}, IE_q[0]}), .in1({{29{1'b0}}, IMW_q}), .out(multiplexer_7_out), .sel(IR[11]));
  Register #(.width(32)) register_3 (.D(R1), .en(and_4_out), .Q(LedData), .clk(CLK), .clr(RST));
  not not_3 (PCEnable, register_2_q);
  or or_4 (or_4_out, Go, RST);
  RAM #(.addrWidth(10), .bus("separate")) ram_3 (
    .addr(mips_alu_1_result[11:2]), .din(MDin[23:16]), .data(ram_3_data), .str(MemWrite), .clk(CLK), .clr(RST));  // open: sel, ld
  RAM #(.addrWidth(10), .bus("separate")) ram_4 (
    .addr(mips_alu_1_result[11:2]), .din(MDin[31:24]), .data(ram_4_data), .str(MemWrite), .clk(CLK), .clr(RST));  // open: sel, ld
  assign bit_extender_4_out = {{24{multiplexer_8_out[7]}}, multiplexer_8_out};  // Bit_Extender bit_extender_4
  Multiplexer #(.select(2), .width(8), .enable("false")) multiplexer_8 (
    .in0(ram_1_data), .in1(ram_2_data), .in2(ram_3_data), .in3(ram_4_data), .out(multiplexer_8_out),
    .sel(mips_alu_1_result[1:0]));
  Multiplexer #(.width(32), .enable("false")) multiplexer_9 (
    .in0({ram_4_data, ram_3_data, ram_2_data, ram_1_data}), .in1(bit_extender_4_out),
    .out(multiplexer_9_out), .sel(\单周期硬布线控制器_1_readmode ));
  or or_5 (\单周期硬布线控制器_1_memtoreg [1], \单周期硬布线控制器_1_mfc0 , JAL);
  Multiplexer #(.width(32), .enable("false")) multiplexer_10 (
    .in0(multiplexer_7_out), .in1({JMPJALAddress[31:28], NextPC}), .out(multiplexer_10_out), .sel(JAL));
  Multiplexer #(.select(2), .width(32), .enable("false")) multiplexer_11 (
    .in0(mips_alu_1_result), .in1(multiplexer_9_out), .in2(multiplexer_10_out), .in3(multiplexer_10_out),
    .out(RDin), .sel(\单周期硬布线控制器_1_memtoreg ));

  // Other names for the same wires on the sheet: Rd = IR[11]; NextPC[31:28] = JMPJALAddress[31:28]; R2[31:0] = MDin

  // Notes on the sheet:
  //   中断源
  //   中断等待指示
  //   总复位信号应将除ROM以外所有存储组件全部清零
  //   数码管输出
  //   指令存储器
  //   contents of rom_1 (hex, n*v repeats v):
  //   20110001 8000c05 20110001 20120002 20130003 8000c09 20110001 20120002 20130003 8000c0d 20110001
  //   20120002 20130003 8000c11 20110001 20120002 20130003 c000cb8 20100001 20110001 118fc0 112020
  //   20020022 c 118882 12200001 8000c15 112020 20020022 c 20110001 118880 112020 20020022 c 12200001
  //   8000c1f 20110001 118fc0 112020 20020022 c 1188c3 112020 20020022 c 118903 112020 20020022 c 118903
  //   112020 20020022 c 118903 112020 20020022 c 118903 112020 20020022 c 118903 112020 20020022 c 118903
  //   112020 20020022 c 118903 112020 20020022 c 20100001 109fc0 139fc3 8021 2012000c 24160003 26100001
  //   3210000f 20080008 20090001 139900 2709825 132020 20020022 c 1094022 1500fff9 22100001 2018000f
  //   2188024 108700 20080008 20090001 139902 2709825 132021 20020022 c 1094022 1500fff9 108702 2c9b022
  //   12c00001 8000c50 4020 1084027 84400 3508ffff 82021 20020022 c 2010ffff 20110000 ae300000 22100001
  //   22310004 ae300000 22100001 22310004 ae300000 22100001 22310004 ae300000 22100001 22310004 ae300000
  //   22100001 22310004 ae300000 22100001 22310004 ae300000 22100001 22310004 ae300000 22100001 22310004
  //   ae300000 22100001 22310004 ae300000 22100001 22310004 ae300000 22100001 22310004 ae300000 22100001
  //   22310004 ae300000 22100001 22310004 ae300000 22100001 22310004 ae300000 22100001 22310004 ae300000
  //   22100001 22310004 22100001 8020 2011003c 8e130000 8e340000 274402a 11000002 ae330000 ae140000
  //   2231fffc 1611fff8 102020 20020022 c 22100004 2011003c 1611fff2 20020032 c 20100000 22100001 102020
  //   20020022 c 22100002 102020 20020022 c 22100003 102020 20020022 c 22100004 102020 20020022 c 22100005
  //   102020 20020022 c 22100006 102020 20020022 c 22100007 102020 20020022 c 22100008 102020 20020022
  //   20020022 c 3e00008
  //   数码管输出应该用寄存器锁存，否则显示数据只能一闪而过
  //   OP
  //   Func
  //   rs
  //   指令字
  //   rt
  //   rd
  //   JMP
  //   JR
  //   OP
  //   Func
  //   Beq
  //   Bne
  //   MemToReg
  //   MemWrite
  //   AluOP
  //   AluSrcB
  //   RegWrite
  //   JAL
  //   RegDst
  //   为方便自动评测，需要输出PC，IR，寄存器文件写入端口RDin，内存写入端口MDin等信号
endmodule

// 单周期硬布线控制器
module \单周期硬布线控制器  (
  input  [5:0] OP,
  input  [5:0] Func,
  input  [4:0] MF,
  input  \使能端 ,
  output [3:0] ALU_OP,
  output MemToReg,
  output MemWrite,
  output BLEZ,
  output ReadMode,
  output MFC0,
  output MTC0,
  output ERET,
  output ALU_SRC,
  output RegWrite,
  output SysCALL,
  output SignedExt,
  output RegDst,
  output Beq,
  output Bne,
  output JR,
  output JMP,
  output JAL
);

  \运算控制器自动生成  \u_运算控制器自动生成_1  (
    .OP0(OP[0]), .OP1(OP[1]), .OP2(OP[2]), .OP3(OP[3]), .OP4(OP[4]), .OP5(OP[5]), .F0(Func[0]), .F1(Func[1]),
    .F2(Func[2]), .F3(Func[3]), .F4(Func[4]), .F5(Func[5]), .S0(ALU_OP[0]), .S1(ALU_OP[1]), .S2(ALU_OP[2]),
    .S3(ALU_OP[3]));
  \控制信号自动生成  \u_控制信号自动生成_1  (
    .in_1(\使能端 ), .OP0(OP[0]), .OP1(OP[1]), .OP2(OP[2]), .OP3(OP[3]), .OP4(OP[4]), .OP5(OP[5]), .F0(Func[0]),
    .F1(Func[1]), .F2(Func[2]), .F3(Func[3]), .F4(Func[4]), .F5(Func[5]), .MF0(MF[0]), .MF1(MF[1]),
    .MF2(MF[2]), .MF3(MF[3]), .MF4(MF[4]), .MemToReg(MemToReg), .MemWrite(MemWrite), .BLEZ(BLEZ),
    .ReadMode(ReadMode), .MFC0(MFC0), .MTC0(MTC0), .ERET(ERET), .ALU_SRC(ALU_SRC), .RegWrite(RegWrite),
    .SysCALL(SysCALL), .SignedExt(SignedExt), .RegDst(RegDst), .BEQ(Beq), .BNE(Bne), .JR(JR), .JUMP(JMP),
    .JAL(JAL));

  // Other names for the same wires on the sheet: OP_CODE[5:0] = OP

  // Notes on the sheet:
  //   控制信号生成，产生数据通路需要的其他控制信号
  //   运算器控制器，根据指令生成运算器功能选择信号
endmodule

// 运算器控制器
module \运算控制器自动生成  (
  input  OP0,
  input  OP1,
  input  OP2,
  input  OP3,
  input  OP4,
  input  OP5,
  input  F0,
  input  F1,
  input  F2,
  input  F3,
  input  F4,
  input  F5,
  output S0,
  output S1,
  output S2,
  output S3
);

  wire and_1_out, and_2_out, and_3_out, and_4_out, and_5_out, and_6_out, and_7_out, and_8_out, and_9_out,
       and_10_out, and_11_out, and_12_out, and_13_out, and_14_out, and_15_out, and_16_out, and_17_out,
       and_18_out, and_19_out, and_20_out, and_21_out, and_22_out, and_23_out, and_24_out, and_25_out,
       and_26_out, and_27_out, and_28_out, and_29_out, and_30_out, and_31_out, and_32_out, and_33_out,
       and_34_out, and_35_out, and_36_out, and_37_out, and_38_out, and_39_out, and_40_out, and_41_out,
       and_42_out, and_43_out, not_1_out, not_2_out, not_3_out, not_4_out, not_5_out, not_6_out, not_7_out,
       not_8_out, not_9_out, not_10_out, not_11_out, not_12_out, not_13_out, not_14_out, not_15_out,
       not_16_out, not_17_out, not_18_out, not_19_out, not_20_out, not_21_out, not_22_out, not_23_out,
       not_24_out, not_25_out, not_26_out, not_27_out, not_28_out, not_29_out, not_30_out, not_31_out,
       not_32_out, not_33_out, not_34_out, not_35_out, not_36_out, not_37_out, not_38_out, not_39_out,
       not_40_out, not_41_out, not_42_out, not_43_out, not_44_out, not_45_out, not_46_out, not_47_out,
       not_48_out, not_49_out, not_50_out, not_51_out, not_52_out, not_53_out, not_54_out, not_55_out,
       not_56_out, not_57_out, not_58_out, not_59_out, not_60_out, not_61_out, not_62_out, not_63_out,
       not_64_out, not_65_out, not_66_out, not_67_out, not_68_out, not_69_out, not_70_out, not_71_out,
       not_72_out, not_73_out, not_74_out, not_75_out, not_76_out, not_77_out, not_78_out, not_79_out,
       not_80_out, not_81_out, not_82_out, not_83_out, not_84_out, not_85_out, not_86_out, not_87_out,
       not_88_out, not_89_out, not_90_out, not_91_out, not_92_out, not_93_out, not_94_out, not_95_out,
       not_96_out, not_97_out, not_98_out, not_99_out, not_100_out, not_101_out, not_102_out, not_103_out,
       not_104_out, not_105_out, not_106_out, not_107_out, not_108_out, not_109_out, not_110_out,
       not_111_out, not_112_out, not_113_out, not_114_out, not_115_out, not_116_out, not_117_out,
       not_118_out, not_119_out, not_120_out, not_121_out, not_122_out, not_123_out, not_124_out,
       not_125_out, not_126_out, not_127_out, not_128_out, not_129_out, not_130_out, not_131_out,
       not_132_out, not_133_out, not_134_out, not_135_out, not_136_out, not_137_out, not_138_out,
       not_139_out, not_140_out, not_141_out, not_142_out, not_143_out, not_144_out, not_145_out,
       not_146_out, not_147_out, not_148_out, not_149_out, not_150_out, not_151_out, not_152_out,
       not_153_out, not_154_out, not_155_out, not_156_out, not_157_out, not_158_out, not_159_out,
       not_160_out, not_161_out, not_162_out, not_163_out, not_164_out, not_165_out, not_166_out,
       not_167_out, not_168_out, not_169_out, not_170_out, not_171_out, not_172_out, not_173_out,
       not_174_out, not_175_out, not_176_out, not_177_out, not_178_out, not_179_out, not_180_out,
       not_181_out, not_182_out, not_183_out, not_184_out, not_185_out, not_186_out, not_187_out,
       not_188_out, not_189_out, not_190_out, not_191_out, not_192_out, not_193_out, not_194_out,
       not_195_out, not_196_out, not_197_out, not_198_out, not_199_out, not_200_out, not_201_out,
       not_202_out, not_203_out, not_204_out, not_205_out, not_206_out, not_207_out, not_208_out,
       not_209_out, not_210_out, not_211_out, not_212_out, not_213_out, not_214_out, not_215_out,
       not_216_out, not_217_out, not_218_out, not_219_out, not_220_out, not_221_out, not_222_out,
       not_223_out, not_224_out, not_225_out, not_226_out, not_227_out, not_228_out, not_229_out,
       not_230_out, not_231_out, not_232_out, not_233_out, not_234_out, not_235_out, not_236_out,
       not_237_out, not_238_out, not_239_out, not_240_out, not_241_out, not_242_out, not_243_out,
       not_244_out, not_245_out, not_246_out, not_247_out, not_248_out, not_249_out, not_250_out,
       not_251_out, not_252_out, not_253_out, not_254_out, not_255_out, not_256_out, not_257_out,
       not_258_out, not_259_out, not_260_out, not_261_out, not_262_out, not_263_out, not_264_out,
       not_265_out, not_266_out, not_267_out, not_268_out, not_269_out, not_270_out, not_271_out,
       not_272_out, not_273_out, not_274_out, not_275_out, not_276_out, not_277_out, not_278_out,
       not_279_out, not_280_out, not_281_out, not_282_out;

  not not_1 (not_1_out, OP5);
  not not_2 (not_2_out, OP4);
  not not_3 (not_3_out, OP3);
  not not_4 (not_4_out, OP2);
  not not_5 (not_5_out, OP1);
  not not_6 (not_6_out, OP0);
  not not_7 (not_7_out, F5);
  not not_8 (not_8_out, F4);
  not not_9 (not_9_out, F3);
  not not_10 (not_10_out, F2);
  not not_11 (not_11_out, OP5);
  not not_12 (not_12_out, OP4);
  not not_13 (not_13_out, OP3);
  not not_14 (not_14_out, OP2);
  not not_15 (not_15_out, OP1);
  not not_16 (not_16_out, OP0);
  not not_17 (not_17_out, F4);
  not not_18 (not_18_out, F3);
  not not_19 (not_19_out, F2);
  not not_20 (not_20_out, F1);
  not not_21 (not_21_out, F0);
  not not_22 (not_22_out, OP5);
  not not_23 (not_23_out, OP4);
  not not_24 (not_24_out, OP3);
  not not_25 (not_25_out, OP2);
  not not_26 (not_26_out, OP1);
  not not_27 (not_27_out, OP0);
  not not_28 (not_28_out, F4);
  not not_29 (not_29_out, F3);
  not not_30 (not_30_out, F2);
  not not_31 (not_31_out, F1);
  not not_32 (not_32_out, OP5);
  not not_33 (not_33_out, OP4);
  not not_34 (not_34_out, OP3);
  not not_35 (not_35_out, OP2);
  not not_36 (not_36_out, OP1);
  not not_37 (not_37_out, OP0);
  not not_38 (not_38_out, F4);
  not not_39 (not_39_out, F3);
  not not_40 (not_40_out, F1);
  not not_41 (not_41_out, F0);
  not not_42 (not_42_out, OP5);
  not not_43 (not_43_out, OP4);
  not not_44 (not_44_out, OP3);
  not not_45 (not_45_out, OP2);
  not not_46 (not_46_out, OP1);
  not not_47 (not_47_out, OP0);
  not not_48 (not_48_out, F4);
  not not_49 (not_49_out, F2);
  not not_50 (not_50_out, F0);
  not not_51 (not_51_out, OP5);
  not not_52 (not_52_out, OP4);
  not not_53 (not_53_out, OP2);
  not not_54 (not_54_out, OP1);
  not not_55 (not_55_out, OP0);
  not not_56 (not_56_out, OP5);
  not not_57 (not_57_out, OP4);
  not not_58 (not_58_out, OP1);
  not not_59 (not_59_out, OP0);
  not not_60 (not_60_out, OP5);
  not not_61 (not_61_out, OP4);
  not not_62 (not_62_out, OP2);
  not not_63 (not_63_out, OP1);
  not not_64 (not_64_out, OP5);
  not not_65 (not_65_out, OP4);
  not not_66 (not_66_out, OP2);
  not not_67 (not_67_out, OP0);
  not not_68 (not_68_out, OP4);
  not not_69 (not_69_out, OP3);
  not not_70 (not_70_out, OP2);
  not not_71 (not_71_out, OP4);
  not not_72 (not_72_out, OP2);
  not not_73 (not_73_out, OP5);
  not not_74 (not_74_out, OP4);
  not not_75 (not_75_out, OP0);
  not not_76 (not_76_out, OP4);
  not not_77 (not_77_out, OP3);
  not not_78 (not_78_out, OP2);
  not not_79 (not_79_out, OP1);
  not not_80 (not_80_out, OP0);
  not not_81 (not_81_out, OP5);
  not not_82 (not_82_out, OP4);
  not not_83 (not_83_out, OP3);
  not not_84 (not_84_out, OP0);
  not not_85 (not_85_out, OP5);
  not not_86 (not_86_out, OP4);
  not not_87 (not_87_out, OP3);
  not not_88 (not_88_out, OP2);
  not not_89 (not_89_out, OP1);
  not not_90 (not_90_out, OP0);
  not not_91 (not_91_out, F5);
  not not_92 (not_92_out, F4);
  not not_93 (not_93_out, F3);
  not not_94 (not_94_out, F2);
  not not_95 (not_95_out, F0);
  not not_96 (not_96_out, OP5);
  not not_97 (not_97_out, OP4);
  not not_98 (not_98_out, OP3);
  not not_99 (not_99_out, OP2);
  not not_100 (not_100_out, OP1);
  not not_101 (not_101_out, OP0);
  not not_102 (not_102_out, F4);
  not not_103 (not_103_out, F3);
  not not_104 (not_104_out, F2);
  not not_105 (not_105_out, F0);
  not not_106 (not_106_out, OP5);
  not not_107 (not_107_out, OP4);
  not not_108 (not_108_out, OP3);
  not not_109 (not_109_out, OP2);
  not not_110 (not_110_out, OP1);
  not not_111 (not_111_out, OP0);
  not not_112 (not_112_out, F4);
  not not_113 (not_113_out, F3);
  not not_114 (not_114_out, F1);
  not not_115 (not_115_out, F0);
  not not_116 (not_116_out, OP5);
  not not_117 (not_117_out, OP4);
  not not_118 (not_118_out, OP3);
  not not_119 (not_119_out, OP2);
  not not_120 (not_120_out, OP1);
  not not_121 (not_121_out, OP0);
  not not_122 (not_122_out, F4);
  not not_123 (not_123_out, F3);
  not not_124 (not_124_out, OP5);
  not not_125 (not_125_out, OP4);
  not not_126 (not_126_out, OP3);
  not not_127 (not_127_out, OP2);
  not not_128 (not_128_out, OP1);
  not not_129 (not_129_out, OP0);
  not not_130 (not_130_out, F4);
  not not_131 (not_131_out, F2);
  not not_132 (not_132_out, F0);
  not not_133 (not_133_out, OP5);
  not not_134 (not_134_out, OP4);
  not not_135 (not_135_out, OP1);
  not not_136 (not_136_out, OP0);
  not not_137 (not_137_out, OP5);
  not not_138 (not_138_out, OP4);
  not not_139 (not_139_out, OP2);
  not not_140 (not_140_out, OP0);
  not not_141 (not_141_out, OP5);
  not not_142 (not_142_out, OP4);
  not not_143 (not_143_out, OP3);
  not not_144 (not_144_out, OP2);
  not not_145 (not_145_out, OP1);
  not not_146 (not_146_out, OP0);
  not not_147 (not_147_out, F4);
  not not_148 (not_148_out, F3);
  not not_149 (not_149_out, F2);
  not not_150 (not_150_out, OP5);
  not not_151 (not_151_out, OP4);
  not not_152 (not_152_out, OP3);
  not not_153 (not_153_out, OP0);
  not not_154 (not_154_out, OP5);
  not not_155 (not_155_out, OP4);
  not not_156 (not_156_out, OP3);
  not not_157 (not_157_out, OP2);
  not not_158 (not_158_out, OP1);
  not not_159 (not_159_out, OP0);
  not not_160 (not_160_out, F4);
  not not_161 (not_161_out, F3);
  not not_162 (not_162_out, F2);
  not not_163 (not_163_out, F1);
  not not_164 (not_164_out, F0);
  not not_165 (not_165_out, OP5);
  not not_166 (not_166_out, OP4);
  not not_167 (not_167_out, OP3);
  not not_168 (not_168_out, OP2);
  not not_169 (not_169_out, OP1);
  not not_170 (not_170_out, OP0);
  not not_171 (not_171_out, F4);
  not not_172 (not_172_out, F3);
  not not_173 (not_173_out, F2);
  not not_174 (not_174_out, F1);
  not not_175 (not_175_out, OP5);
  not not_176 (not_176_out, OP4);
  not not_177 (not_177_out, OP3);
  not not_178 (not_178_out, OP2);
  not not_179 (not_179_out, OP1);
  not not_180 (not_180_out, OP0);
  not not_181 (not_181_out, F4);
  not not_182 (not_182_out, F3);
  not not_183 (not_183_out, F2);
  not not_184 (not_184_out, F0);
  not not_185 (not_185_out, OP5);
  not not_186 (not_186_out, OP4);
  not not_187 (not_187_out, OP3);
  not not_188 (not_188_out, OP2);
  not not_189 (not_189_out, OP1);
  not not_190 (not_190_out, OP0);
  not not_191 (not_191_out, F4);
  not not_192 (not_192_out, F3);
  not not_193 (not_193_out, F1);
  not not_194 (not_194_out, F0);
  not not_195 (not_195_out, OP5);
  not not_196 (not_196_out, OP4);
  not not_197 (not_197_out, OP3);
  not not_198 (not_198_out, OP2);
  not not_199 (not_199_out, OP1);
  not not_200 (not_200_out, OP0);
  not not_201 (not_201_out, F4);
  not not_202 (not_202_out, F2);
  not not_203 (not_203_out, OP5);
  not not_204 (not_204_out, OP4);
  not not_205 (not_205_out, OP2);
  not not_206 (not_206_out, OP1);
  not not_207 (not_207_out, OP0);
  not not_208 (not_208_out, OP5);
  not not_209 (not_209_out, OP4);
  not not_210 (not_210_out, OP1);
  not not_211 (not_211_out, OP0);
  not not_212 (not_212_out, OP5);
  not not_213 (not_213_out, OP4);
  not not_214 (not_214_out, OP2);
  not not_215 (not_215_out, OP1);
  not not_216 (not_216_out, OP4);
  not not_217 (not_217_out, OP3);
  not not_218 (not_218_out, OP2);
  not not_219 (not_219_out, OP4);
  not not_220 (not_220_out, OP2);
  not not_221 (not_221_out, OP5);
  not not_222 (not_222_out, OP4);
  not not_223 (not_223_out, OP3);
  not not_224 (not_224_out, OP2);
  not not_225 (not_225_out, OP1);
  not not_226 (not_226_out, OP0);
  not not_227 (not_227_out, F4);
  not not_228 (not_228_out, F3);
  not not_229 (not_229_out, F2);
  not not_230 (not_230_out, OP4);
  not not_231 (not_231_out, OP3);
  not not_232 (not_232_out, OP2);
  not not_233 (not_233_out, OP1);
  not not_234 (not_234_out, OP0);
  not not_235 (not_235_out, OP5);
  not not_236 (not_236_out, OP4);
  not not_237 (not_237_out, OP3);
  not not_238 (not_238_out, OP2);
  not not_239 (not_239_out, OP1);
  not not_240 (not_240_out, OP0);
  not not_241 (not_241_out, F4);
  not not_242 (not_242_out, F3);
  not not_243 (not_243_out, F1);
  not not_244 (not_244_out, OP5);
  not not_245 (not_245_out, OP4);
  not not_246 (not_246_out, OP3);
  not not_247 (not_247_out, OP2);
  not not_248 (not_248_out, OP1);
  not not_249 (not_249_out, OP0);
  not not_250 (not_250_out, F4);
  not not_251 (not_251_out, F3);
  not not_252 (not_252_out, OP5);
  not not_253 (not_253_out, OP4);
  not not_254 (not_254_out, OP3);
  not not_255 (not_255_out, OP2);
  not not_256 (not_256_out, OP1);
  not not_257 (not_257_out, OP0);
  not not_258 (not_258_out, F4);
  not not_259 (not_259_out, F2);
  not not_260 (not_260_out, F0);
  not not_261 (not_261_out, OP5);
  not not_262 (not_262_out, OP4);
  not not_263 (not_263_out, OP3);
  not not_264 (not_264_out, OP2);
  not not_265 (not_265_out, OP1);
  not not_266 (not_266_out, OP0);
  not not_267 (not_267_out, F4);
  not not_268 (not_268_out, F2);
  not not_269 (not_269_out, OP5);
  not not_270 (not_270_out, OP4);
  not not_271 (not_271_out, OP2);
  not not_272 (not_272_out, OP0);
  not not_273 (not_273_out, OP5);
  not not_274 (not_274_out, OP4);
  not not_275 (not_275_out, OP1);
  not not_276 (not_276_out, OP5);
  not not_277 (not_277_out, OP4);
  not not_278 (not_278_out, OP0);
  not not_279 (not_279_out, OP5);
  not not_280 (not_280_out, OP4);
  not not_281 (not_281_out, OP3);
  not not_282 (not_282_out, OP0);
  and and_1 (and_1_out, not_1_out, not_2_out, not_3_out, not_4_out, not_5_out, not_6_out, not_7_out, not_8_out, not_9_out, not_10_out, F1, F0);
  and and_2 (and_2_out, not_11_out, not_12_out, not_13_out, not_14_out, not_15_out, not_16_out, F5, not_17_out, not_18_out, not_19_out, not_20_out, not_21_out);
  and and_3 (and_3_out, not_22_out, not_23_out, not_24_out, not_25_out, not_26_out, not_27_out, F5, not_28_out, not_29_out, not_30_out, not_31_out, F0);
  and and_4 (and_4_out, not_32_out, not_33_out, not_34_out, not_35_out, not_36_out, not_37_out, F5, not_38_out, not_39_out, F2, not_40_out, not_41_out);
  and and_5 (and_5_out, not_42_out, not_43_out, not_44_out, not_45_out, not_46_out, not_47_out, F5, not_48_out, F3, not_49_out, F1, not_50_out);
  and and_6 (and_6_out, not_51_out, not_52_out, OP3, not_53_out, not_54_out, not_55_out);
  and and_7 (and_7_out, not_56_out, not_57_out, OP3, OP2, not_58_out, not_59_out);
  and and_8 (and_8_out, not_60_out, not_61_out, OP3, not_62_out, not_63_out, OP0);
  and and_9 (and_9_out, not_64_out, not_65_out, OP3, not_66_out, OP1, not_67_out);
  and and_10 (and_10_out, OP5, not_68_out, not_69_out, not_70_out, OP1, OP0);
  and and_11 (and_11_out, OP5, not_71_out, OP3, not_72_out, OP1, OP0);
  and and_12 (and_12_out, not_73_out, not_74_out, OP3, OP2, OP1, not_75_out);
  and and_13 (and_13_out, OP5, not_76_out, not_77_out, not_78_out, not_79_out, not_80_out);
  and and_14 (and_14_out, not_81_out, not_82_out, not_83_out, OP2, OP1, not_84_out);
  and and_15 (and_15_out, not_85_out, not_86_out, not_87_out, not_88_out, not_89_out, not_90_out, not_91_out, not_92_out, not_93_out, not_94_out, F1, not_95_out);
  and and_16 (and_16_out, not_96_out, not_97_out, not_98_out, not_99_out, not_100_out, not_101_out, F5, not_102_out, not_103_out, not_104_out, F1, not_105_out);
  and and_17 (and_17_out, not_106_out, not_107_out, not_108_out, not_109_out, not_110_out, not_111_out, F5, not_112_out, not_113_out, F2, not_114_out, not_115_out);
  and and_18 (and_18_out, not_116_out, not_117_out, not_118_out, not_119_out, not_120_out, not_121_out, F5, not_122_out, not_123_out, F2, F1, F0);
  and and_19 (and_19_out, not_124_out, not_125_out, not_126_out, not_127_out, not_128_out, not_129_out, F5, not_130_out, F3, not_131_out, F1, not_132_out);
  and and_20 (and_20_out, not_133_out, not_134_out, OP3, OP2, not_135_out, not_136_out);
  and and_21 (and_21_out, not_137_out, not_138_out, OP3, not_139_out, OP1, not_140_out);
  and and_22 (and_22_out, not_141_out, not_142_out, not_143_out, not_144_out, not_145_out, not_146_out, F5, not_147_out, not_148_out, not_149_out, F1, F0);
  and and_23 (and_23_out, not_150_out, not_151_out, not_152_out, OP2, OP1, not_153_out);
  and and_24 (and_24_out, not_154_out, not_155_out, not_156_out, not_157_out, not_158_out, not_159_out, F5, not_160_out, not_161_out, not_162_out, not_163_out, not_164_out);
  and and_25 (and_25_out, not_165_out, not_166_out, not_167_out, not_168_out, not_169_out, not_170_out, F5, not_171_out, not_172_out, not_173_out, not_174_out, F0);
  and and_26 (and_26_out, not_175_out, not_176_out, not_177_out, not_178_out, not_179_out, not_180_out, F5, not_181_out, not_182_out, not_183_out, F1, not_184_out);
  and and_27 (and_27_out, not_185_out, not_186_out, not_187_out, not_188_out, not_189_out, not_190_out, F5, not_191_out, not_192_out, F2, not_193_out, not_194_out);
  and and_28 (and_28_out, not_195_out, not_196_out, not_197_out, not_198_out, not_199_out, not_200_out, F5, not_201_out, F3, not_202_out, F1, F0);
  and and_29 (and_29_out, not_203_out, not_204_out, OP3, not_205_out, not_206_out, not_207_out);
  and and_30 (and_30_out, not_208_out, not_209_out, OP3, OP2, not_210_out, not_211_out);
  and and_31 (and_31_out, not_212_out, not_213_out, OP3, not_214_out, not_215_out, OP0);
  and and_32 (and_32_out, OP5, not_216_out, not_217_out, not_218_out, OP1, OP0);
  and and_33 (and_33_out, OP5, not_219_out, OP3, not_220_out, OP1, OP0);
  and and_34 (and_34_out, not_221_out, not_222_out, not_223_out, not_224_out, not_225_out, not_226_out, F5, not_227_out, not_228_out, not_229_out, F1, F0);
  and and_35 (and_35_out, OP5, not_230_out, not_231_out, not_232_out, not_233_out, not_234_out);
  and and_36 (and_36_out, not_235_out, not_236_out, not_237_out, not_238_out, not_239_out, not_240_out, F5, not_241_out, not_242_out, F2, not_243_out, F0);
  and and_37 (and_37_out, not_244_out, not_245_out, not_246_out, not_247_out, not_248_out, not_249_out, F5, not_250_out, not_251_out, F2, F1, F0);
  and and_38 (and_38_out, not_252_out, not_253_out, not_254_out, not_255_out, not_256_out, not_257_out, F5, not_258_out, F3, not_259_out, F1, not_260_out);
  and and_39 (and_39_out, not_261_out, not_262_out, not_263_out, not_264_out, not_265_out, not_266_out, F5, not_267_out, F3, not_268_out, F1, F0);
  and and_40 (and_40_out, not_269_out, not_270_out, OP3, not_271_out, OP1, not_272_out);
  and and_41 (and_41_out, not_273_out, not_274_out, OP3, OP2, not_275_out, OP0);
  and and_42 (and_42_out, not_276_out, not_277_out, OP3, OP2, OP1, not_278_out);
  and and_43 (and_43_out, not_279_out, not_280_out, not_281_out, OP2, OP1, not_282_out);
  or or_1 (S1, and_15_out, and_16_out, and_17_out, and_18_out, and_19_out, and_20_out, and_21_out, and_22_out, and_23_out);
  or or_2 (S3, and_36_out, and_37_out, and_38_out, and_39_out, and_40_out, and_41_out, and_42_out, and_43_out);
  or or_3 (S0, and_1_out, and_2_out, and_3_out, and_4_out, and_5_out, and_6_out, and_7_out, and_8_out, and_9_out, and_10_out, and_11_out, and_12_out, and_13_out, and_14_out);
  or or_4 (S2, and_24_out, and_25_out, and_26_out, and_27_out, and_28_out, and_29_out, and_30_out, and_31_out, and_32_out, and_33_out, and_34_out, and_35_out);
endmodule

// 控制信号生成
module \控制信号自动生成  (
  input  in_1,
  input  OP0,
  input  OP1,
  input  OP2,
  input  OP3,
  input  OP4,
  input  OP5,
  input  F0,
  input  F1,
  input  F2,
  input  F3,
  input  F4,
  input  F5,
  input  MF0,
  input  MF1,
  input  MF2,
  input  MF3,
  input  MF4,
  output MemToReg,
  output MemWrite,
  output BLEZ,
  output ReadMode,
  output MFC0,
  output MTC0,
  output ERET,
  output ALU_SRC,
  output RegWrite,
  output SysCALL,
  output SignedExt,
  output RegDst,
  output BEQ,
  output BNE,
  output JR,
  output JUMP,
  output JAL
);

  wire and_1_out, and_2_out, and_3_out, and_4_out, and_5_out, and_6_out, and_7_out, and_8_out, and_9_out,
       and_10_out, and_11_out, and_12_out, and_13_out, and_14_out, and_15_out, and_16_out, and_17_out,
       and_18_out, and_19_out, and_20_out, and_21_out, and_22_out, and_23_out, and_24_out, and_25_out,
       and_26_out, and_27_out, and_28_out, and_29_out, and_30_out, and_31_out, and_32_out, and_33_out,
       and_34_out, and_35_out, and_36_out, and_37_out, and_38_out, and_39_out, and_40_out, and_41_out,
       and_42_out, and_43_out, and_44_out, and_45_out, and_46_out, and_47_out, and_48_out, and_49_out,
       and_50_out, and_51_out, and_52_out, and_53_out, and_54_out, and_55_out, and_56_out, and_57_out,
       and_58_out, and_59_out, and_60_out, and_73_out, and_74_out, and_75_out, and_76_out, and_80_out,
       and_81_out, not_1_out, not_2_out, not_3_out, not_4_out, not_5_out, not_6_out, not_7_out, not_8_out,
       not_9_out, not_10_out, not_11_out, not_12_out, not_13_out, not_14_out, not_15_out, not_16_out,
       not_17_out, not_18_out, not_19_out, not_20_out, not_21_out, not_22_out, not_23_out, not_24_out,
       not_25_out, not_26_out, not_27_out, not_28_out, not_29_out, not_30_out, not_31_out, not_32_out,
       not_33_out, not_34_out, not_35_out, not_36_out, not_37_out, not_38_out, not_39_out, not_40_out,
       not_41_out, not_42_out, not_43_out, not_44_out, not_45_out, not_46_out, not_47_out, not_48_out,
       not_49_out, not_50_out, not_51_out, not_52_out, not_53_out, not_54_out, not_55_out, not_56_out,
       not_57_out, not_58_out, not_59_out, not_60_out, not_61_out, not_62_out, not_63_out, not_64_out,
       not_65_out, not_66_out, not_67_out, not_68_out, not_69_out, not_70_out, not_71_out, not_72_out,
       not_73_out, not_74_out, not_75_out, not_76_out, not_77_out, not_78_out, not_79_out, not_80_out,
       not_81_out, not_82_out, not_83_out, not_84_out, not_85_out, not_86_out, not_87_out, not_88_out,
       not_89_out, not_90_out, not_91_out, not_92_out, not_93_out, not_94_out, not_95_out, not_96_out,
       not_97_out, not_98_out, not_99_out, not_100_out, not_101_out, not_102_out, not_103_out, not_104_out,
       not_105_out, not_106_out, not_107_out, not_108_out, not_109_out, not_110_out, not_111_out,
       not_112_out, not_113_out, not_114_out, not_115_out, not_116_out, not_117_out, not_118_out,
       not_119_out, not_120_out, not_121_out, not_122_out, not_123_out, not_124_out, not_125_out,
       not_126_out, not_127_out, not_128_out, not_129_out, not_130_out, not_131_out, not_132_out,
       not_133_out, not_134_out, not_135_out, not_136_out, not_137_out, not_138_out, not_139_out,
       not_140_out, not_141_out, not_142_out, not_143_out, not_144_out, not_145_out, not_146_out,
       not_147_out, not_148_out, not_149_out, not_150_out, not_151_out, not_152_out, not_153_out,
       not_154_out, not_155_out, not_156_out, not_157_out, not_158_out, not_159_out, not_160_out,
       not_161_out, not_162_out, not_163_out, not_164_out, not_165_out, not_166_out, not_167_out,
       not_168_out, not_169_out, not_170_out, not_171_out, not_172_out, not_173_out, not_174_out,
       not_175_out, not_176_out, not_177_out, not_178_out, not_179_out, not_180_out, not_181_out,
       not_182_out, not_183_out, not_184_out, not_185_out, not_186_out, not_187_out, not_188_out,
       not_189_out, not_190_out, not_191_out, not_192_out, not_193_out, not_194_out, not_195_out,
       not_196_out, not_197_out, not_198_out, not_199_out, not_200_out, not_201_out, not_202_out,
       not_203_out, not_204_out, not_205_out, not_206_out, not_207_out, not_208_out, not_209_out,
       not_210_out, not_211_out, not_212_out, not_213_out, not_214_out, not_215_out, not_216_out,
       not_217_out, not_218_out, not_219_out, not_220_out, not_221_out, not_222_out, not_223_out,
       not_224_out, not_225_out, not_226_out, not_227_out, not_228_out, not_229_out, not_230_out,
       not_231_out, not_232_out, not_233_out, not_234_out, not_235_out, not_236_out, not_237_out,
       not_238_out, not_239_out, not_240_out, not_241_out, not_242_out, not_243_out, not_244_out,
       not_245_out, not_246_out, not_247_out, not_248_out, not_249_out, not_250_out, not_251_out,
       not_252_out, not_253_out, not_254_out, not_255_out, not_256_out, not_257_out, not_258_out,
       not_259_out, not_260_out, not_261_out, not_262_out, not_263_out, not_264_out, not_265_out,
       not_266_out, not_267_out, not_268_out, not_269_out, not_270_out, not_271_out, not_272_out,
       not_273_out, not_274_out, not_275_out, not_276_out, not_277_out, not_278_out, not_279_out,
       not_280_out, not_281_out, not_282_out, not_283_out, not_284_out, not_285_out, not_286_out,
       not_287_out, not_288_out, not_289_out, not_290_out, not_291_out, not_292_out, not_293_out,
       not_294_out, not_295_out, not_296_out, not_297_out, not_298_out, not_299_out, not_300_out,
       not_301_out, not_302_out, not_303_out, not_304_out, not_305_out, not_306_out, not_307_out,
       not_308_out, not_309_out, not_310_out, not_311_out, not_312_out, not_313_out, not_314_out,
       not_315_out, not_316_out, not_317_out, not_318_out, not_319_out, not_320_out, not_321_out,
       not_322_out, not_323_out, not_324_out, not_325_out, not_326_out, not_327_out, not_328_out,
       not_329_out, not_330_out, not_331_out, not_332_out, not_333_out, not_334_out, not_335_out,
       not_336_out, not_337_out, not_338_out, not_339_out, not_340_out, not_341_out, not_342_out,
       not_343_out, not_344_out, not_345_out, not_346_out, not_347_out, not_348_out, not_349_out,
       not_350_out, not_351_out, not_352_out, not_353_out, not_354_out, not_355_out, not_356_out,
       not_357_out, not_358_out, not_359_out, not_360_out, not_361_out, not_362_out, not_363_out,
       not_364_out, not_365_out, not_366_out, not_367_out, not_368_out, not_369_out, not_370_out,
       not_371_out, not_372_out, not_373_out, not_374_out, not_375_out, not_376_out, not_377_out,
       not_378_out, not_379_out, not_380_out, not_381_out, not_382_out, not_383_out, not_384_out,
       not_385_out, not_386_out, not_387_out, not_388_out, not_389_out, not_390_out, not_391_out,
       not_392_out, not_393_out, not_394_out, not_395_out, not_396_out, not_397_out, or_1_out, or_2_out,
       or_3_out, or_4_out, or_5_out;

  not not_1 (not_1_out, OP4);
  not not_2 (not_2_out, OP3);
  not not_3 (not_3_out, OP2);
  not not_4 (not_4_out, OP4);
  not not_5 (not_5_out, OP3);
  not not_6 (not_6_out, OP2);
  not not_7 (not_7_out, OP1);
  not not_8 (not_8_out, OP0);
  not not_9 (not_9_out, OP4);
  not not_10 (not_10_out, OP2);
  not not_11 (not_11_out, OP5);
  not not_12 (not_12_out, OP4);
  not not_13 (not_13_out, OP2);
  not not_14 (not_14_out, OP1);
  not not_15 (not_15_out, OP0);
  not not_16 (not_16_out, OP5);
  not not_17 (not_17_out, OP4);
  not not_18 (not_18_out, OP1);
  not not_19 (not_19_out, OP0);
  not not_20 (not_20_out, OP5);
  not not_21 (not_21_out, OP4);
  not not_22 (not_22_out, OP2);
  not not_23 (not_23_out, OP1);
  not not_24 (not_24_out, OP5);
  not not_25 (not_25_out, OP4);
  not not_26 (not_26_out, OP2);
  not not_27 (not_27_out, OP0);
  not not_28 (not_28_out, OP5);
  not not_29 (not_29_out, OP4);
  not not_30 (not_30_out, OP1);
  not not_31 (not_31_out, OP4);
  not not_32 (not_32_out, OP3);
  not not_33 (not_33_out, OP2);
  not not_34 (not_34_out, OP4);
  not not_35 (not_35_out, OP2);
  not not_36 (not_36_out, OP5);
  not not_37 (not_37_out, OP4);
  not not_38 (not_38_out, OP0);
  not not_39 (not_39_out, OP4);
  not not_40 (not_40_out, OP3);
  not not_41 (not_41_out, OP2);
  not not_42 (not_42_out, OP1);
  not not_43 (not_43_out, OP0);
  not not_44 (not_44_out, OP5);
  not not_45 (not_45_out, OP4);
  not not_46 (not_46_out, OP3);
  not not_47 (not_47_out, OP2);
  not not_48 (not_48_out, OP1);
  not not_49 (not_49_out, OP0);
  not not_50 (not_50_out, F5);
  not not_51 (not_51_out, F4);
  not not_52 (not_52_out, F3);
  not not_53 (not_53_out, F2);
  not not_54 (not_54_out, F1);
  not not_55 (not_55_out, F0);
  not not_56 (not_56_out, OP5);
  not not_57 (not_57_out, OP4);
  not not_58 (not_58_out, OP3);
  not not_59 (not_59_out, OP2);
  not not_60 (not_60_out, OP1);
  not not_61 (not_61_out, OP0);
  not not_62 (not_62_out, F5);
  not not_63 (not_63_out, F4);
  not not_64 (not_64_out, F3);
  not not_65 (not_65_out, F2);
  not not_66 (not_66_out, OP5);
  not not_67 (not_67_out, OP4);
  not not_68 (not_68_out, OP3);
  not not_69 (not_69_out, OP2);
  not not_70 (not_70_out, OP1);
  not not_71 (not_71_out, OP0);
  not not_72 (not_72_out, F5);
  not not_73 (not_73_out, F4);
  not not_74 (not_74_out, F3);
  not not_75 (not_75_out, F2);
  not not_76 (not_76_out, F0);
  not not_77 (not_77_out, OP5);
  not not_78 (not_78_out, OP4);
  not not_79 (not_79_out, OP3);
  not not_80 (not_80_out, OP2);
  not not_81 (not_81_out, OP1);
  not not_82 (not_82_out, OP0);
  not not_83 (not_83_out, F4);
  not not_84 (not_84_out, F3);
  not not_85 (not_85_out, F2);
  not not_86 (not_86_out, F1);
  not not_87 (not_87_out, F0);
  not not_88 (not_88_out, OP5);
  not not_89 (not_89_out, OP4);
  not not_90 (not_90_out, OP3);
  not not_91 (not_91_out, OP2);
  not not_92 (not_92_out, OP1);
  not not_93 (not_93_out, OP0);
  not not_94 (not_94_out, F4);
  not not_95 (not_95_out, F3);
  not not_96 (not_96_out, F2);
  not not_97 (not_97_out, F1);
  not not_98 (not_98_out, OP5);
  not not_99 (not_99_out, OP4);
  not not_100 (not_100_out, OP3);
  not not_101 (not_101_out, OP2);
  not not_102 (not_102_out, OP1);
  not not_103 (not_103_out, OP0);
  not not_104 (not_104_out, F4);
  not not_105 (not_105_out, F3);
  not not_106 (not_106_out, F2);
  not not_107 (not_107_out, F0);
  not not_108 (not_108_out, OP5);
  not not_109 (not_109_out, OP4);
  not not_110 (not_110_out, OP3);
  not not_111 (not_111_out, OP2);
  not not_112 (not_112_out, OP1);
  not not_113 (not_113_out, OP0);
  not not_114 (not_114_out, F4);
  not not_115 (not_115_out, F3);
  not not_116 (not_116_out, F1);
  not not_117 (not_117_out, F0);
  not not_118 (not_118_out, OP5);
  not not_119 (not_119_out, OP4);
  not not_120 (not_120_out, OP3);
  not not_121 (not_121_out, OP2);
  not not_122 (not_122_out, OP1);
  not not_123 (not_123_out, OP0);
  not not_124 (not_124_out, F4);
  not not_125 (not_125_out, F3);
  not not_126 (not_126_out, F1);
  not not_127 (not_127_out, OP5);
  not not_128 (not_128_out, OP4);
  not not_129 (not_129_out, OP3);
  not not_130 (not_130_out, OP2);
  not not_131 (not_131_out, OP1);
  not not_132 (not_132_out, OP0);
  not not_133 (not_133_out, F4);
  not not_134 (not_134_out, F3);
  not not_135 (not_135_out, OP5);
  not not_136 (not_136_out, OP4);
  not not_137 (not_137_out, OP3);
  not not_138 (not_138_out, OP2);
  not not_139 (not_139_out, OP1);
  not not_140 (not_140_out, OP0);
  not not_141 (not_141_out, F4);
  not not_142 (not_142_out, F2);
  not not_143 (not_143_out, F0);
  not not_144 (not_144_out, OP5);
  not not_145 (not_145_out, OP4);
  not not_146 (not_146_out, OP3);
  not not_147 (not_147_out, OP2);
  not not_148 (not_148_out, OP1);
  not not_149 (not_149_out, OP0);
  not not_150 (not_150_out, F4);
  not not_151 (not_151_out, F2);
  not not_152 (not_152_out, OP5);
  not not_153 (not_153_out, OP4);
  not not_154 (not_154_out, OP3);
  not not_155 (not_155_out, OP2);
  not not_156 (not_156_out, OP5);
  not not_157 (not_157_out, OP4);
  not not_158 (not_158_out, OP2);
  not not_159 (not_159_out, OP1);
  not not_160 (not_160_out, OP0);
  not not_161 (not_161_out, OP5);
  not not_162 (not_162_out, OP4);
  not not_163 (not_163_out, OP1);
  not not_164 (not_164_out, OP0);
  not not_165 (not_165_out, OP5);
  not not_166 (not_166_out, OP4);
  not not_167 (not_167_out, OP2);
  not not_168 (not_168_out, OP1);
  not not_169 (not_169_out, OP5);
  not not_170 (not_170_out, OP4);
  not not_171 (not_171_out, OP2);
  not not_172 (not_172_out, OP0);
  not not_173 (not_173_out, OP5);
  not not_174 (not_174_out, OP4);
  not not_175 (not_175_out, OP1);
  not not_176 (not_176_out, OP4);
  not not_177 (not_177_out, OP3);
  not not_178 (not_178_out, OP2);
  not not_179 (not_179_out, OP5);
  not not_180 (not_180_out, OP4);
  not not_181 (not_181_out, OP3);
  not not_182 (not_182_out, OP2);
  not not_183 (not_183_out, OP1);
  not not_184 (not_184_out, OP0);
  not not_185 (not_185_out, F4);
  not not_186 (not_186_out, F3);
  not not_187 (not_187_out, F2);
  not not_188 (not_188_out, OP5);
  not not_189 (not_189_out, OP4);
  not not_190 (not_190_out, OP0);
  not not_191 (not_191_out, OP4);
  not not_192 (not_192_out, OP3);
  not not_193 (not_193_out, OP2);
  not not_194 (not_194_out, OP1);
  not not_195 (not_195_out, OP0);
  not not_196 (not_196_out, OP5);
  not not_197 (not_197_out, OP4);
  not not_198 (not_198_out, OP3);
  not not_199 (not_199_out, OP2);
  not not_200 (not_200_out, OP1);
  not not_201 (not_201_out, OP0);
  not not_202 (not_202_out, F5);
  not not_203 (not_203_out, F4);
  not not_204 (not_204_out, F1);
  not not_205 (not_205_out, F0);
  not not_206 (not_206_out, OP5);
  not not_207 (not_207_out, OP4);
  not not_208 (not_208_out, OP3);
  not not_209 (not_209_out, OP1);
  not not_210 (not_210_out, OP0);
  not not_211 (not_211_out, OP5);
  not not_212 (not_212_out, OP4);
  not not_213 (not_213_out, OP3);
  not not_214 (not_214_out, OP1);
  not not_215 (not_215_out, OP5);
  not not_216 (not_216_out, OP4);
  not not_217 (not_217_out, OP2);
  not not_218 (not_218_out, OP1);
  not not_219 (not_219_out, OP0);
  not not_220 (not_220_out, OP5);
  not not_221 (not_221_out, OP4);
  not not_222 (not_222_out, OP2);
  not not_223 (not_223_out, OP1);
  not not_224 (not_224_out, OP5);
  not not_225 (not_225_out, OP4);
  not not_226 (not_226_out, OP2);
  not not_227 (not_227_out, OP0);
  not not_228 (not_228_out, OP4);
  not not_229 (not_229_out, OP3);
  not not_230 (not_230_out, OP2);
  not not_231 (not_231_out, OP4);
  not not_232 (not_232_out, OP2);
  not not_233 (not_233_out, OP4);
  not not_234 (not_234_out, OP3);
  not not_235 (not_235_out, OP2);
  not not_236 (not_236_out, OP1);
  not not_237 (not_237_out, OP0);
  not not_238 (not_238_out, OP5);
  not not_239 (not_239_out, OP4);
  not not_240 (not_240_out, OP3);
  not not_241 (not_241_out, OP0);
  not not_242 (not_242_out, OP5);
  not not_243 (not_243_out, OP4);
  not not_244 (not_244_out, OP3);
  not not_245 (not_245_out, OP2);
  not not_246 (not_246_out, OP1);
  not not_247 (not_247_out, OP0);
  not not_248 (not_248_out, F5);
  not not_249 (not_249_out, F4);
  not not_250 (not_250_out, F3);
  not not_251 (not_251_out, F2);
  not not_252 (not_252_out, F1);
  not not_253 (not_253_out, F0);
  not not_254 (not_254_out, OP5);
  not not_255 (not_255_out, OP4);
  not not_256 (not_256_out, OP3);
  not not_257 (not_257_out, OP2);
  not not_258 (not_258_out, OP1);
  not not_259 (not_259_out, OP0);
  not not_260 (not_260_out, F5);
  not not_261 (not_261_out, F4);
  not not_262 (not_262_out, F3);
  not not_263 (not_263_out, F2);
  not not_264 (not_264_out, OP5);
  not not_265 (not_265_out, OP4);
  not not_266 (not_266_out, OP3);
  not not_267 (not_267_out, OP2);
  not not_268 (not_268_out, OP1);
  not not_269 (not_269_out, OP0);
  not not_270 (not_270_out, F5);
  not not_271 (not_271_out, F4);
  not not_272 (not_272_out, F3);
  not not_273 (not_273_out, F2);
  not not_274 (not_274_out, F0);
  not not_275 (not_275_out, OP5);
  not not_276 (not_276_out, OP4);
  not not_277 (not_277_out, OP3);
  not not_278 (not_278_out, OP2);
  not not_279 (not_279_out, OP1);
  not not_280 (not_280_out, OP0);
  not not_281 (not_281_out, F4);
  not not_282 (not_282_out, F3);
  not not_283 (not_283_out, F2);
  not not_284 (not_284_out, F1);
  not not_285 (not_285_out, F0);
  not not_286 (not_286_out, OP5);
  not not_287 (not_287_out, OP4);
  not not_288 (not_288_out, OP3);
  not not_289 (not_289_out, OP2);
  not not_290 (not_290_out, OP1);
  not not_291 (not_291_out, OP0);
  not not_292 (not_292_out, F4);
  not not_293 (not_293_out, F3);
  not not_294 (not_294_out, F2);
  not not_295 (not_295_out, F1);
  not not_296 (not_296_out, OP5);
  not not_297 (not_297_out, OP4);
  not not_298 (not_298_out, OP3);
  not not_299 (not_299_out, OP2);
  not not_300 (not_300_out, OP1);
  not not_301 (not_301_out, OP0);
  not not_302 (not_302_out, F4);
  not not_303 (not_303_out, F3);
  not not_304 (not_304_out, F2);
  not not_305 (not_305_out, F0);
  not not_306 (not_306_out, OP5);
  not not_307 (not_307_out, OP4);
  not not_308 (not_308_out, OP3);
  not not_309 (not_309_out, OP2);
  not not_310 (not_310_out, OP1);
  not not_311 (not_311_out, OP0);
  not not_312 (not_312_out, F4);
  not not_313 (not_313_out, F3);
  not not_314 (not_314_out, F1);
  not not_315 (not_315_out, F0);
  not not_316 (not_316_out, OP5);
  not not_317 (not_317_out, OP4);
  not not_318 (not_318_out, OP3);
  not not_319 (not_319_out, OP2);
  not not_320 (not_320_out, OP1);
  not not_321 (not_321_out, OP0);
  not not_322 (not_322_out, F4);
  not not_323 (not_323_out, F3);
  not not_324 (not_324_out, F1);
  not not_325 (not_325_out, OP5);
  not not_326 (not_326_out, OP4);
  not not_327 (not_327_out, OP3);
  not not_328 (not_328_out, OP2);
  not not_329 (not_329_out, OP1);
  not not_330 (not_330_out, OP0);
  not not_331 (not_331_out, F4);
  not not_332 (not_332_out, F3);
  not not_333 (not_333_out, OP5);
  not not_334 (not_334_out, OP4);
  not not_335 (not_335_out, OP3);
  not not_336 (not_336_out, OP2);
  not not_337 (not_337_out, OP1);
  not not_338 (not_338_out, OP0);
  not not_339 (not_339_out, F4);
  not not_340 (not_340_out, F2);
  not not_341 (not_341_out, F0);
  not not_342 (not_342_out, OP5);
  not not_343 (not_343_out, OP4);
  not not_344 (not_344_out, OP3);
  not not_345 (not_345_out, OP2);
  not not_346 (not_346_out, OP1);
  not not_347 (not_347_out, OP0);
  not not_348 (not_348_out, F4);
  not not_349 (not_349_out, F2);
  not not_350 (not_350_out, OP5);
  not not_351 (not_351_out, OP4);
  not not_352 (not_352_out, OP3);
  not not_353 (not_353_out, OP2);
  not not_354 (not_354_out, OP1);
  not not_355 (not_355_out, OP0);
  not not_356 (not_356_out, F4);
  not not_357 (not_357_out, F3);
  not not_358 (not_358_out, F2);
  not not_359 (not_359_out, OP5);
  not not_360 (not_360_out, OP4);
  not not_361 (not_361_out, OP3);
  not not_362 (not_362_out, OP1);
  not not_363 (not_363_out, OP0);
  not not_364 (not_364_out, OP5);
  not not_365 (not_365_out, OP4);
  not not_366 (not_366_out, OP3);
  not not_367 (not_367_out, OP1);
  not not_368 (not_368_out, OP5);
  not not_369 (not_369_out, OP4);
  not not_370 (not_370_out, OP3);
  not not_371 (not_371_out, OP2);
  not not_372 (not_372_out, OP1);
  not not_373 (not_373_out, OP0);
  not not_374 (not_374_out, F5);
  not not_375 (not_375_out, F4);
  not not_376 (not_376_out, F2);
  not not_377 (not_377_out, F1);
  not not_378 (not_378_out, F0);
  not not_379 (not_379_out, OP5);
  not not_380 (not_380_out, OP4);
  not not_381 (not_381_out, OP3);
  not not_382 (not_382_out, OP2);
  not not_383 (not_383_out, OP0);
  not not_384 (not_384_out, OP5);
  not not_385 (not_385_out, OP4);
  not not_386 (not_386_out, OP3);
  not not_387 (not_387_out, OP2);
  and and_1 (and_1_out, OP5, not_1_out, not_2_out, not_3_out, OP1, OP0);
  and and_2 (and_2_out, OP5, not_4_out, not_5_out, not_6_out, not_7_out, not_8_out);
  and and_3 (and_3_out, OP5, not_9_out, OP3, not_10_out, OP1, OP0);
  and and_4 (and_4_out, not_11_out, not_12_out, OP3, not_13_out, not_14_out, not_15_out);
  and and_5 (and_5_out, not_16_out, not_17_out, OP3, OP2, not_18_out, not_19_out);
  and and_6 (and_6_out, not_20_out, not_21_out, OP3, not_22_out, not_23_out, OP0);
  and and_7 (and_7_out, not_24_out, not_25_out, OP3, not_26_out, OP1, not_27_out);
  and and_8 (and_8_out, not_28_out, not_29_out, OP3, OP2, not_30_out, OP0);
  and and_9 (and_9_out, OP5, not_31_out, not_32_out, not_33_out, OP1, OP0);
  and and_10 (and_10_out, OP5, not_34_out, OP3, not_35_out, OP1, OP0);
  and and_11 (and_11_out, not_36_out, not_37_out, OP3, OP2, OP1, not_38_out);
  and and_12 (and_12_out, OP5, not_39_out, not_40_out, not_41_out, not_42_out, not_43_out);
  and and_13 (and_13_out, not_44_out, not_45_out, not_46_out, not_47_out, not_48_out, not_49_out, not_50_out, not_51_out, not_52_out, not_53_out, not_54_out, not_55_out);
  and and_14 (and_14_out, not_56_out, not_57_out, not_58_out, not_59_out, not_60_out, not_61_out, not_62_out, not_63_out, not_64_out, not_65_out, F1, F0);
  and and_15 (and_15_out, not_66_out, not_67_out, not_68_out, not_69_out, not_70_out, not_71_out, not_72_out, not_73_out, not_74_out, not_75_out, F1, not_76_out);
  and and_16 (and_16_out, not_77_out, not_78_out, not_79_out, not_80_out, not_81_out, not_82_out, F5, not_83_out, not_84_out, not_85_out, not_86_out, not_87_out);
  and and_17 (and_17_out, not_88_out, not_89_out, not_90_out, not_91_out, not_92_out, not_93_out, F5, not_94_out, not_95_out, not_96_out, not_97_out, F0);
  and and_18 (and_18_out, not_98_out, not_99_out, not_100_out, not_101_out, not_102_out, not_103_out, F5, not_104_out, not_105_out, not_106_out, F1, not_107_out);
  and and_19 (and_19_out, not_108_out, not_109_out, not_110_out, not_111_out, not_112_out, not_113_out, F5, not_114_out, not_115_out, F2, not_116_out, not_117_out);
  and and_20 (and_20_out, not_118_out, not_119_out, not_120_out, not_121_out, not_122_out, not_123_out, F5, not_124_out, not_125_out, F2, not_126_out, F0);
  and and_21 (and_21_out, not_127_out, not_128_out, not_129_out, not_130_out, not_131_out, not_132_out, F5, not_133_out, not_134_out, F2, F1, F0);
  and and_22 (and_22_out, not_135_out, not_136_out, not_137_out, not_138_out, not_139_out, not_140_out, F5, not_141_out, F3, not_142_out, F1, not_143_out);
  and and_23 (and_23_out, not_144_out, not_145_out, not_146_out, not_147_out, not_148_out, not_149_out, F5, not_150_out, F3, not_151_out, F1, F0);
  and and_24 (and_24_out, not_152_out, not_153_out, not_154_out, not_155_out, OP1, OP0);
  and and_25 (and_25_out, not_156_out, not_157_out, OP3, not_158_out, not_159_out, not_160_out);
  and and_26 (and_26_out, not_161_out, not_162_out, OP3, OP2, not_163_out, not_164_out);
  and and_27 (and_27_out, not_165_out, not_166_out, OP3, not_167_out, not_168_out, OP0);
  and and_28 (and_28_out, not_169_out, not_170_out, OP3, not_171_out, OP1, not_172_out);
  and and_29 (and_29_out, not_173_out, not_174_out, OP3, OP2, not_175_out, OP0);
  and and_30 (and_30_out, OP5, not_176_out, not_177_out, not_178_out, OP1, OP0);
  and and_31 (and_31_out, not_179_out, not_180_out, not_181_out, not_182_out, not_183_out, not_184_out, F5, not_185_out, not_186_out, not_187_out, F1, F0);
  and and_32 (and_32_out, not_188_out, not_189_out, OP3, OP2, OP1, not_190_out);
  and and_33 (and_33_out, OP5, not_191_out, not_192_out, not_193_out, not_194_out, not_195_out);
  and and_34 (and_34_out, not_196_out, not_197_out, not_198_out, not_199_out, not_200_out, not_201_out, not_202_out, not_203_out, F3, F2, not_204_out, not_205_out);
  and and_35 (and_35_out, not_206_out, not_207_out, not_208_out, OP2, not_209_out, not_210_out);
  and and_36 (and_36_out, not_211_out, not_212_out, not_213_out, OP2, not_214_out, OP0);
  and and_37 (and_37_out, not_215_out, not_216_out, OP3, not_217_out, not_218_out, not_219_out);
  and and_38 (and_38_out, not_220_out, not_221_out, OP3, not_222_out, not_223_out, OP0);
  and and_39 (and_39_out, not_224_out, not_225_out, OP3, not_226_out, OP1, not_227_out);
  and and_40 (and_40_out, OP5, not_228_out, not_229_out, not_230_out, OP1, OP0);
  and and_41 (and_41_out, OP5, not_231_out, OP3, not_232_out, OP1, OP0);
  and and_42 (and_42_out, OP5, not_233_out, not_234_out, not_235_out, not_236_out, not_237_out);
  and and_43 (and_43_out, not_238_out, not_239_out, not_240_out, OP2, OP1, not_241_out);
  and and_44 (and_44_out, not_242_out, not_243_out, not_244_out, not_245_out, not_246_out, not_247_out, not_248_out, not_249_out, not_250_out, not_251_out, not_252_out, not_253_out);
  and and_45 (and_45_out, not_254_out, not_255_out, not_256_out, not_257_out, not_258_out, not_259_out, not_260_out, not_261_out, not_262_out, not_263_out, F1, F0);
  and and_46 (and_46_out, not_264_out, not_265_out, not_266_out, not_267_out, not_268_out, not_269_out, not_270_out, not_271_out, not_272_out, not_273_out, F1, not_274_out);
  and and_47 (and_47_out, not_275_out, not_276_out, not_277_out, not_278_out, not_279_out, not_280_out, F5, not_281_out, not_282_out, not_283_out, not_284_out, not_285_out);
  and and_48 (and_48_out, not_286_out, not_287_out, not_288_out, not_289_out, not_290_out, not_291_out, F5, not_292_out, not_293_out, not_294_out, not_295_out, F0);
  and and_49 (and_49_out, not_296_out, not_297_out, not_298_out, not_299_out, not_300_out, not_301_out, F5, not_302_out, not_303_out, not_304_out, F1, not_305_out);
  and and_50 (and_50_out, not_306_out, not_307_out, not_308_out, not_309_out, not_310_out, not_311_out, F5, not_312_out, not_313_out, F2, not_314_out, not_315_out);
  and and_51 (and_51_out, not_316_out, not_317_out, not_318_out, not_319_out, not_320_out, not_321_out, F5, not_322_out, not_323_out, F2, not_324_out, F0);
  and and_52 (and_52_out, not_325_out, not_326_out, not_327_out, not_328_out, not_329_out, not_330_out, F5, not_331_out, not_332_out, F2, F1, F0);
  and and_53 (and_53_out, not_333_out, not_334_out, not_335_out, not_336_out, not_337_out, not_338_out, F5, not_339_out, F3, not_340_out, F1, not_341_out);
  and and_54 (and_54_out, not_342_out, not_343_out, not_344_out, not_345_out, not_346_out, not_347_out, F5, not_348_out, F3, not_349_out, F1, F0);
  and and_55 (and_55_out, not_350_out, not_351_out, not_352_out, not_353_out, not_354_out, not_355_out, F5, not_356_out, not_357_out, not_358_out, F1, F0);
  and and_56 (and_56_out, not_359_out, not_360_out, not_361_out, OP2, not_362_out, not_363_out);
  and and_57 (and_57_out, not_364_out, not_365_out, not_366_out, OP2, not_367_out, OP0);
  and and_58 (and_58_out, not_368_out, not_369_out, not_370_out, not_371_out, not_372_out, not_373_out, not_374_out, not_375_out, F3, not_376_out, not_377_out, not_378_out);
  and and_59 (and_59_out, not_379_out, not_380_out, not_381_out, not_382_out, OP1, not_383_out);
  and and_60 (and_60_out, not_384_out, not_385_out, not_386_out, not_387_out, OP1, OP0);
  not not_388 (not_388_out, in_1);
  or or_1 (or_1_out, and_1_out, and_2_out);
  or or_2 (or_2_out, and_4_out, and_5_out, and_6_out, and_7_out, and_8_out, and_9_out, and_10_out, and_11_out, and_12_out);
  or or_3 (or_3_out, and_35_out, and_36_out, and_37_out, and_38_out, and_39_out, and_40_out, and_41_out, and_42_out, and_43_out);
  and and_61 (MemToReg, or_1_out, not_388_out);
  and and_62 (MemWrite, and_3_out, not_388_out);
  and and_63 (ALU_SRC, or_2_out, not_388_out);
  or or_4 (or_4_out, and_13_out, and_14_out, and_15_out, and_16_out, and_17_out, and_18_out, and_19_out, and_20_out, and_21_out, and_22_out, and_23_out, and_24_out, and_25_out, and_26_out, and_27_out, and_28_out, and_29_out, and_30_out, and_31_out, and_32_out, and_33_out, MFC0);
  or or_5 (or_5_out, and_44_out, and_45_out, and_46_out, and_47_out, and_48_out, and_49_out, and_50_out, and_51_out, and_52_out, and_53_out, and_54_out, and_55_out);
  and and_64 (RegWrite, or_4_out, not_388_out);
  and and_65 (SysCALL, and_34_out, not_388_out);
  and and_66 (SignedExt, or_3_out, not_388_out);
  and and_67 (RegDst, or_5_out, not_388_out);
  and and_68 (BEQ, and_56_out, not_388_out);
  and and_69 (BNE, and_57_out, not_388_out);
  and and_70 (JR, and_58_out, not_388_out);
  and and_71 (JUMP, and_59_out, not_388_out);
  and and_72 (JAL, and_60_out, not_388_out);
  and and_73 (and_73_out, ~OP0, ~OP1, ~OP2, ~OP3, OP4, ~OP5);  // AND_Gate
  and and_74 (and_74_out, ~MF0, ~MF1, ~MF2, ~MF3, ~MF4);  // AND_Gate
  and and_75 (and_75_out, ~MF0, ~MF1, MF2, ~MF3, ~MF4);  // AND_Gate
  and and_76 (and_76_out, ~F0, ~F1, ~F2, F3, F4, ~F5);  // AND_Gate
  not not_389 (not_389_out, OP5);
  not not_390 (not_390_out, OP4);
  not not_391 (not_391_out, OP3);
  not not_392 (not_392_out, OP0);
  not not_393 (not_393_out, OP4);
  not not_394 (not_394_out, OP3);
  not not_395 (not_395_out, OP2);
  not not_396 (not_396_out, OP1);
  not not_397 (not_397_out, OP0);
  and and_77 (MFC0, and_73_out, and_74_out);
  and and_78 (MTC0, and_73_out, and_75_out);
  and and_79 (ERET, and_73_out, and_76_out);
  and and_80 (and_80_out, not_389_out, not_390_out, not_391_out, OP2, OP1, not_392_out);
  and and_81 (and_81_out, OP5, not_393_out, not_394_out, not_395_out, not_396_out, not_397_out);
  and and_82 (BLEZ, and_80_out, not_388_out);
  and and_83 (ReadMode, and_81_out, not_388_out);
endmodule

// ALU
module MIPS_ALU (
  input  [4:0] shamt,
  input  [31:0] X,
  input  [31:0] Y,
  input  [3:0] AluOP,
  output Equal,
  output [31:0] Result,
  output [31:0] Result_2
);

  wire [0:0] comparator_1_lt, comparator_2_lt;
  wire [31:0] adder_1_out, AND_out, divider_1_out, divider_1_rem, multiplier_1_cout, multiplier_1_out,
       NOR_out, OR_out, shifter_1_out, shifter_2_out, shifter_3_out, subtractor_1_out, XOR_out;

  assign AND_out = X & Y;  // AND_Gate AND, 32 bits wide
  assign OR_out = X | Y;  // OR_Gate OR, 32 bits wide
  Shifter #(.width(32)) shifter_1 (.in(Y), .\dist (shamt), .out(shifter_1_out));
  Shifter #(.width(32), .shift("ar")) shifter_2 (.in(Y), .\dist (shamt), .out(shifter_2_out));
  Shifter #(.width(32), .shift("lr")) shifter_3 (.in(Y), .\dist (shamt), .out(shifter_3_out));
  Multiplier #(.width(32)) multiplier_1 (.a(X), .b(Y), .out(multiplier_1_out), .cout(multiplier_1_cout));  // open: cin
  Divider #(.width(32)) divider_1 (.a(X), .b(Y), .out(divider_1_out), .rem(divider_1_rem));  // open: upper
  Adder #(.width(32)) adder_1 (.a(X), .b(Y), .out(adder_1_out));  // open: cin, cout
  Subtractor #(.width(32)) subtractor_1 (.a(X), .b(Y), .out(subtractor_1_out));  // open: bin, bout
  assign XOR_out = X ^ Y;  // XOR_Gate XOR, 32 bits wide
  assign NOR_out = ~(X | Y);  // NOR_Gate NOR, 32 bits wide
  Comparator #(.width(32)) comparator_1 (.a(X), .b(Y), .eq(Equal), .lt(comparator_1_lt[0]));  // open: gt
  Comparator #(.width(32), .mode("unsigned")) comparator_2 (.a(X), .b(Y), .lt(comparator_2_lt[0]));  // open: gt, eq
  Multiplexer #(.select(4), .width(32), .enable("false")) multiplexer_1 (
    .in0(shifter_1_out), .in1(shifter_2_out), .in2(shifter_3_out), .in3(multiplier_1_out),
    .in4(divider_1_out), .in5(adder_1_out), .in6(subtractor_1_out), .in7(AND_out), .in8(OR_out),
    .in9(XOR_out), .in10(NOR_out), .in11({{31{1'b0}}, comparator_1_lt[0]}),
    .in12({{31{1'b0}}, comparator_2_lt[0]}), .in13({32{1'b0}}), .in14({32{1'b0}}), .in15({32{1'b0}}),
    .out(Result), .sel(AluOP));
  Multiplexer #(.select(4), .width(32), .enable("false")) multiplexer_2 (
    .in0({32{1'b0}}), .in1({32{1'b0}}), .in2({32{1'b0}}), .in3(multiplier_1_cout), .in4(divider_1_rem),
    .in5({32{1'b0}}), .in6({32{1'b0}}), .in7({32{1'b0}}), .in8({32{1'b0}}), .in9({32{1'b0}}),
    .in10({32{1'b0}}), .in11({32{1'b0}}), .in12({32{1'b0}}), .in13({32{1'b0}}), .in14({32{1'b0}}),
    .in15({32{1'b0}}), .out(Result_2), .sel(AluOP));

  // Other names for the same wires on the sheet: Result2[31:0] = Result_2; S[3:0] = AluOP

  // Notes on the sheet:
  //   不要改变此引脚区域内容，也不要改变ALU封装形式
  //   输入引脚
  //   输出引脚
endmodule

module MIPS_Regifile (
  input  [31:0] Din,
  input  Clk,
  input  WE,
  input  [4:0] R1_num,
  input  [4:0] W_num,
  input  [4:0] R2_num,
  output [31:0] R1,
  output [31:0] R2
);

  // RegisterFile registerfile_1: pin names not known; wires that end beside it: Din, Clk, WE, W_num, R1_num, R2_num, R1, R2
endmodule

module \理想流水线  (
  output RegWrite,
  output MemWrite,
  output [31:0] IF_PC,
  output [31:0] ID_PC,
  output [31:0] EX_PC,
  output [31:0] M_PC,
  output [31:0] WB_PC,
  output [31:0] RDin,
  output [31:0] MDin,
  output [31:0] LedData
);

  wire and_1_out, and_2_out, CLK, comparator_1_eq, Go, IR1, IR2, IR3, not_1_out, not_2_out, nStop, or_1_out,
       or_2_out, register_2_q, RST, rused_1__1, rused_1__2, Syscall, W1, W2, W3, \气泡 ,
       \重定向流水线控制信号_1_syscall , \重定向流水线跳转逻辑_1_normal ;
  wire [0:0] \重定向锁存器3_1_dout32_3 ;
  wire [3:0] \重定向流水线控制信号_1_aluop ;
  wire [4:0] IDShamt, \译码逻辑输出信号_1_r1 , \译码逻辑输出信号_1_r2 , \译码逻辑输出信号_1_w_num ;
  wire [6:0] \重定向锁存器3_1_dout32_3_2 , \重定向锁存器4_1_dout32_3 ;
  wire [9:0] \重定向流水线控制信号_1_readmode ;
  wire [15:0] adder_2_out, \LoadUse次数 , \总周期数 , \插入气泡数 , \无条件分支数 , \条件分支成功数 ;
  wire [19:0] \重定向锁存器2_1_dout32_8 ;
  wire [31:0] adder_1_out, mips_alu_1_result, mips_regifile_1_r1, mips_regifile_1_r2, multiplexer_1_out,
       multiplexer_2_out, rom_1_data, \四路存储器_1_memory , \译码逻辑输出信号_1_immediate , \重定向流水线跳转逻辑_1_nextpc ,
       \重定向锁存器2_1_dout32_7 , \重定向锁存器2_1_dout32_9 , \重定向锁存器2_1_dout32_10 , \重定向锁存器2_1_dout32_11 ,
       \重定向锁存器2_1_dout32_12 , \重定向锁存器3_1_dout32_2 , \重定向锁存器3_1_dout32_4 , \重定向锁存器4_1_dout32_2 ,
       \重定向锁存器4_1_dout32_4 , \锁存器1_1_dout32_3 , \锁存器1_1_dout32_4 ;

  Button \u_总复位  (.out(RST));
  Button _1 (.out(IR1));
  Button _2 (.out(IR2));
  Button _3 (.out(IR3));
  Button \u_继续运行  (.out(Go));
  LED led_1 (.in(W1));
  LED led_2 (.in(W2));
  LED led_3 (.in(W3));
  Button button_1 (.out(RST));
  Hex_Digit_Display hex_digit_display_1 (.value(LedData[31:28]));  // open: dp
  Register #(.width(32)) PC (.D(\重定向流水线跳转逻辑_1_nextpc ), .Q(IF_PC), .clk(CLK), .clr(RST));  // open: en
  Register #(.width(16)) register_1 (.D(adder_2_out), .Q(\总周期数 ), .clk(CLK), .clr(RST));  // open: en
  Hex_Digit_Display hex_digit_display_2 (.value(LedData[27:24]));  // open: dp
  Hex_Digit_Display hex_digit_display_3 (.value(LedData[23:20]));  // open: dp
  Adder #(.width(32)) adder_1 (.a(32'h4), .b(IF_PC), .out(adder_1_out));  // open: cin, cout
  Adder #(.width(16)) adder_2 (.a(16'h1), .b(\总周期数 ), .out(adder_2_out));  // open: cin, cout
  Hex_Digit_Display hex_digit_display_4 (.value(LedData[15:12]));  // open: dp
  Hex_Digit_Display hex_digit_display_5 (.value(LedData[19:16]));  // open: dp
  Hex_Digit_Display hex_digit_display_6 (.value(LedData[11:8]));  // open: dp
  Hex_Digit_Display hex_digit_display_7 (.value(LedData[7:4]));  // open: dp
  Clock clock_1 (.out(CLK));
  not not_1 (not_1_out, \重定向流水线跳转逻辑_1_normal );
  \锁存器1  \u_锁存器1_1  (
    .Din32_3(adder_1_out), .Din32_4(rom_1_data), .CLK(CLK), .Dout32_3(\锁存器1_1_dout32_3 ),
    .Dout32_4(\锁存器1_1_dout32_4 ), .\同步清零_气泡_高电平有效 (not_1_out), .Din32(IF_PC), .Dout32(ID_PC));  // open: Din32_2, 传输状态In_表明当前传输数据有效, Dout32_2, 传输状态Out_表明当前传输数据有效, 使能端_低电平有效_stall_高电平有效
  ROM #(.addrWidth(10), .dataWidth(32)) rom_1 (.addr(IF_PC[11:2]), .data(rom_1_data));  // open: sel
  Hex_Digit_Display hex_digit_display_8 (.value(LedData[3:0]));  // open: dp
  \重定向流水线控制信号  \u_重定向流水线控制信号_1  (
    .in_1(1'b0), .in_2(\锁存器1_1_dout32_4 ), .MemToReg(\重定向流水线控制信号_1_readmode [1]),
    .ReadMode(\重定向流水线控制信号_1_readmode [0]), .MemWrite(\重定向流水线控制信号_1_readmode [2]),
    .AluOP(\重定向流水线控制信号_1_aluop ), .ALU_SRC(\重定向流水线控制信号_1_readmode [7]),
    .RegWrite(\重定向流水线控制信号_1_readmode [8]), .SysCALL(\重定向流水线控制信号_1_syscall ), .JAL(\重定向流水线控制信号_1_readmode [9]));  // open: MFC0, MTC0, ERET
  \译码逻辑输出信号  \u_译码逻辑输出信号_1  (
    .in_1(\锁存器1_1_dout32_4 ), .R1(\译码逻辑输出信号_1_r1 ), .R2(\译码逻辑输出信号_1_r2 ), .W_num(\译码逻辑输出信号_1_w_num ),
    .Immediate(\译码逻辑输出信号_1_immediate ), .shamt(IDShamt));
  // Probe on \总周期数 
  // Probe on \无条件分支数 
  // Probe on \条件分支成功数 
  // Probe on \插入气泡数 
  // Probe on \LoadUse次数 
  // Probe on IF_PC[11:0]
  not not_2 (not_2_out, \重定向流水线跳转逻辑_1_normal );
  or or_1 (or_1_out, not_2_out, \气泡 );
  MIPS_Regifile mips_regifile_1 (
    .Din(RDin), .Clk(CLK), .R1(mips_regifile_1_r1), .R2(mips_regifile_1_r2), .WE(RegWrite),
    .W_num(\重定向锁存器4_1_dout32_3 [6:2]), .R1_num(\译码逻辑输出信号_1_r1 ), .R2_num(\译码逻辑输出信号_1_r2 ));
  // Probe on EX_PC[11:0]
  // Probe on ID_PC[11:0]
  \重定向流水线跳转逻辑  \u_重定向流水线跳转逻辑_1  (
    .IP(\重定向锁存器2_1_dout32_7 ), .R1(\重定向锁存器2_1_dout32_10 ), .R2(\重定向锁存器2_1_dout32_11 ), .PC_8(adder_1_out),
    .NextPC(\重定向流水线跳转逻辑_1_nextpc ), .Normal(\重定向流水线跳转逻辑_1_normal ), .PC_4(\重定向锁存器2_1_dout32_9 ));  // open: JumpAddress, JalJumpBranch
  \重定向锁存器2  \u_重定向锁存器2_1  (
    .Din32_6(\重定向流水线控制信号_1_syscall ), .Din32_7(\锁存器1_1_dout32_4 ),
    .Din32_8({\译码逻辑输出信号_1_w_num , IDShamt, \重定向流水线控制信号_1_readmode [9:7], \重定向流水线控制信号_1_aluop , \重定向流水线控制信号_1_readmode [2:0]}),
    .Din32_9(\锁存器1_1_dout32_3 ), .Din32_10(mips_regifile_1_r1), .Din32_11(mips_regifile_1_r2),
    .Din32_12(\译码逻辑输出信号_1_immediate ), .CLK(CLK), .Dout32_6(Syscall), .Dout32_7(\重定向锁存器2_1_dout32_7 ),
    .Dout32_8(\重定向锁存器2_1_dout32_8 ), .Dout32_9(\重定向锁存器2_1_dout32_9 ), .Dout32_10(\重定向锁存器2_1_dout32_10 ),
    .Dout32_11(\重定向锁存器2_1_dout32_11 ), .Dout32_12(\重定向锁存器2_1_dout32_12 ), .\同步清零_气泡_高电平有效 (or_1_out),
    .Din32_2(ID_PC), .Dout32_2(EX_PC));  // open: Din32_3, Din32_4, Din32_5, Dout32_3, Dout32_4, Dout32_5, 使能端_低电平有效_stall_高电平有效, Din32, Dout32
  // Probe on M_PC[11:0]
  // Probe on WB_PC[11:0]
  Multiplexer #(.width(32), .enable("false")) multiplexer_1 (
    .in0(\重定向锁存器2_1_dout32_11 ), .in1(\重定向锁存器2_1_dout32_12 ), .out(multiplexer_1_out),
    .sel(\重定向锁存器2_1_dout32_8 [7]));
  Comparator #(.width(32)) comparator_1 (.a(\重定向锁存器2_1_dout32_11 ), .b(32'h22), .eq(comparator_1_eq));  // open: gt, lt
  MIPS_ALU mips_alu_1 (
    .X(\重定向锁存器2_1_dout32_10 ), .Y(multiplexer_1_out), .AluOP(\重定向锁存器2_1_dout32_8 [6:3]),
    .Result(mips_alu_1_result), .shamt(\重定向锁存器2_1_dout32_8 [14:10]));  // open: Equal, Result_2
  and and_1 (and_1_out, Syscall, comparator_1_eq);
  and and_2 (and_2_out, Syscall, ~comparator_1_eq);  // AND_Gate
  \重定向锁存器3  \u_重定向锁存器3_1  (
    .Din32_2(multiplexer_2_out),
    .Din32_3({\重定向锁存器2_1_dout32_8 [19:15], \重定向锁存器2_1_dout32_8 [8], \重定向锁存器2_1_dout32_8 [2:0]}),
    .Din32_4(mips_alu_1_result), .Din32_5(\重定向锁存器2_1_dout32_11 ), .CLK(CLK), .Dout32_2(\重定向锁存器3_1_dout32_2 ),
    .Dout32_3({\重定向锁存器3_1_dout32_3_2 [6:1], MemWrite, \重定向锁存器3_1_dout32_3_2 [0], \重定向锁存器3_1_dout32_3 [0]}),
    .Dout32_4(\重定向锁存器3_1_dout32_4 ), .Dout32_5(MDin), .\使能端_低电平有效_stall_高电平有效 (1'b0), .Din32(EX_PC),
    .Dout32(M_PC));  // open: 传输状态In_表明当前传输数据有效, 传输状态Out_表明当前传输数据有效, 同步清零_气泡_高电平有效
  Multiplexer #(.width(32), .enable("false")) multiplexer_2 (
    .in0(mips_alu_1_result), .in1(\重定向锁存器2_1_dout32_9 ), .out(multiplexer_2_out),
    .sel(\重定向锁存器2_1_dout32_8 [9]));
  not not_3 (nStop, register_2_q);
  Register #(.width(1)) register_2 (.D(and_2_out), .en(nStop), .Q(register_2_q), .clk(CLK), .clr(or_2_out));
  or or_2 (or_2_out, Go, RST);
  Register #(.width(32)) register_3 (.D(\重定向锁存器2_1_dout32_10 ), .en(and_1_out), .Q(LedData), .clk(CLK), .clr(RST));
  RUsed rused_1 (
    .ExRegWrite(\重定向锁存器2_1_dout32_8 [8]), .ExR(\重定向锁存器2_1_dout32_8 [19:15]), .IP(\锁存器1_1_dout32_4 ),
    .MemRegWrite(\重定向锁存器3_1_dout32_3_2 [1]), .MemR(\重定向锁存器3_1_dout32_3_2 [6:2]), ._1(rused_1__1),
    ._2(rused_1__2));
  or or_3 (\气泡 , rused_1__1, rused_1__2);
  \重定向锁存器4  \u_重定向锁存器4_1  (
    .Din32_2(\重定向锁存器3_1_dout32_2 ), .Din32_3(\重定向锁存器3_1_dout32_3_2 ), .Din32_4(\四路存储器_1_memory ), .CLK(CLK),
    .Dout32_2(\重定向锁存器4_1_dout32_2 ),
    .Dout32_3({\重定向锁存器4_1_dout32_3 [6:2], RegWrite, \重定向锁存器4_1_dout32_3 [0]}),
    .Dout32_4(\重定向锁存器4_1_dout32_4 ), .\使能端_低电平有效_stall_高电平有效 (1'b0), .Din32(M_PC), .Dout32(WB_PC));  // open: 传输状态In_表明当前传输数据有效, 传输状态Out_表明当前传输数据有效, 同步清零_气泡_高电平有效
  \四路存储器  \u_四路存储器_1  (
    .CLK(CLK), .Address(\重定向锁存器3_1_dout32_4 ), .Memory(\四路存储器_1_memory ), .MemWrite(MemWrite),
    .Mode(\重定向锁存器3_1_dout32_3 [0]), .Data(MDin), .RST(RST));
  Multiplexer #(.width(32), .enable("false")) multiplexer_3 (
    .in0(\重定向锁存器4_1_dout32_2 ), .in1(\重定向锁存器4_1_dout32_4 ), .out(RDin), .sel(\重定向锁存器4_1_dout32_3 [0]));

  // Other names for the same wires on the sheet: MEM_PC[31:0] = M_PC

  // Notes on the sheet:
  //   中断源
  //   中断等待指示
  //   数码管输出
  //   contents of rom_1 (hex, n*v repeats v):
  //   20100000 20110000 20120000 20130000 36100000 36310001 36520002 36730003 ae100000 ae110004 ae120008
  //   ae13000c 2002000a 20110000 20120000 20130000 c
  //   流水调试日志用
  //   为方便自动评测，需要输出流水线各段保存的PC值，注意是PC不是PC+4，另外ID段寄存器写入信息，Mem段内存写入信息也要输出
endmodule

module \气泡流水线  (
  output RegWrite,
  output MemWrite,
  output [31:0] IF_PC,
  output [31:0] ID_PC,
  output [31:0] EX_PC,
  output [31:0] M_PC,
  output [31:0] WB_PC,
  output [31:0] RDin,
  output [31:0] MDin,
  output [31:0] LedData
);

  wire and_1_out, and_2_out, and_3_out, CLK, comparator_1_eq, Go, IR1, IR2, IR3, not_1_out, not_2_out,
       not_3_out, nStop, or_1_out, or_2_out, or_3_out, register_2_q, RST, rused_1__1, rused_1__2, Syscall,
       W1, W2, W3, \气泡 , \重定向流水线控制信号_1_syscall , \重定向流水线跳转逻辑_1_normal ;
  wire [0:0] \重定向锁存器3_1_dout32_3 ;
  wire [3:0] \重定向流水线控制信号_1_aluop ;
  wire [4:0] IDShamt, \译码逻辑输出信号_1_r1 , \译码逻辑输出信号_1_r2 , \译码逻辑输出信号_1_w_num ;
  wire [6:0] \重定向锁存器3_1_dout32_3_2 , \重定向锁存器4_1_dout32_3 ;
  wire [9:0] \重定向流水线控制信号_1_readmode ;
  wire [15:0] adder_2_out, \LoadUse次数 , \总周期数 , \插入气泡数 , \无条件分支数 , \条件分支成功数 ;
  wire [19:0] \重定向锁存器2_1_dout32_8 ;
  wire [31:0] adder_1_out, mips_alu_1_result, mips_fregifile_1_r1, mips_fregifile_1_r2, multiplexer_1_out,
       multiplexer_2_out, rom_1_data, \四路存储器_1_memory , \译码逻辑输出信号_1_immediate , \重定向流水线跳转逻辑_1_nextpc ,
       \重定向锁存器2_1_dout32_7 , \重定向锁存器2_1_dout32_9 , \重定向锁存器2_1_dout32_10 , \重定向锁存器2_1_dout32_11 ,
       \重定向锁存器2_1_dout32_12 , \重定向锁存器3_1_dout32_2 , \重定向锁存器3_1_dout32_4 , \重定向锁存器4_1_dout32_2 ,
       \重定向锁存器4_1_dout32_4 , \锁存器1_1_dout32_3 , \锁存器1_1_dout32_4 ;

  Button \u_总复位  (.out(RST));
  Button _1 (.out(IR1));
  Button _2 (.out(IR2));
  Button _3 (.out(IR3));
  Button \u_继续运行  (.out(Go));
  LED led_1 (.in(W1));
  LED led_2 (.in(W2));
  LED led_3 (.in(W3));
  Button button_1 (.out(RST));
  and and_1 (and_1_out, nStop, ~\气泡 );  // AND_Gate
  Hex_Digit_Display hex_digit_display_1 (.value(LedData[31:28]));  // open: dp
  Register #(.width(32)) PC (.D(\重定向流水线跳转逻辑_1_nextpc ), .en(and_1_out), .Q(IF_PC), .clk(CLK), .clr(RST));
  Register #(.width(16)) register_1 (.D(adder_2_out), .Q(\总周期数 ), .clk(CLK), .clr(RST));  // open: en
  Hex_Digit_Display hex_digit_display_2 (.value(LedData[27:24]));  // open: dp
  Hex_Digit_Display hex_digit_display_3 (.value(LedData[23:20]));  // open: dp
  Adder #(.width(32)) adder_1 (.a(32'h4), .b(IF_PC), .out(adder_1_out));  // open: cin, cout
  Adder #(.width(16)) adder_2 (.a(16'h1), .b(\总周期数 ), .out(adder_2_out));  // open: cin, cout
  Hex_Digit_Display hex_digit_display_4 (.value(LedData[19:16]));  // open: dp
  Hex_Digit_Display hex_digit_display_5 (.value(LedData[15:12]));  // open: dp
  not not_1 (not_1_out, nStop);
  Hex_Digit_Display hex_digit_display_6 (.value(LedData[11:8]));  // open: dp
  Hex_Digit_Display hex_digit_display_7 (.value(LedData[7:4]));  // open: dp
  Clock clock_1 (.out(CLK));
  not not_2 (not_2_out, \重定向流水线跳转逻辑_1_normal );
  \锁存器1  \u_锁存器1_1  (
    .Din32_3(adder_1_out), .Din32_4(rom_1_data), .CLK(CLK), .Dout32_3(\锁存器1_1_dout32_3 ),
    .Dout32_4(\锁存器1_1_dout32_4 ), .\同步清零_气泡_高电平有效 (not_2_out), .\使能端_低电平有效_stall_高电平有效 (or_1_out),
    .Din32(IF_PC), .Dout32(ID_PC));  // open: Din32_2, 传输状态In_表明当前传输数据有效, Dout32_2, 传输状态Out_表明当前传输数据有效
  ROM #(.addrWidth(10), .dataWidth(32)) rom_1 (.addr(IF_PC[11:2]), .data(rom_1_data));  // open: sel
  or or_1 (or_1_out, not_1_out, \气泡 );
  Hex_Digit_Display hex_digit_display_8 (.value(LedData[3:0]));  // open: dp
  \重定向流水线控制信号  \u_重定向流水线控制信号_1  (
    .in_1(1'b0), .in_2(\锁存器1_1_dout32_4 ), .MemToReg(\重定向流水线控制信号_1_readmode [1]),
    .ReadMode(\重定向流水线控制信号_1_readmode [0]), .MemWrite(\重定向流水线控制信号_1_readmode [2]),
    .AluOP(\重定向流水线控制信号_1_aluop ), .ALU_SRC(\重定向流水线控制信号_1_readmode [7]),
    .RegWrite(\重定向流水线控制信号_1_readmode [8]), .SysCALL(\重定向流水线控制信号_1_syscall ), .JAL(\重定向流水线控制信号_1_readmode [9]));  // open: MFC0, MTC0, ERET
  \译码逻辑输出信号  \u_译码逻辑输出信号_1  (
    .in_1(\锁存器1_1_dout32_4 ), .R1(\译码逻辑输出信号_1_r1 ), .R2(\译码逻辑输出信号_1_r2 ), .W_num(\译码逻辑输出信号_1_w_num ),
    .Immediate(\译码逻辑输出信号_1_immediate ), .shamt(IDShamt));
  // Probe on \总周期数 
  // Probe on \无条件分支数 
  // Probe on \条件分支成功数 
  // Probe on \插入气泡数 
  // Probe on \LoadUse次数 
  // Probe on IF_PC[11:0]
  not not_3 (not_3_out, \重定向流水线跳转逻辑_1_normal );
  or or_2 (or_2_out, not_3_out, \气泡 );
  MIPS_FRegifile mips_fregifile_1 (
    .Din(RDin), .Clk(CLK), .R1(mips_fregifile_1_r1), .R2(mips_fregifile_1_r2), .WE(RegWrite),
    .W_num(\重定向锁存器4_1_dout32_3 [6:2]), .R1_num(\译码逻辑输出信号_1_r1 ), .R2_num(\译码逻辑输出信号_1_r2 ));
  // Probe on ID_PC[11:0]
  // Probe on EX_PC[11:0]
  \重定向流水线跳转逻辑  \u_重定向流水线跳转逻辑_1  (
    .IP(\重定向锁存器2_1_dout32_7 ), .R1(\重定向锁存器2_1_dout32_10 ), .R2(\重定向锁存器2_1_dout32_11 ), .PC_8(adder_1_out),
    .NextPC(\重定向流水线跳转逻辑_1_nextpc ), .Normal(\重定向流水线跳转逻辑_1_normal ), .PC_4(\重定向锁存器2_1_dout32_9 ));  // open: JumpAddress, JalJumpBranch
  \重定向锁存器2  \u_重定向锁存器2_1  (
    .Din32_6(\重定向流水线控制信号_1_syscall ), .Din32_7(\锁存器1_1_dout32_4 ),
    .Din32_8({\译码逻辑输出信号_1_w_num , IDShamt, \重定向流水线控制信号_1_readmode [9:7], \重定向流水线控制信号_1_aluop , \重定向流水线控制信号_1_readmode [2:0]}),
    .Din32_9(\锁存器1_1_dout32_3 ), .Din32_10(mips_fregifile_1_r1), .Din32_11(mips_fregifile_1_r2),
    .Din32_12(\译码逻辑输出信号_1_immediate ), .CLK(CLK), .Dout32_6(Syscall), .Dout32_7(\重定向锁存器2_1_dout32_7 ),
    .Dout32_8(\重定向锁存器2_1_dout32_8 ), .Dout32_9(\重定向锁存器2_1_dout32_9 ), .Dout32_10(\重定向锁存器2_1_dout32_10 ),
    .Dout32_11(\重定向锁存器2_1_dout32_11 ), .Dout32_12(\重定向锁存器2_1_dout32_12 ), .\同步清零_气泡_高电平有效 (or_2_out),
    .Din32_2(ID_PC), .Dout32_2(EX_PC));  // open: Din32_3, Din32_4, Din32_5, Dout32_3, Dout32_4, Dout32_5, 使能端_低电平有效_stall_高电平有效, Din32, Dout32
  // Probe on M_PC[11:0]
  // Probe on WB_PC[11:0]
  Multiplexer #(.width(32), .enable("false")) multiplexer_1 (
    .in0(\重定向锁存器2_1_dout32_11 ), .in1(\重定向锁存器2_1_dout32_12 ), .out(multiplexer_1_out),
    .sel(\重定向锁存器2_1_dout32_8 [7]));
  Comparator #(.width(32)) comparator_1 (.a(\重定向锁存器2_1_dout32_11 ), .b(32'h22), .eq(comparator_1_eq));  // open: gt, lt
  MIPS_ALU mips_alu_1 (
    .X(\重定向锁存器2_1_dout32_10 ), .Y(multiplexer_1_out), .AluOP(\重定向锁存器2_1_dout32_8 [6:3]),
    .Result(mips_alu_1_result), .shamt(\重定向锁存器2_1_dout32_8 [14:10]));  // open: Equal, Result_2
  and and_2 (and_2_out, Syscall, comparator_1_eq);
  and and_3 (and_3_out, Syscall, ~comparator_1_eq);  // AND_Gate
  \重定向锁存器3  \u_重定向锁存器3_1  (
    .Din32_2(multiplexer_2_out),
    .Din32_3({\重定向锁存器2_1_dout32_8 [19:15], \重定向锁存器2_1_dout32_8 [8], \重定向锁存器2_1_dout32_8 [2:0]}),
    .Din32_4(mips_alu_1_result), .Din32_5(\重定向锁存器2_1_dout32_11 ), .CLK(CLK), .Dout32_2(\重定向锁存器3_1_dout32_2 ),
    .Dout32_3({\重定向锁存器3_1_dout32_3_2 [6:1], MemWrite, \重定向锁存器3_1_dout32_3_2 [0], \重定向锁存器3_1_dout32_3 [0]}),
    .Dout32_4(\重定向锁存器3_1_dout32_4 ), .Dout32_5(MDin), .\使能端_低电平有效_stall_高电平有效 (1'b0), .Din32(EX_PC),
    .Dout32(M_PC));  // open: 传输状态In_表明当前传输数据有效, 传输状态Out_表明当前传输数据有效, 同步清零_气泡_高电平有效
  Multiplexer #(.width(32), .enable("false")) multiplexer_2 (
    .in0(mips_alu_1_result), .in1(\重定向锁存器2_1_dout32_9 ), .out(multiplexer_2_out),
    .sel(\重定向锁存器2_1_dout32_8 [9]));
  Register #(.width(1)) register_2 (.D(and_3_out), .en(nStop), .Q(register_2_q), .clk(CLK), .clr(or_3_out));
  not not_4 (nStop, register_2_q);
  or or_3 (or_3_out, Go, RST);
  Register #(.width(32)) register_3 (.D(\重定向锁存器2_1_dout32_10 ), .en(and_2_out), .Q(LedData), .clk(CLK), .clr(RST));
  RUsed rused_1 (
    .ExRegWrite(\重定向锁存器2_1_dout32_8 [8]), .ExR(\重定向锁存器2_1_dout32_8 [19:15]), .IP(\锁存器1_1_dout32_4 ),
    .MemRegWrite(\重定向锁存器3_1_dout32_3_2 [1]), .MemR(\重定向锁存器3_1_dout32_3_2 [6:2]), ._1(rused_1__1),
    ._2(rused_1__2));
  or or_4 (\气泡 , rused_1__1, rused_1__2);
  \重定向锁存器4  \u_重定向锁存器4_1  (
    .Din32_2(\重定向锁存器3_1_dout32_2 ), .Din32_3(\重定向锁存器3_1_dout32_3_2 ), .Din32_4(\四路存储器_1_memory ), .CLK(CLK),
    .Dout32_2(\重定向锁存器4_1_dout32_2 ),
    .Dout32_3({\重定向锁存器4_1_dout32_3 [6:2], RegWrite, \重定向锁存器4_1_dout32_3 [0]}),
    .Dout32_4(\重定向锁存器4_1_dout32_4 ), .\使能端_低电平有效_stall_高电平有效 (1'b0), .Din32(M_PC), .Dout32(WB_PC));  // open: 传输状态In_表明当前传输数据有效, 传输状态Out_表明当前传输数据有效, 同步清零_气泡_高电平有效
  \四路存储器  \u_四路存储器_1  (
    .CLK(CLK), .Address(\重定向锁存器3_1_dout32_4 ), .Memory(\四路存储器_1_memory ), .MemWrite(MemWrite),
    .Mode(\重定向锁存器3_1_dout32_3 [0]), .Data(MDin), .RST(RST));
  Multiplexer #(.width(32), .enable("false")) multiplexer_3 (
    .in0(\重定向锁存器4_1_dout32_2 ), .in1(\重定向锁存器4_1_dout32_4 ), .out(RDin), .sel(\重定向锁存器4_1_dout32_3 [0]));

  // Other names for the same wires on the sheet: MEM_PC[31:0] = M_PC

  // Notes on the sheet:
  //   中断源
  //   中断等待指示
  //   数码管输出
  //   contents of rom_1 (hex, n*v repeats v):
  //   20110001 8000c05 20110001 20120002 20130003 8000c09 20110001 20120002 20130003 8000c0d 20110001
  //   20120002 20130003 8000c11 20110001 20120002 20130003 c000cb8 20100001 20110001 118fc0 112020
  //   20020022 c 118882 12200001 8000c15 112020 20020022 c 20110001 118880 112020 20020022 c 12200001
  //   8000c1f 20110001 118fc0 112020 20020022 c 1188c3 112020 20020022 c 118903 112020 20020022 c 118903
  //   112020 20020022 c 118903 112020 20020022 c 118903 112020 20020022 c 118903 112020 20020022 c 118903
  //   112020 20020022 c 118903 112020 20020022 c 20100001 109fc0 139fc3 8021 2012000c 24160003 26100001
  //   3210000f 20080008 20090001 139900 2709825 132020 20020022 c 1094022 1500fff9 22100001 2018000f
  //   2188024 108700 20080008 20090001 139902 2709825 132021 20020022 c 1094022 1500fff9 108702 2c9b022
  //   12c00001 8000c50 4020 1084027 84400 3508ffff 82021 20020022 c 2010ffff 20110000 ae300000 22100001
  //   22310004 ae300000 22100001 22310004 ae300000 22100001 22310004 ae300000 22100001 22310004 ae300000
  //   22100001 22310004 ae300000 22100001 22310004 ae300000 22100001 22310004 ae300000 22100001 22310004
  //   ae300000 22100001 22310004 ae300000 22100001 22310004 ae300000 22100001 22310004 ae300000 22100001
  //   22310004 ae300000 22100001 22310004 ae300000 22100001 22310004 ae300000 22100001 22310004 ae300000
  //   22100001 22310004 22100001 8020 2011003c 8e130000 8e340000 274402a 11000002 ae330000 ae140000
  //   2231fffc 1611fff8 102020 20020022 c 22100004 2011003c 1611fff2 20020032 c 20100000 22100001 102020
  //   20020022 c 22100002 102020 20020022 c 22100003 102020 20020022 c 22100004 102020 20020022 c 22100005
  //   102020 20020022 c 22100006 102020 20020022 c 22100007 102020 20020022 c 22100008 102020 20020022
  //   20020022 c 3e00008
  //   流水调试日志用
  //   为方便自动评测，需要输出流水线各段保存的PC值，注意是PC不是PC+4，另外ID段寄存器写入信息，Mem段内存写入信息也要输出
endmodule

module \重定向流水线  (
  output RegWrite,
  output MemWrite,
  output [31:0] IF_PC,
  output [31:0] ID_PC,
  output [31:0] EX_PC,
  output [31:0] M_PC,
  output [31:0] WB_PC,
  output [31:0] RDin,
  output [31:0] MDin,
  output [31:0] LedData
);

  wire and_1_out, and_2_out, CLK, comparator_1_eq, Go, IR1, IR2, IR3, not_1_out, not_2_out, not_3_out, nStop,
       or_1_out, or_2_out, register_1_q, RST, Syscall, W1, W2, W3, \气泡 , \重定向流水线控制信号_1_syscall ,
       \重定向流水线跳转逻辑_1_normal ;
  wire [1:0] \重定向锁存器2_1_dout32 , \重定向锁存器2_1_dout32_2 ;
  wire [3:0] Select, \重定向流水线控制信号_1_aluop , \重定向锁存器3_1_dout32_3 ;
  wire [4:0] IDShamt, \译码逻辑输出信号_1_r1 , \译码逻辑输出信号_1_r2 , \译码逻辑输出信号_1_w_num , \重定向锁存器2_1_dout32_8_2 ,
       \重定向锁存器3_1_dout32_3_2 ;
  wire [6:0] \重定向锁存器4_1_dout32_3 ;
  wire [9:0] \重定向流水线控制信号_1_readmode ;
  wire [14:0] \重定向锁存器2_1_dout32_8 ;
  wire [15:0] \LoadUse次数 , \总周期数 , \插入气泡数 , \无条件分支数 , \条件分支成功数 ;
  wire [31:0] adder_1_out, mips_alu_1_result, mips_fregifile_1_r1, mips_fregifile_1_r2, multiplexer_1_out,
       multiplexer_2_out, multiplexer_3_out, multiplexer_4_out, rom_1_data, \四路存储器_1_memory ,
       \译码逻辑输出信号_1_immediate , \重定向流水线跳转逻辑_1_nextpc , \重定向锁存器2_1_dout32_7 , \重定向锁存器2_1_dout32_9 ,
       \重定向锁存器2_1_dout32_10 , \重定向锁存器2_1_dout32_11 , \重定向锁存器2_1_dout32_12 , \重定向锁存器3_1_dout32_2 ,
       \重定向锁存器3_1_dout32_4 , \重定向锁存器4_1_dout32_2 , \重定向锁存器4_1_dout32_4 , \锁存器1_1_dout32_3 , \锁存器1_1_dout32_4 ;

  Button \u_总复位  (.out(RST));
  Button _1 (.out(IR1));
  Button _2 (.out(IR2));
  Button _3 (.out(IR3));
  Button \u_继续运行  (.out(Go));
  LED led_1 (.in(W1));
  LED led_2 (.in(W2));
  LED led_3 (.in(W3));
  Button button_1 (.out(RST));
  not not_1 (not_1_out, \气泡 );
  Hex_Digit_Display hex_digit_display_1 (.value(LedData[31:28]));  // open: dp
  Register #(.width(32)) PC (.D(\重定向流水线跳转逻辑_1_nextpc ), .en(not_1_out), .Q(IF_PC), .clk(CLK), .clr(RST));
  Hex_Digit_Display hex_digit_display_2 (.value(LedData[23:20]));  // open: dp
  Hex_Digit_Display hex_digit_display_3 (.value(LedData[27:24]));  // open: dp
  Adder #(.width(32)) adder_1 (.a(32'h4), .b(IF_PC), .out(adder_1_out));  // open: cin, cout
  Clock clock_1 (.out(CLK));
  Hex_Digit_Display hex_digit_display_4 (.value(LedData[15:12]));  // open: dp
  Hex_Digit_Display hex_digit_display_5 (.value(LedData[19:16]));  // open: dp
  Hex_Digit_Display hex_digit_display_6 (.value(LedData[11:8]));  // open: dp
  Hex_Digit_Display hex_digit_display_7 (.value(LedData[7:4]));  // open: dp
  not not_2 (not_2_out, \重定向流水线跳转逻辑_1_normal );
  \锁存器1  \u_锁存器1_1  (
    .Din32_3(adder_1_out), .Din32_4(rom_1_data), .CLK(CLK), .Dout32_3(\锁存器1_1_dout32_3 ),
    .Dout32_4(\锁存器1_1_dout32_4 ), .\同步清零_气泡_高电平有效 (not_2_out), .\使能端_低电平有效_stall_高电平有效 (\气泡 ), .Din32(IF_PC),
    .Dout32(ID_PC));  // open: Din32_2, 传输状态In_表明当前传输数据有效, Dout32_2, 传输状态Out_表明当前传输数据有效
  ROM #(.addrWidth(10), .dataWidth(32)) rom_1 (.addr(IF_PC[11:2]), .data(rom_1_data));  // open: sel
  Hex_Digit_Display hex_digit_display_8 (.value(LedData[3:0]));  // open: dp
  \重定向流水线控制信号  \u_重定向流水线控制信号_1  (
    .in_1(1'b0), .in_2(\锁存器1_1_dout32_4 ), .MemToReg(\重定向流水线控制信号_1_readmode [1]),
    .ReadMode(\重定向流水线控制信号_1_readmode [0]), .MemWrite(\重定向流水线控制信号_1_readmode [2]),
    .AluOP(\重定向流水线控制信号_1_aluop ), .ALU_SRC(\重定向流水线控制信号_1_readmode [7]),
    .RegWrite(\重定向流水线控制信号_1_readmode [8]), .SysCALL(\重定向流水线控制信号_1_syscall ), .JAL(\重定向流水线控制信号_1_readmode [9]));  // open: MFC0, MTC0, ERET
  \译码逻辑输出信号  \u_译码逻辑输出信号_1  (
    .in_1(\锁存器1_1_dout32_4 ), .R1(\译码逻辑输出信号_1_r1 ), .R2(\译码逻辑输出信号_1_r2 ), .W_num(\译码逻辑输出信号_1_w_num ),
    .Immediate(\译码逻辑输出信号_1_immediate ), .shamt(IDShamt));
  // Probe on \总周期数 
  // Probe on \无条件分支数 
  // Probe on \条件分支成功数 
  // Probe on \插入气泡数 
  // Probe on \LoadUse次数 
  // Probe on IF_PC[11:0]
  not not_3 (not_3_out, \重定向流水线跳转逻辑_1_normal );
  MIPS_FRegifile mips_fregifile_1 (
    .Din(RDin), .Clk(CLK), .R1(mips_fregifile_1_r1), .R2(mips_fregifile_1_r2), .WE(RegWrite),
    .W_num(\重定向锁存器4_1_dout32_3 [6:2]), .R1_num(\译码逻辑输出信号_1_r1 ), .R2_num(\译码逻辑输出信号_1_r2 ));
  // Probe on ID_PC[11:0]
  // Probe on EX_PC[11:0]
  \重定向流水线跳转逻辑  \u_重定向流水线跳转逻辑_1  (
    .IP(\重定向锁存器2_1_dout32_7 ), .R1(multiplexer_1_out), .R2(multiplexer_2_out), .PC_8(adder_1_out),
    .NextPC(\重定向流水线跳转逻辑_1_nextpc ), .Normal(\重定向流水线跳转逻辑_1_normal ), .PC_4(\重定向锁存器2_1_dout32_9 ));  // open: JumpAddress, JalJumpBranch
  or or_1 (or_1_out, not_3_out, \气泡 );
  \重定向锁存器2  \u_重定向锁存器2_1  (
    .Din32_6(\重定向流水线控制信号_1_syscall ), .Din32_7(\锁存器1_1_dout32_4 ),
    .Din32_8({\译码逻辑输出信号_1_w_num , IDShamt, \重定向流水线控制信号_1_readmode [9:7], \重定向流水线控制信号_1_aluop , \重定向流水线控制信号_1_readmode [2:0]}),
    .Din32_9(\锁存器1_1_dout32_3 ), .Din32_10(mips_fregifile_1_r1), .Din32_11(mips_fregifile_1_r2),
    .Din32_12(\译码逻辑输出信号_1_immediate ), .CLK(CLK), .Dout32_6(Syscall), .Dout32_7(\重定向锁存器2_1_dout32_7 ),
    .Dout32_8({\重定向锁存器2_1_dout32_8_2 , \重定向锁存器2_1_dout32_8 }), .Dout32_9(\重定向锁存器2_1_dout32_9 ),
    .Dout32_10(\重定向锁存器2_1_dout32_10 ), .Dout32_11(\重定向锁存器2_1_dout32_11 ), .Dout32_12(\重定向锁存器2_1_dout32_12 ),
    .\同步清零_气泡_高电平有效 (or_1_out), .Din32_2(ID_PC), .Dout32_2(EX_PC), .Din32(Select),
    .Dout32({\重定向锁存器2_1_dout32_2 , \重定向锁存器2_1_dout32 }));  // open: Din32_3, Din32_4, Din32_5, Dout32_3, Dout32_4, Dout32_5, 使能端_低电平有效_stall_高电平有效
  // Probe on M_PC[11:0]
  Multiplexer #(.select(2), .width(32), .enable("false")) multiplexer_1 (
    .in0(\重定向锁存器2_1_dout32_10 ), .in1(\重定向锁存器3_1_dout32_2 ), .in2(RDin), .in3(\重定向锁存器3_1_dout32_2 ),
    .out(multiplexer_1_out), .sel(\重定向锁存器2_1_dout32 ));
  Multiplexer #(.select(2), .width(32), .enable("false")) multiplexer_2 (
    .in0(\重定向锁存器2_1_dout32_11 ), .in1(\重定向锁存器3_1_dout32_2 ), .in2(RDin), .in3(\重定向锁存器3_1_dout32_2 ),
    .out(multiplexer_2_out), .sel(\重定向锁存器2_1_dout32_2 ));
  // Probe on WB_PC[11:0]
  Multiplexer #(.width(32), .enable("false")) multiplexer_3 (
    .in0(multiplexer_2_out), .in1(\重定向锁存器2_1_dout32_12 ), .out(multiplexer_3_out),
    .sel(\重定向锁存器2_1_dout32_8 [7]));
  \重定向选择信号  \u_重定向选择信号_1  (
    .ExRegWrite(\重定向锁存器2_1_dout32_8 [8]), .ExR(\重定向锁存器2_1_dout32_8_2 ), .IP(\锁存器1_1_dout32_4 ),
    .MemRegWrite(\重定向锁存器3_1_dout32_3 [3]), .MemR(\重定向锁存器3_1_dout32_3_2 ), .MemMemToReg(1'b0),
    .ExMemToReg(\重定向锁存器2_1_dout32_8 [1]), .R1Select(Select[1:0]), .R2Select(Select[3:2]), .\气泡 (\气泡 ));
  Comparator #(.width(32)) comparator_1 (.a(multiplexer_2_out), .b(32'h22), .eq(comparator_1_eq));  // open: gt, lt
  MIPS_ALU mips_alu_1 (
    .X(multiplexer_1_out), .Y(multiplexer_3_out), .AluOP(\重定向锁存器2_1_dout32_8 [6:3]),
    .Result(mips_alu_1_result), .shamt(\重定向锁存器2_1_dout32_8 [14:10]));  // open: Equal, Result_2
  and and_1 (and_1_out, Syscall, comparator_1_eq);
  and and_2 (and_2_out, Syscall, ~comparator_1_eq);  // AND_Gate
  \重定向锁存器3  \u_重定向锁存器3_1  (
    .Din32_2(multiplexer_4_out),
    .Din32_3({\重定向锁存器2_1_dout32_8_2 , \重定向锁存器2_1_dout32_8 [8], \重定向锁存器2_1_dout32_8 [2:0]}),
    .Din32_4(mips_alu_1_result), .Din32_5(multiplexer_2_out), .CLK(CLK), .Dout32_2(\重定向锁存器3_1_dout32_2 ),
    .Dout32_3({\重定向锁存器3_1_dout32_3_2 , \重定向锁存器3_1_dout32_3 [3], MemWrite, \重定向锁存器3_1_dout32_3 [1:0]}),
    .Dout32_4(\重定向锁存器3_1_dout32_4 ), .Dout32_5(MDin), .\使能端_低电平有效_stall_高电平有效 (1'b0), .Din32(EX_PC),
    .Dout32(M_PC));  // open: 传输状态In_表明当前传输数据有效, 传输状态Out_表明当前传输数据有效, 同步清零_气泡_高电平有效
  Multiplexer #(.width(32), .enable("false")) multiplexer_4 (
    .in0(mips_alu_1_result), .in1(\重定向锁存器2_1_dout32_9 ), .out(multiplexer_4_out),
    .sel(\重定向锁存器2_1_dout32_8 [9]));
  not not_4 (nStop, register_1_q);
  Register #(.width(1)) register_1 (.D(and_2_out), .en(nStop), .Q(register_1_q), .clk(CLK), .clr(or_2_out));
  or or_2 (or_2_out, Go, RST);
  Register #(.width(32)) register_2 (.D(multiplexer_1_out), .en(and_1_out), .Q(LedData), .clk(CLK), .clr(RST));
  \重定向锁存器4  \u_重定向锁存器4_1  (
    .Din32_2(\重定向锁存器3_1_dout32_2 ),
    .Din32_3({\重定向锁存器3_1_dout32_3_2 , \重定向锁存器3_1_dout32_3 [3], \重定向锁存器3_1_dout32_3 [1]}),
    .Din32_4(\四路存储器_1_memory ), .CLK(CLK), .Dout32_2(\重定向锁存器4_1_dout32_2 ),
    .Dout32_3({\重定向锁存器4_1_dout32_3 [6:2], RegWrite, \重定向锁存器4_1_dout32_3 [0]}),
    .Dout32_4(\重定向锁存器4_1_dout32_4 ), .\使能端_低电平有效_stall_高电平有效 (1'b0), .Din32(M_PC), .Dout32(WB_PC));  // open: 传输状态In_表明当前传输数据有效, 传输状态Out_表明当前传输数据有效, 同步清零_气泡_高电平有效
  \四路存储器  \u_四路存储器_1  (
    .CLK(CLK), .Address(\重定向锁存器3_1_dout32_4 ), .Memory(\四路存储器_1_memory ), .MemWrite(MemWrite),
    .Mode(\重定向锁存器3_1_dout32_3 [0]), .Data(MDin), .RST(RST));
  Multiplexer #(.width(32), .enable("false")) multiplexer_5 (
    .in0(\重定向锁存器4_1_dout32_2 ), .in1(\重定向锁存器4_1_dout32_4 ), .out(RDin), .sel(\重定向锁存器4_1_dout32_3 [0]));

  // Other names for the same wires on the sheet: MEM_PC[31:0] = M_PC

  // Notes on the sheet:
  //   中断源
  //   中断等待指示
  //   数码管输出
  //   contents of rom_1 (hex, n*v repeats v):
  //   20110001 8000c05 20110001 20120002 20130003 8000c09 20110001 20120002 20130003 8000c0d 20110001
  //   20120002 20130003 8000c11 20110001 20120002 20130003 c000cb8 20100001 20110001 118fc0 112020
  //   20020022 c 118882 12200001 8000c15 112020 20020022 c 20110001 118880 112020 20020022 c 12200001
  //   8000c1f 20110001 118fc0 112020 20020022 c 1188c3 112020 20020022 c 118903 112020 20020022 c 118903
  //   112020 20020022 c 118903 112020 20020022 c 118903 112020 20020022 c 118903 112020 20020022 c 118903
  //   112020 20020022 c 118903 112020 20020022 c 20100001 109fc0 139fc3 8021 2012000c 24160003 26100001
  //   3210000f 20080008 20090001 139900 2709825 132020 20020022 c 1094022 1500fff9 22100001 2018000f
  //   2188024 108700 20080008 20090001 139902 2709825 132021 20020022 c 1094022 1500fff9 108702 2c9b022
  //   12c00001 8000c50 4020 1084027 84400 3508ffff 82021 20020022 c 2010ffff 20110000 ae300000 22100001
  //   22310004 ae300000 22100001 22310004 ae300000 22100001 22310004 ae300000 22100001 22310004 ae300000
  //   22100001 22310004 ae300000 22100001 22310004 ae300000 22100001 22310004 ae300000 22100001 22310004
  //   ae300000 22100001 22310004 ae300000 22100001 22310004 ae300000 22100001 22310004 ae300000 22100001
  //   22310004 ae300000 22100001 22310004 ae300000 22100001 22310004 ae300000 22100001 22310004 ae300000
  //   22100001 22310004 22100001 8020 2011003c 8e130000 8e340000 274402a 11000002 ae330000 ae140000
  //   2231fffc 1611fff8 102020 20020022 c 22100004 2011003c 1611fff2 20020032 c 20100000 22100001 102020
  //   20020022 c 22100002 102020 20020022 c 22100003 102020 20020022 c 22100004 102020 20020022 c 22100005
  //   102020 20020022 c 22100006 102020 20020022 c 22100007 102020 20020022 c 22100008 102020 20020022
  //   20020022 c 3e00008
  //   流水调试日志用
  //   为方便自动评测，需要输出流水线各段保存的PC值，注意是PC不是PC+4，另外ID段寄存器写入信息，Mem段内存写入信息也要输出
endmodule

module \中断按键参考电路  (
  input  \同步清零信号 ,
  output \与中断屏蔽位与 
);

  wire \_1号中断_out , and_1_out, clock_1_out, d_ff_1_q, or_1_out, or_2_out;

  Clock clock_1 (.out(clock_1_out));
  Button \_1号中断  (.out(\_1号中断_out ));
  or or_1 (or_1_out, \与中断屏蔽位与 , d_ff_1_q);
  LED \_1号中断等待指示灯  (.in(or_1_out));
  D_Flip_Flop d_ff_1 (.clk(\_1号中断_out ), .D(1'b1), .Q(d_ff_1_q), .reset(\与中断屏蔽位与 ));  // open: Qn, preset, en
  or or_2 (or_2_out, d_ff_1_q, \与中断屏蔽位与 );
  and and_1 (and_1_out, or_2_out, ~\同步清零信号 );  // AND_Gate
  D_Flip_Flop IR1 (.clk(clock_1_out), .D(and_1_out), .Q(\与中断屏蔽位与 ));  // open: Qn, preset, en, reset

  // Notes on the sheet:
  //   中断信号采样参考电路
  //   Reset 
endmodule

module MIPS_FRegifile (
  input  [31:0] Din,
  input  Clk,
  input  WE,
  input  [4:0] R1_num,
  input  [4:0] W_num,
  input  [4:0] R2_num,
  output [31:0] R1,
  output [31:0] R2
);

  // RegisterFile registerfile_1: pin names not known; wires that end beside it: Din, Clk, WE, W_num, R1_num, R2_num, R1, R2
endmodule

module \锁存器1  (
  input  [31:0] Din32,
  input  Din32_2,
  input  [31:0] Din32_3,
  input  [31:0] Din32_4,
  input  \传输状态In_表明当前传输数据有效 ,
  input  CLK,
  input  \同步清零_气泡_高电平有效 ,
  input  \使能端_低电平有效_stall_高电平有效 ,
  output [31:0] Dout32,
  output Dout32_2,
  output [31:0] Dout32_3,
  output [31:0] Dout32_4,
  output \传输状态Out_表明当前传输数据有效 
);

  wire multiplexer_2_out, multiplexer_5_out, pull_resistor_2_node;
  wire [31:0] multiplexer_1_out, multiplexer_3_out, multiplexer_4_out;

  Multiplexer #(.width(32), .enable("false")) multiplexer_1 (
    .in0(Din32), .in1({32{1'b0}}), .out(multiplexer_1_out), .sel(\同步清零_气泡_高电平有效 ));
  Multiplexer #(.enable("false")) multiplexer_2 (
    .in0(Din32_2), .in1(1'b0), .out(multiplexer_2_out), .sel(\同步清零_气泡_高电平有效 ));
  Multiplexer #(.width(32), .enable("false")) multiplexer_3 (
    .in0(Din32_3), .in1({32{1'b0}}), .out(multiplexer_3_out), .sel(\同步清零_气泡_高电平有效 ));
  Multiplexer #(.width(32), .enable("false")) multiplexer_4 (
    .in0(Din32_4), .in1({32{1'b0}}), .out(multiplexer_4_out), .sel(\同步清零_气泡_高电平有效 ));
  Multiplexer #(.enable("false")) multiplexer_5 (
    .in0(\传输状态In_表明当前传输数据有效 ), .in1(1'b0), .out(multiplexer_5_out), .sel(\同步清零_气泡_高电平有效 ));
  Pull_Resistor pull_resistor_1 (.node(\同步清零_气泡_高电平有效 ));
  Pull_Resistor pull_resistor_2 (.node(pull_resistor_2_node));
  not not_1 (pull_resistor_2_node, \使能端_低电平有效_stall_高电平有效 );
  Register #(.width(32)) register_1 (
    .D(multiplexer_1_out), .en(pull_resistor_2_node), .Q(Dout32), .clk(CLK));  // open: clr
  Register #(.width(1)) register_2 (
    .D(multiplexer_2_out), .en(pull_resistor_2_node), .Q(Dout32_2), .clk(CLK));  // open: clr
  Register #(.width(32)) register_3 (
    .D(multiplexer_3_out), .en(pull_resistor_2_node), .Q(Dout32_3), .clk(CLK));  // open: clr
  Register #(.width(32)) register_4 (
    .D(multiplexer_4_out), .en(pull_resistor_2_node), .Q(Dout32_4), .clk(CLK));  // open: clr
  Register #(.width(1)) register_5 (
    .D(multiplexer_5_out), .en(pull_resistor_2_node), .Q(\传输状态Out_表明当前传输数据有效 ), .clk(CLK));  // open: clr
endmodule
module RUsed (
  input  ExRegWrite,
  input  [4:0] ExR,
  input  [31:0] IP,
  input  MemRegWrite,
  input  [4:0] MemR,
  output _1,
  output _2
);

  wire and_1_out, and_2_out, and_3_out, and_4_out, and_5_out, and_6_out, and_7_out, and_8_out, and_9_out,
       and_10_out, and_11_out, and_12_out, and_13_out, and_14_out, and_15_out, and_16_out, and_17_out,
       and_18_out, and_19_out, and_20_out, comparator_1_eq, comparator_2_eq, comparator_3_eq,
       comparator_4_eq, comparator_5_eq, comparator_6_eq, nor_1_out, nor_2_out, not_1_out, not_2_out,
       not_3_out, not_4_out, not_5_out, not_6_out, not_7_out, not_8_out, not_9_out, not_10_out, not_11_out,
       not_12_out, not_13_out, not_14_out, not_15_out, not_16_out, not_17_out, not_18_out, not_19_out,
       not_20_out, not_21_out, not_22_out, not_23_out, not_24_out, not_25_out, not_26_out, not_27_out,
       not_28_out, not_29_out, not_30_out, not_31_out, not_32_out, not_33_out, not_34_out, not_35_out,
       not_36_out, not_37_out, not_38_out, not_39_out, not_40_out, not_41_out, not_42_out, not_43_out,
       not_44_out, not_45_out, not_46_out, not_47_out, not_48_out, not_49_out, not_50_out, not_51_out,
       not_52_out, not_53_out, not_54_out, not_55_out, not_56_out, not_57_out, not_58_out, not_59_out,
       not_60_out, not_61_out, not_62_out, not_63_out, not_64_out, not_65_out, not_66_out, not_67_out,
       not_68_out, not_69_out, not_70_out, not_71_out, not_72_out, not_73_out, not_74_out, not_75_out,
       not_76_out, not_77_out, not_78_out, not_79_out, not_80_out, not_81_out, not_82_out, not_83_out,
       not_84_out, not_85_out, not_86_out, not_87_out, not_88_out, not_89_out;
  wire [9:0] multiplexer_1_out;

  not not_1 (not_1_out, IP[31]);
  not not_2 (not_2_out, IP[30]);
  not not_3 (not_3_out, IP[29]);
  not not_4 (not_4_out, IP[28]);
  not not_5 (not_5_out, IP[27]);
  not not_6 (not_6_out, IP[26]);
  not not_7 (not_7_out, IP[5]);
  not not_8 (not_8_out, IP[4]);
  not not_9 (not_9_out, IP[1]);
  not not_10 (not_10_out, IP[0]);
  not not_11 (not_11_out, IP[31]);
  not not_12 (not_12_out, IP[30]);
  not not_13 (not_13_out, IP[29]);
  not not_14 (not_14_out, IP[28]);
  not not_15 (not_15_out, IP[26]);
  not not_16 (not_16_out, IP[31]);
  not not_17 (not_17_out, IP[30]);
  not not_18 (not_18_out, IP[29]);
  not not_19 (not_19_out, IP[28]);
  not not_20 (not_20_out, IP[31]);
  not not_21 (not_21_out, IP[30]);
  not not_22 (not_22_out, IP[29]);
  not not_23 (not_23_out, IP[28]);
  not not_24 (not_24_out, IP[27]);
  not not_25 (not_25_out, IP[26]);
  not not_26 (not_26_out, IP[5]);
  not not_27 (not_27_out, IP[4]);
  not not_28 (not_28_out, IP[2]);
  not not_29 (not_29_out, IP[1]);
  not not_30 (not_30_out, IP[0]);
  not not_31 (not_31_out, IP[22]);
  and and_1 (and_1_out, not_11_out, not_12_out, not_13_out, not_14_out, IP[27], not_15_out);
  and and_2 (and_2_out, not_16_out, not_17_out, not_18_out, not_19_out, IP[27], IP[26]);
  not not_32 (not_32_out, IP[31]);
  not not_33 (not_33_out, IP[30]);
  not not_34 (not_34_out, IP[29]);
  not not_35 (not_35_out, IP[28]);
  not not_36 (not_36_out, IP[26]);
  not not_37 (not_37_out, IP[31]);
  not not_38 (not_38_out, IP[30]);
  not not_39 (not_39_out, IP[29]);
  not not_40 (not_40_out, IP[28]);
  not not_41 (not_41_out, IP[31]);
  not not_42 (not_42_out, IP[30]);
  not not_43 (not_43_out, IP[28]);
  not not_44 (not_44_out, IP[27]);
  not not_45 (not_45_out, IP[26]);
  not not_46 (not_46_out, IP[31]);
  not not_47 (not_47_out, IP[30]);
  not not_48 (not_48_out, IP[27]);
  not not_49 (not_49_out, IP[26]);
  not not_50 (not_50_out, IP[31]);
  not not_51 (not_51_out, IP[30]);
  not not_52 (not_52_out, IP[28]);
  not not_53 (not_53_out, IP[27]);
  not not_54 (not_54_out, IP[31]);
  not not_55 (not_55_out, IP[30]);
  not not_56 (not_56_out, IP[28]);
  not not_57 (not_57_out, IP[26]);
  not not_58 (not_58_out, IP[31]);
  not not_59 (not_59_out, IP[30]);
  not not_60 (not_60_out, IP[27]);
  not not_61 (not_61_out, IP[30]);
  not not_62 (not_62_out, IP[29]);
  not not_63 (not_63_out, IP[28]);
  not not_64 (not_64_out, IP[31]);
  not not_65 (not_65_out, IP[30]);
  not not_66 (not_66_out, IP[26]);
  not not_67 (not_67_out, IP[30]);
  not not_68 (not_68_out, IP[29]);
  not not_69 (not_69_out, IP[28]);
  not not_70 (not_70_out, IP[27]);
  not not_71 (not_71_out, IP[26]);
  not not_72 (not_72_out, IP[31]);
  not not_73 (not_73_out, IP[29]);
  not not_74 (not_74_out, IP[28]);
  not not_75 (not_75_out, IP[27]);
  not not_76 (not_76_out, IP[26]);
  not not_77 (not_77_out, IP[21]);
  not not_78 (not_78_out, IP[24]);
  not not_79 (not_79_out, IP[25]);
  not not_80 (not_80_out, IP[31]);
  not not_81 (not_81_out, IP[29]);
  not not_82 (not_82_out, IP[28]);
  not not_83 (not_83_out, IP[27]);
  not not_84 (not_84_out, IP[26]);
  not not_85 (not_85_out, IP[21]);
  not not_86 (not_86_out, IP[22]);
  not not_87 (not_87_out, IP[23]);
  not not_88 (not_88_out, IP[24]);
  not not_89 (not_89_out, IP[25]);
  and and_3 (and_3_out, not_1_out, not_2_out, not_3_out, not_4_out, not_5_out, not_6_out, not_7_out, not_8_out, IP[3], IP[2], not_9_out, not_10_out);
  nor nor_1 (nor_1_out, and_16_out, and_1_out, and_2_out, and_15_out);
  and and_4 (and_4_out, not_20_out, not_21_out, not_22_out, not_23_out, not_24_out, not_25_out, not_26_out, not_27_out, IP[3], not_28_out, not_29_out, not_30_out);
  and and_5 (and_5_out, not_32_out, not_33_out, not_34_out, not_35_out, IP[27], not_36_out);
  and and_6 (and_6_out, not_37_out, not_38_out, not_39_out, not_40_out, IP[27], IP[26]);
  and and_7 (and_7_out, not_41_out, not_42_out, IP[29], not_43_out, not_44_out, not_45_out);
  and and_8 (and_8_out, not_46_out, not_47_out, IP[29], IP[28], not_48_out, not_49_out);
  and and_9 (and_9_out, not_50_out, not_51_out, IP[29], not_52_out, not_53_out, IP[26]);
  and and_10 (and_10_out, not_54_out, not_55_out, IP[29], not_56_out, IP[27], not_57_out);
  and and_11 (and_11_out, not_58_out, not_59_out, IP[29], IP[28], not_60_out, IP[26]);
  and and_12 (and_12_out, IP[31], not_61_out, not_62_out, not_63_out, IP[27], IP[26]);
  and and_13 (and_13_out, not_64_out, not_65_out, IP[29], IP[28], IP[27], not_66_out);
  and and_14 (and_14_out, IP[31], not_67_out, not_68_out, not_69_out, not_70_out, not_71_out);
  and and_15 (and_15_out, not_72_out, IP[30], not_73_out, not_74_out, not_75_out, not_76_out, not_77_out, not_31_out, IP[23], not_78_out, not_79_out);
  and and_16 (and_16_out, not_80_out, IP[30], not_81_out, not_82_out, not_83_out, not_84_out, not_85_out, not_86_out, not_87_out, not_88_out, not_89_out);
  nor nor_2 (nor_2_out, and_4_out, and_5_out, and_6_out, and_7_out, and_8_out, and_9_out, and_10_out, and_11_out, and_12_out, and_13_out, and_14_out, and_16_out);
  Multiplexer #(.width(10), .enable("false")) multiplexer_1 (
    .in0({IP[20:16], IP[25:21]}), .in1(10'h44), .out(multiplexer_1_out), .sel(and_3_out));
  Comparator #(.width(5)) comparator_1 (.a(ExR), .b({5{1'b0}}), .eq(comparator_1_eq));  // open: gt, lt
  Comparator #(.width(5)) comparator_2 (.a(multiplexer_1_out[4:0]), .b(ExR), .eq(comparator_2_eq));  // open: gt, lt
  Comparator #(.width(5)) comparator_3 (.a(multiplexer_1_out[9:5]), .b(ExR), .eq(comparator_3_eq));  // open: gt, lt
  Comparator #(.width(5)) comparator_4 (.a(MemR), .b({5{1'b0}}), .eq(comparator_4_eq));  // open: gt, lt
  Comparator #(.width(5)) comparator_5 (.a(multiplexer_1_out[4:0]), .b(MemR), .eq(comparator_5_eq));  // open: gt, lt
  Comparator #(.width(5)) comparator_6 (.a(multiplexer_1_out[9:5]), .b(MemR), .eq(comparator_6_eq));  // open: gt, lt
  and and_17 (and_17_out, nor_1_out, ExRegWrite, comparator_2_eq, ~comparator_1_eq);  // AND_Gate
  and and_18 (and_18_out, nor_2_out, ExRegWrite, comparator_3_eq, ~comparator_1_eq);  // AND_Gate
  and and_19 (and_19_out, nor_1_out, MemRegWrite, comparator_5_eq, ~comparator_4_eq);  // AND_Gate
  and and_20 (and_20_out, MemRegWrite, nor_2_out, comparator_6_eq, ~comparator_4_eq);  // AND_Gate
  or or_1 (_1, and_17_out, and_18_out);
  or or_2 (_2, and_19_out, and_20_out);
endmodule

module \四路存储器  (
  input  MemWrite,
  input  CLK,
  input  Mode,
  input  [31:0] Address,
  input  RST,
  input  [31:0] Data,
  output [31:0] Memory
);

  wire [7:0] multiplexer_1_out, ram_1_data, ram_2_data, ram_3_data, ram_4_data;
  wire [31:0] bit_extender_1_out;

  RAM #(.addrWidth(10), .bus("separate")) ram_1 (
    .addr(Address[11:2]), .din(Data[7:0]), .data(ram_1_data), .str(MemWrite), .clk(CLK), .clr(RST));  // open: sel, ld
  RAM #(.addrWidth(10), .bus("separate")) ram_2 (
    .addr(Address[11:2]), .din(Data[15:8]), .data(ram_2_data), .str(MemWrite), .clk(CLK), .clr(RST));  // open: sel, ld
  RAM #(.addrWidth(10), .bus("separate")) ram_3 (
    .addr(Address[11:2]), .din(Data[23:16]), .data(ram_3_data), .str(MemWrite), .clk(CLK), .clr(RST));  // open: sel, ld
  RAM #(.addrWidth(10), .bus("separate")) ram_4 (
    .addr(Address[11:2]), .din(Data[31:24]), .data(ram_4_data), .str(MemWrite), .clk(CLK), .clr(RST));  // open: sel, ld
  assign bit_extender_1_out = {{24{multiplexer_1_out[7]}}, multiplexer_1_out};  // Bit_Extender bit_extender_1
  Multiplexer #(.select(2), .width(8), .enable("false")) multiplexer_1 (
    .in0(ram_1_data), .in1(ram_2_data), .in2(ram_3_data), .in3(ram_4_data), .out(multiplexer_1_out),
    .sel(Address[1:0]));
  Multiplexer #(.width(32), .enable("false")) multiplexer_2 (
    .in0({ram_4_data, ram_3_data, ram_2_data, ram_1_data}), .in1(bit_extender_1_out), .out(Memory), .sel(Mode));
endmodule

module \重定向流水线控制信号  (
  input  in_1,
  input  [31:0] in_2,
  output MemToReg,
  output ReadMode,
  output MemWrite,
  output MFC0,
  output MTC0,
  output [3:0] AluOP,
  output ERET,
  output ALU_SRC,
  output RegWrite,
  output SysCALL,
  output JAL
);

  wire and_1_out, and_2_out, and_3_out, and_4_out, and_5_out, and_6_out, and_7_out, and_8_out, and_9_out,
       and_10_out, and_11_out, and_12_out, and_13_out, and_14_out, and_15_out, and_16_out, and_17_out,
       and_18_out, and_19_out, and_20_out, and_21_out, and_22_out, and_23_out, and_24_out, and_25_out,
       and_26_out, and_27_out, and_28_out, and_29_out, and_30_out, and_31_out, and_32_out, and_33_out,
       and_34_out, and_35_out, and_42_out, and_43_out, and_44_out, and_45_out, and_49_out, not_1_out,
       not_2_out, not_3_out, not_4_out, not_5_out, not_6_out, not_7_out, not_8_out, not_9_out, not_10_out,
       not_11_out, not_12_out, not_13_out, not_14_out, not_15_out, not_16_out, not_17_out, not_18_out,
       not_19_out, not_20_out, not_21_out, not_22_out, not_23_out, not_24_out, not_25_out, not_26_out,
       not_27_out, not_28_out, not_29_out, not_30_out, not_31_out, not_32_out, not_33_out, not_34_out,
       not_35_out, not_36_out, not_37_out, not_38_out, not_39_out, not_40_out, not_41_out, not_42_out,
       not_43_out, not_44_out, not_45_out, not_46_out, not_47_out, not_48_out, not_49_out, not_50_out,
       not_51_out, not_52_out, not_53_out, not_54_out, not_55_out, not_56_out, not_57_out, not_58_out,
       not_59_out, not_60_out, not_61_out, not_62_out, not_63_out, not_64_out, not_65_out, not_66_out,
       not_67_out, not_68_out, not_69_out, not_70_out, not_71_out, not_72_out, not_73_out, not_74_out,
       not_75_out, not_76_out, not_77_out, not_78_out, not_79_out, not_80_out, not_81_out, not_82_out,
       not_83_out, not_84_out, not_85_out, not_86_out, not_87_out, not_88_out, not_89_out, not_90_out,
       not_91_out, not_92_out, not_93_out, not_94_out, not_95_out, not_96_out, not_97_out, not_98_out,
       not_99_out, not_100_out, not_101_out, not_102_out, not_103_out, not_104_out, not_105_out, not_106_out,
       not_107_out, not_108_out, not_109_out, not_110_out, not_111_out, not_112_out, not_113_out,
       not_114_out, not_115_out, not_116_out, not_117_out, not_118_out, not_119_out, not_120_out,
       not_121_out, not_122_out, not_123_out, not_124_out, not_125_out, not_126_out, not_127_out,
       not_128_out, not_129_out, not_130_out, not_131_out, not_132_out, not_133_out, not_134_out,
       not_135_out, not_136_out, not_137_out, not_138_out, not_139_out, not_140_out, not_141_out,
       not_142_out, not_143_out, not_144_out, not_145_out, not_146_out, not_147_out, not_148_out,
       not_149_out, not_150_out, not_151_out, not_152_out, not_153_out, not_154_out, not_155_out,
       not_156_out, not_157_out, not_158_out, not_159_out, not_160_out, not_161_out, not_162_out,
       not_163_out, not_164_out, not_165_out, not_166_out, not_167_out, not_168_out, not_169_out,
       not_170_out, not_171_out, not_172_out, not_173_out, not_174_out, not_175_out, not_176_out,
       not_177_out, not_178_out, not_179_out, not_180_out, not_181_out, not_182_out, not_183_out,
       not_184_out, not_185_out, not_186_out, not_187_out, not_188_out, not_189_out, not_190_out,
       not_191_out, not_192_out, not_193_out, not_194_out, not_195_out, not_196_out, not_197_out,
       not_198_out, not_199_out, not_200_out, not_201_out, not_202_out, not_203_out, not_204_out,
       not_205_out, not_206_out, not_207_out, not_208_out, not_209_out, not_210_out, not_211_out,
       not_212_out, not_213_out, not_214_out, not_215_out, or_1_out, or_2_out, or_3_out;

  \运算控制器自动生成  \u_运算控制器自动生成_1  (
    .OP0(in_2[26]), .OP1(in_2[27]), .OP2(in_2[28]), .OP3(in_2[29]), .OP4(in_2[30]), .OP5(in_2[31]),
    .F0(in_2[0]), .F1(in_2[1]), .F2(in_2[2]), .F3(in_2[3]), .F4(in_2[4]), .F5(in_2[5]), .S0(AluOP[0]),
    .S1(AluOP[1]), .S2(AluOP[2]), .S3(AluOP[3]));
  not not_1 (not_1_out, in_2[30]);
  not not_2 (not_2_out, in_2[29]);
  not not_3 (not_3_out, in_2[28]);
  not not_4 (not_4_out, in_2[30]);
  not not_5 (not_5_out, in_2[29]);
  not not_6 (not_6_out, in_2[28]);
  not not_7 (not_7_out, in_2[27]);
  not not_8 (not_8_out, in_2[26]);
  not not_9 (not_9_out, in_2[30]);
  not not_10 (not_10_out, in_2[28]);
  not not_11 (not_11_out, in_2[31]);
  not not_12 (not_12_out, in_2[30]);
  not not_13 (not_13_out, in_2[28]);
  not not_14 (not_14_out, in_2[27]);
  not not_15 (not_15_out, in_2[26]);
  not not_16 (not_16_out, in_2[31]);
  not not_17 (not_17_out, in_2[30]);
  not not_18 (not_18_out, in_2[27]);
  not not_19 (not_19_out, in_2[26]);
  not not_20 (not_20_out, in_2[31]);
  not not_21 (not_21_out, in_2[30]);
  not not_22 (not_22_out, in_2[28]);
  not not_23 (not_23_out, in_2[27]);
  not not_24 (not_24_out, in_2[31]);
  not not_25 (not_25_out, in_2[30]);
  not not_26 (not_26_out, in_2[28]);
  not not_27 (not_27_out, in_2[26]);
  not not_28 (not_28_out, in_2[31]);
  not not_29 (not_29_out, in_2[30]);
  not not_30 (not_30_out, in_2[27]);
  not not_31 (not_31_out, in_2[30]);
  not not_32 (not_32_out, in_2[29]);
  not not_33 (not_33_out, in_2[28]);
  not not_34 (not_34_out, in_2[30]);
  not not_35 (not_35_out, in_2[28]);
  not not_36 (not_36_out, in_2[31]);
  not not_37 (not_37_out, in_2[30]);
  not not_38 (not_38_out, in_2[26]);
  not not_39 (not_39_out, in_2[30]);
  not not_40 (not_40_out, in_2[29]);
  not not_41 (not_41_out, in_2[28]);
  not not_42 (not_42_out, in_2[27]);
  not not_43 (not_43_out, in_2[26]);
  not not_44 (not_44_out, in_2[31]);
  not not_45 (not_45_out, in_2[30]);
  not not_46 (not_46_out, in_2[29]);
  not not_47 (not_47_out, in_2[28]);
  not not_48 (not_48_out, in_2[27]);
  not not_49 (not_49_out, in_2[26]);
  not not_50 (not_50_out, in_2[5]);
  not not_51 (not_51_out, in_2[4]);
  not not_52 (not_52_out, in_2[3]);
  not not_53 (not_53_out, in_2[2]);
  not not_54 (not_54_out, in_2[1]);
  not not_55 (not_55_out, in_2[0]);
  not not_56 (not_56_out, in_2[31]);
  not not_57 (not_57_out, in_2[30]);
  not not_58 (not_58_out, in_2[29]);
  not not_59 (not_59_out, in_2[28]);
  not not_60 (not_60_out, in_2[27]);
  not not_61 (not_61_out, in_2[26]);
  not not_62 (not_62_out, in_2[5]);
  not not_63 (not_63_out, in_2[4]);
  not not_64 (not_64_out, in_2[3]);
  not not_65 (not_65_out, in_2[2]);
  not not_66 (not_66_out, in_2[31]);
  not not_67 (not_67_out, in_2[30]);
  not not_68 (not_68_out, in_2[29]);
  not not_69 (not_69_out, in_2[28]);
  not not_70 (not_70_out, in_2[27]);
  not not_71 (not_71_out, in_2[26]);
  not not_72 (not_72_out, in_2[5]);
  not not_73 (not_73_out, in_2[4]);
  not not_74 (not_74_out, in_2[3]);
  not not_75 (not_75_out, in_2[2]);
  not not_76 (not_76_out, in_2[0]);
  not not_77 (not_77_out, in_2[31]);
  not not_78 (not_78_out, in_2[30]);
  not not_79 (not_79_out, in_2[29]);
  not not_80 (not_80_out, in_2[28]);
  not not_81 (not_81_out, in_2[27]);
  not not_82 (not_82_out, in_2[26]);
  not not_83 (not_83_out, in_2[4]);
  not not_84 (not_84_out, in_2[3]);
  not not_85 (not_85_out, in_2[2]);
  not not_86 (not_86_out, in_2[1]);
  not not_87 (not_87_out, in_2[0]);
  not not_88 (not_88_out, in_2[31]);
  not not_89 (not_89_out, in_2[30]);
  not not_90 (not_90_out, in_2[29]);
  not not_91 (not_91_out, in_2[28]);
  not not_92 (not_92_out, in_2[27]);
  not not_93 (not_93_out, in_2[26]);
  not not_94 (not_94_out, in_2[4]);
  not not_95 (not_95_out, in_2[3]);
  not not_96 (not_96_out, in_2[2]);
  not not_97 (not_97_out, in_2[1]);
  not not_98 (not_98_out, in_2[31]);
  not not_99 (not_99_out, in_2[30]);
  not not_100 (not_100_out, in_2[29]);
  not not_101 (not_101_out, in_2[28]);
  not not_102 (not_102_out, in_2[27]);
  not not_103 (not_103_out, in_2[26]);
  not not_104 (not_104_out, in_2[4]);
  not not_105 (not_105_out, in_2[3]);
  not not_106 (not_106_out, in_2[2]);
  not not_107 (not_107_out, in_2[0]);
  not not_108 (not_108_out, in_2[31]);
  not not_109 (not_109_out, in_2[30]);
  not not_110 (not_110_out, in_2[29]);
  not not_111 (not_111_out, in_2[28]);
  not not_112 (not_112_out, in_2[27]);
  not not_113 (not_113_out, in_2[26]);
  not not_114 (not_114_out, in_2[4]);
  not not_115 (not_115_out, in_2[3]);
  not not_116 (not_116_out, in_2[1]);
  not not_117 (not_117_out, in_2[0]);
  not not_118 (not_118_out, in_2[31]);
  not not_119 (not_119_out, in_2[30]);
  not not_120 (not_120_out, in_2[29]);
  not not_121 (not_121_out, in_2[28]);
  not not_122 (not_122_out, in_2[27]);
  not not_123 (not_123_out, in_2[26]);
  not not_124 (not_124_out, in_2[4]);
  not not_125 (not_125_out, in_2[3]);
  not not_126 (not_126_out, in_2[1]);
  not not_127 (not_127_out, in_2[31]);
  not not_128 (not_128_out, in_2[30]);
  not not_129 (not_129_out, in_2[29]);
  not not_130 (not_130_out, in_2[28]);
  not not_131 (not_131_out, in_2[27]);
  not not_132 (not_132_out, in_2[26]);
  not not_133 (not_133_out, in_2[4]);
  not not_134 (not_134_out, in_2[3]);
  not not_135 (not_135_out, in_2[31]);
  not not_136 (not_136_out, in_2[30]);
  not not_137 (not_137_out, in_2[29]);
  not not_138 (not_138_out, in_2[28]);
  not not_139 (not_139_out, in_2[27]);
  not not_140 (not_140_out, in_2[26]);
  not not_141 (not_141_out, in_2[4]);
  not not_142 (not_142_out, in_2[2]);
  not not_143 (not_143_out, in_2[0]);
  not not_144 (not_144_out, in_2[31]);
  not not_145 (not_145_out, in_2[30]);
  not not_146 (not_146_out, in_2[29]);
  not not_147 (not_147_out, in_2[28]);
  not not_148 (not_148_out, in_2[27]);
  not not_149 (not_149_out, in_2[26]);
  not not_150 (not_150_out, in_2[4]);
  not not_151 (not_151_out, in_2[2]);
  not not_152 (not_152_out, in_2[31]);
  not not_153 (not_153_out, in_2[30]);
  not not_154 (not_154_out, in_2[29]);
  not not_155 (not_155_out, in_2[28]);
  not not_156 (not_156_out, in_2[31]);
  not not_157 (not_157_out, in_2[30]);
  not not_158 (not_158_out, in_2[28]);
  not not_159 (not_159_out, in_2[27]);
  not not_160 (not_160_out, in_2[26]);
  not not_161 (not_161_out, in_2[31]);
  not not_162 (not_162_out, in_2[30]);
  not not_163 (not_163_out, in_2[27]);
  not not_164 (not_164_out, in_2[26]);
  not not_165 (not_165_out, in_2[31]);
  not not_166 (not_166_out, in_2[30]);
  not not_167 (not_167_out, in_2[28]);
  not not_168 (not_168_out, in_2[27]);
  not not_169 (not_169_out, in_2[31]);
  not not_170 (not_170_out, in_2[30]);
  not not_171 (not_171_out, in_2[28]);
  not not_172 (not_172_out, in_2[26]);
  not not_173 (not_173_out, in_2[31]);
  not not_174 (not_174_out, in_2[30]);
  not not_175 (not_175_out, in_2[27]);
  not not_176 (not_176_out, in_2[30]);
  not not_177 (not_177_out, in_2[29]);
  not not_178 (not_178_out, in_2[28]);
  not not_179 (not_179_out, in_2[31]);
  not not_180 (not_180_out, in_2[30]);
  not not_181 (not_181_out, in_2[29]);
  not not_182 (not_182_out, in_2[28]);
  not not_183 (not_183_out, in_2[27]);
  not not_184 (not_184_out, in_2[26]);
  not not_185 (not_185_out, in_2[4]);
  not not_186 (not_186_out, in_2[3]);
  not not_187 (not_187_out, in_2[2]);
  not not_188 (not_188_out, in_2[31]);
  not not_189 (not_189_out, in_2[30]);
  not not_190 (not_190_out, in_2[26]);
  not not_191 (not_191_out, in_2[30]);
  not not_192 (not_192_out, in_2[29]);
  not not_193 (not_193_out, in_2[28]);
  not not_194 (not_194_out, in_2[27]);
  not not_195 (not_195_out, in_2[26]);
  not not_196 (not_196_out, in_2[31]);
  not not_197 (not_197_out, in_2[30]);
  not not_198 (not_198_out, in_2[29]);
  not not_199 (not_199_out, in_2[28]);
  not not_200 (not_200_out, in_2[27]);
  not not_201 (not_201_out, in_2[26]);
  not not_202 (not_202_out, in_2[5]);
  not not_203 (not_203_out, in_2[4]);
  not not_204 (not_204_out, in_2[1]);
  not not_205 (not_205_out, in_2[0]);
  not not_206 (not_206_out, in_2[31]);
  not not_207 (not_207_out, in_2[30]);
  not not_208 (not_208_out, in_2[29]);
  not not_209 (not_209_out, in_2[28]);
  and and_1 (and_1_out, in_2[31], not_1_out, not_2_out, not_3_out, in_2[27], in_2[26]);
  and and_2 (and_2_out, in_2[31], not_4_out, not_5_out, not_6_out, not_7_out, not_8_out);
  and and_3 (and_3_out, in_2[31], not_9_out, in_2[29], not_10_out, in_2[27], in_2[26]);
  and and_4 (and_4_out, not_11_out, not_12_out, in_2[29], not_13_out, not_14_out, not_15_out);
  and and_5 (and_5_out, not_16_out, not_17_out, in_2[29], in_2[28], not_18_out, not_19_out);
  and and_6 (and_6_out, not_20_out, not_21_out, in_2[29], not_22_out, not_23_out, in_2[26]);
  and and_7 (and_7_out, not_24_out, not_25_out, in_2[29], not_26_out, in_2[27], not_27_out);
  and and_8 (and_8_out, not_28_out, not_29_out, in_2[29], in_2[28], not_30_out, in_2[26]);
  and and_9 (and_9_out, in_2[31], not_31_out, not_32_out, not_33_out, in_2[27], in_2[26]);
  and and_10 (and_10_out, in_2[31], not_34_out, in_2[29], not_35_out, in_2[27], in_2[26]);
  and and_11 (and_11_out, not_36_out, not_37_out, in_2[29], in_2[28], in_2[27], not_38_out);
  and and_12 (and_12_out, in_2[31], not_39_out, not_40_out, not_41_out, not_42_out, not_43_out);
  and and_13 (and_13_out, not_44_out, not_45_out, not_46_out, not_47_out, not_48_out, not_49_out, not_50_out, not_51_out, not_52_out, not_53_out, not_54_out, not_55_out);
  and and_14 (and_14_out, not_56_out, not_57_out, not_58_out, not_59_out, not_60_out, not_61_out, not_62_out, not_63_out, not_64_out, not_65_out, in_2[1], in_2[0]);
  and and_15 (and_15_out, not_66_out, not_67_out, not_68_out, not_69_out, not_70_out, not_71_out, not_72_out, not_73_out, not_74_out, not_75_out, in_2[1], not_76_out);
  and and_16 (and_16_out, not_77_out, not_78_out, not_79_out, not_80_out, not_81_out, not_82_out, in_2[5], not_83_out, not_84_out, not_85_out, not_86_out, not_87_out);
  and and_17 (and_17_out, not_88_out, not_89_out, not_90_out, not_91_out, not_92_out, not_93_out, in_2[5], not_94_out, not_95_out, not_96_out, not_97_out, in_2[0]);
  and and_18 (and_18_out, not_98_out, not_99_out, not_100_out, not_101_out, not_102_out, not_103_out, in_2[5], not_104_out, not_105_out, not_106_out, in_2[1], not_107_out);
  and and_19 (and_19_out, not_108_out, not_109_out, not_110_out, not_111_out, not_112_out, not_113_out, in_2[5], not_114_out, not_115_out, in_2[2], not_116_out, not_117_out);
  and and_20 (and_20_out, not_118_out, not_119_out, not_120_out, not_121_out, not_122_out, not_123_out, in_2[5], not_124_out, not_125_out, in_2[2], not_126_out, in_2[0]);
  and and_21 (and_21_out, not_127_out, not_128_out, not_129_out, not_130_out, not_131_out, not_132_out, in_2[5], not_133_out, not_134_out, in_2[2], in_2[1], in_2[0]);
  and and_22 (and_22_out, not_135_out, not_136_out, not_137_out, not_138_out, not_139_out, not_140_out, in_2[5], not_141_out, in_2[3], not_142_out, in_2[1], not_143_out);
  and and_23 (and_23_out, not_144_out, not_145_out, not_146_out, not_147_out, not_148_out, not_149_out, in_2[5], not_150_out, in_2[3], not_151_out, in_2[1], in_2[0]);
  and and_24 (and_24_out, not_152_out, not_153_out, not_154_out, not_155_out, in_2[27], in_2[26]);
  and and_25 (and_25_out, not_156_out, not_157_out, in_2[29], not_158_out, not_159_out, not_160_out);
  and and_26 (and_26_out, not_161_out, not_162_out, in_2[29], in_2[28], not_163_out, not_164_out);
  and and_27 (and_27_out, not_165_out, not_166_out, in_2[29], not_167_out, not_168_out, in_2[26]);
  and and_28 (and_28_out, not_169_out, not_170_out, in_2[29], not_171_out, in_2[27], not_172_out);
  and and_29 (and_29_out, not_173_out, not_174_out, in_2[29], in_2[28], not_175_out, in_2[26]);
  and and_30 (and_30_out, in_2[31], not_176_out, not_177_out, not_178_out, in_2[27], in_2[26]);
  and and_31 (and_31_out, not_179_out, not_180_out, not_181_out, not_182_out, not_183_out, not_184_out, in_2[5], not_185_out, not_186_out, not_187_out, in_2[1], in_2[0]);
  and and_32 (and_32_out, not_188_out, not_189_out, in_2[29], in_2[28], in_2[27], not_190_out);
  and and_33 (and_33_out, in_2[31], not_191_out, not_192_out, not_193_out, not_194_out, not_195_out);
  and and_34 (and_34_out, not_196_out, not_197_out, not_198_out, not_199_out, not_200_out, not_201_out, not_202_out, not_203_out, in_2[3], in_2[2], not_204_out, not_205_out);
  and and_35 (and_35_out, not_206_out, not_207_out, not_208_out, not_209_out, in_2[27], in_2[26]);
  not not_210 (not_210_out, in_1);
  or or_1 (or_1_out, and_1_out, and_2_out);
  or or_2 (or_2_out, and_4_out, and_5_out, and_6_out, and_7_out, and_8_out, and_9_out, and_10_out, and_11_out, and_12_out);
  and and_36 (MemToReg, or_1_out, not_210_out);
  and and_37 (MemWrite, and_3_out, not_210_out);
  and and_38 (ALU_SRC, or_2_out, not_210_out);
  or or_3 (or_3_out, and_13_out, and_14_out, and_15_out, and_16_out, and_17_out, and_18_out, and_19_out, and_20_out, and_21_out, and_22_out, and_23_out, and_24_out, and_25_out, and_26_out, and_27_out, and_28_out, and_29_out, and_30_out, and_31_out, and_32_out, and_33_out, MFC0);
  and and_39 (RegWrite, or_3_out, not_210_out);
  and and_40 (SysCALL, and_34_out, not_210_out);
  and and_41 (JAL, and_35_out, not_210_out);
  and and_42 (and_42_out, ~in_2[26], ~in_2[27], ~in_2[28], ~in_2[29], in_2[30], ~in_2[31]);  // AND_Gate
  and and_43 (and_43_out, ~in_2[0], ~in_2[1], ~in_2[2], in_2[3], in_2[4], ~in_2[5]);  // AND_Gate
  and and_44 (and_44_out, ~in_2[21], ~in_2[22], ~in_2[23], ~in_2[24], ~in_2[25]);  // AND_Gate
  and and_45 (and_45_out, ~in_2[21], ~in_2[22], in_2[23], ~in_2[24], ~in_2[25]);  // AND_Gate
  not not_211 (not_211_out, in_2[30]);
  not not_212 (not_212_out, in_2[29]);
  not not_213 (not_213_out, in_2[28]);
  not not_214 (not_214_out, in_2[27]);
  not not_215 (not_215_out, in_2[26]);
  and and_46 (MFC0, and_42_out, and_44_out);
  and and_47 (MTC0, and_42_out, and_45_out);
  and and_48 (ERET, and_42_out, and_43_out);
  and and_49 (and_49_out, in_2[31], not_211_out, not_212_out, not_213_out, not_214_out, not_215_out);
  and and_50 (ReadMode, and_49_out, not_210_out);

  // Other names for the same wires on the sheet: F0 = in_2[0]; F1 = in_2[1]; F2 = in_2[2]; F3 = in_2[3]; F4 = in_2[4];
  //   F5 = in_2[5]; OP0 = in_2[26]; OP1 = in_2[27]; OP2 = in_2[28]; OP3 = in_2[29]; OP4 = in_2[30]; OP5 = in_2[31]
endmodule

module \重定向流水线跳转逻辑  (
  input  [31:0] IP,
  input  [31:0] R1,
  input  [31:0] R2,
  input  [31:0] PC_4,
  input  [31:0] PC_8,
  output [31:0] NextPC,
  output Normal,
  output [31:0] JumpAddress,
  output JalJumpBranch
);

  wire and_1_out, and_2_out, and_3_out, and_4_out, and_5_out, and_6_out, and_7_out, and_8_out, and_9_out,
       comparator_1_eq, comparator_1_lt, not_1_out, not_2_out, not_3_out, not_4_out, not_5_out, not_6_out,
       not_7_out, not_8_out, not_9_out, not_10_out, not_11_out, not_12_out, not_13_out, not_14_out,
       not_15_out, not_16_out, not_17_out, not_18_out, not_19_out, not_20_out, not_21_out, not_22_out,
       not_23_out, not_24_out, not_25_out, not_26_out, not_27_out, not_28_out, not_29_out, not_30_out,
       not_31_out, not_32_out, not_33_out, or_1_out, or_2_out, or_3_out;
  wire [27:0] shifter_2_out_2;
  wire [31:0] adder_1_out, bit_extender_1_out, bit_extender_2_out, shifter_1_out;
  wire [31:28] shifter_2_out;

  not not_1 (not_1_out, IP[31]);
  not not_2 (not_2_out, IP[30]);
  not not_3 (not_3_out, IP[29]);
  not not_4 (not_4_out, IP[27]);
  not not_5 (not_5_out, IP[26]);
  not not_6 (not_6_out, IP[31]);
  not not_7 (not_7_out, IP[30]);
  not not_8 (not_8_out, IP[29]);
  not not_9 (not_9_out, IP[27]);
  not not_10 (not_10_out, IP[31]);
  not not_11 (not_11_out, IP[30]);
  not not_12 (not_12_out, IP[29]);
  not not_13 (not_13_out, IP[28]);
  not not_14 (not_14_out, IP[27]);
  not not_15 (not_15_out, IP[26]);
  not not_16 (not_16_out, IP[5]);
  not not_17 (not_17_out, IP[4]);
  not not_18 (not_18_out, IP[2]);
  not not_19 (not_19_out, IP[1]);
  not not_20 (not_20_out, IP[0]);
  not not_21 (not_21_out, IP[31]);
  not not_22 (not_22_out, IP[30]);
  not not_23 (not_23_out, IP[29]);
  not not_24 (not_24_out, IP[28]);
  not not_25 (not_25_out, IP[26]);
  not not_26 (not_26_out, IP[31]);
  not not_27 (not_27_out, IP[30]);
  not not_28 (not_28_out, IP[29]);
  not not_29 (not_29_out, IP[28]);
  and and_1 (and_1_out, not_1_out, not_2_out, not_3_out, IP[28], not_4_out, not_5_out);
  and and_2 (and_2_out, not_6_out, not_7_out, not_8_out, IP[28], not_9_out, IP[26]);
  and and_3 (and_3_out, not_10_out, not_11_out, not_12_out, not_13_out, not_14_out, not_15_out, not_16_out, not_17_out, IP[3], not_18_out, not_19_out, not_20_out);
  and and_4 (and_4_out, not_21_out, not_22_out, not_23_out, not_24_out, IP[27], not_25_out);
  and and_5 (and_5_out, not_26_out, not_27_out, not_28_out, not_29_out, IP[27], IP[26]);
  Comparator #(.width(32)) comparator_1 (.a(R1), .b(R2), .eq(comparator_1_eq), .lt(comparator_1_lt));  // open: gt
  assign bit_extender_1_out = {{16{IP[15]}}, IP[15:0]};  // Bit_Extender bit_extender_1
  Shifter #(.width(32)) shifter_1 (.in(bit_extender_1_out), .\dist (5'b00010), .out(shifter_1_out));
  assign JumpAddress = and_3_out ? R1 : 32'bz;  // Controlled_Buffer controlled_buffer_1
  assign bit_extender_2_out = {{6{IP[25]}}, IP[25:0]};  // Bit_Extender bit_extender_2
  Adder #(.width(32)) adder_1 (.a(PC_4), .b(shifter_1_out), .out(adder_1_out));  // open: cin, cout
  assign NextPC = and_3_out ? R1 : 32'bz;  // Controlled_Buffer controlled_buffer_2
  Shifter #(.width(32)) shifter_2 (.in(bit_extender_2_out), .\dist (5'b00010), .out({shifter_2_out, shifter_2_out_2}));
  or or_1 (or_1_out, and_4_out, and_5_out);
  not not_30 (not_30_out, IP[31]);
  not not_31 (not_31_out, IP[30]);
  not not_32 (not_32_out, IP[29]);
  not not_33 (not_33_out, IP[26]);
  and and_6 (and_6_out, not_30_out, not_31_out, not_32_out, IP[28], IP[27], not_33_out);
  or or_2 (or_2_out, comparator_1_lt, comparator_1_eq);
  and and_7 (and_7_out, or_2_out, and_6_out);
  and and_8 (and_8_out, comparator_1_eq, and_1_out);
  and and_9 (and_9_out, ~comparator_1_eq, and_2_out);  // AND_Gate
  assign JumpAddress = or_3_out ? adder_1_out : 32'bz;  // Controlled_Buffer controlled_buffer_3
  nor nor_1 (Normal, or_3_out, and_4_out, and_5_out, and_3_out);
  // NOR_Gate nor_2 has open pins: in0=or_3_out, in1=and_4_out, in2=and_5_out, out=open
  assign JumpAddress = or_1_out ? {PC_4[31:28], shifter_2_out_2} : 32'bz;  // Controlled_Buffer controlled_buffer_4
  assign NextPC = or_1_out ? {PC_4[31:28], shifter_2_out_2} : 32'bz;  // Controlled_Buffer controlled_buffer_5
  or or_3 (or_3_out, and_7_out, and_8_out, and_9_out);
  assign NextPC = or_3_out ? adder_1_out : 32'bz;  // Controlled_Buffer controlled_buffer_6
  assign NextPC = Normal ? PC_8 : 32'bz;  // Controlled_Buffer controlled_buffer_7
  or or_4 (JalJumpBranch, or_3_out, or_1_out);
endmodule

module \译码逻辑输出信号  (
  input  [31:0] in_1,
  output [4:0] R1,
  output [4:0] R2,
  output [4:0] W_num,
  output [31:0] Immediate,
  output [4:0] shamt
);

  wire and_1_out, and_2_out, and_3_out, and_7_out, and_8_out, and_9_out, and_10_out, and_11_out, and_12_out,
       and_13_out, and_14_out, and_15_out, and_16_out, and_17_out, and_18_out, and_19_out, and_20_out,
       and_21_out, and_22_out, and_23_out, and_24_out, and_25_out, and_26_out, and_27_out, JAL, MFC0, MTC0,
       not_1_out, not_2_out, not_3_out, not_4_out, not_5_out, not_6_out, not_7_out, not_8_out, not_9_out,
       not_10_out, not_11_out, not_12_out, not_13_out, not_14_out, not_15_out, not_16_out, not_17_out,
       not_18_out, not_19_out, not_20_out, not_21_out, not_22_out, not_23_out, not_24_out, not_25_out,
       not_26_out, not_27_out, not_28_out, not_29_out, not_30_out, not_31_out, not_32_out, not_33_out,
       not_34_out, not_35_out, not_36_out, not_37_out, not_38_out, not_39_out, not_40_out, not_41_out,
       not_42_out, not_43_out, not_44_out, not_45_out, not_46_out, not_47_out, not_48_out, not_49_out,
       not_50_out, not_51_out, not_52_out, not_53_out, not_54_out, not_55_out, not_56_out, not_57_out,
       not_58_out, not_59_out, not_60_out, not_61_out, not_62_out, not_63_out, not_64_out, not_65_out,
       not_66_out, not_67_out, not_68_out, not_69_out, not_70_out, not_71_out, not_72_out, not_73_out,
       not_74_out, not_75_out, not_76_out, not_77_out, not_78_out, not_79_out, not_80_out, not_81_out,
       not_82_out, not_83_out, not_84_out, not_85_out, not_86_out, not_87_out, not_88_out, not_89_out,
       not_90_out, not_91_out, not_92_out, not_93_out, not_94_out, not_95_out, not_96_out, not_97_out,
       not_98_out, not_99_out, not_100_out, not_101_out, not_102_out, not_103_out, not_104_out, not_105_out,
       not_106_out, not_107_out, not_108_out, not_109_out, not_110_out, not_111_out, not_112_out,
       not_113_out, not_114_out, not_115_out, not_116_out, not_117_out, not_118_out, not_119_out,
       not_120_out, not_121_out, not_122_out, not_123_out, not_124_out, not_125_out, not_126_out,
       not_127_out, not_128_out, not_129_out, not_130_out, not_131_out, not_132_out, not_133_out,
       not_134_out, not_135_out, not_136_out, not_137_out, not_138_out, not_139_out, not_140_out,
       not_141_out, not_142_out, not_143_out, not_144_out, not_145_out, not_146_out, not_147_out,
       not_148_out, not_149_out, not_150_out, not_151_out, not_152_out, not_153_out, not_154_out,
       not_155_out, not_156_out, not_157_out, not_158_out, not_159_out, not_160_out, not_161_out,
       not_162_out, not_163_out, not_164_out, not_165_out, not_166_out, not_167_out, RegDst, SignedExt,
       SysCall;
  wire [1:1] or_1_out;
  wire [31:0] bit_extender_1_out, bit_extender_2_out;

  assign bit_extender_1_out = {{16{1'b0}}, in_1[15:0]};  // Bit_Extender bit_extender_1
  assign bit_extender_2_out = {{16{in_1[15]}}, in_1[15:0]};  // Bit_Extender bit_extender_2
  or or_1 (or_1_out[1], MFC0, MTC0);
  Multiplexer #(.select(2), .width(5), .enable("false")) multiplexer_1 (
    .in0(in_1[25:21]), .in1(5'b00100), .in2({5{1'b0}}), .in3({5{1'b0}}), .out(R1),
    .sel({or_1_out[1], SysCall}));
  Multiplexer #(.width(5), .enable("false")) multiplexer_2 (.in0(in_1[20:16]), .in1(5'b00010), .out(R2), .sel(SysCall));
  Multiplexer #(.width(32), .enable("false")) multiplexer_3 (
    .in0(bit_extender_1_out), .in1(bit_extender_2_out), .out(Immediate), .sel(SignedExt));
  Multiplexer #(.select(2), .width(5), .enable("false")) multiplexer_4 (
    .in0(in_1[20:16]), .in1(in_1[15:11]), .in2({5{1'b1}}), .in3({5{1'b1}}), .out(W_num), .sel({JAL, RegDst}));
  and and_1 (and_1_out, ~in_1[26], ~in_1[27], ~in_1[28], ~in_1[29], in_1[30], ~in_1[31]);  // AND_Gate
  and and_2 (and_2_out, ~in_1[21], ~in_1[22], ~in_1[23], ~in_1[24], ~in_1[25]);  // AND_Gate
  and and_3 (and_3_out, ~in_1[21], ~in_1[22], in_1[23], ~in_1[24], ~in_1[25]);  // AND_Gate
  and and_4 (MFC0, and_1_out, and_2_out);
  and and_5 (MTC0, and_1_out, and_3_out);
  not not_1 (not_1_out, in_1[31]);
  not not_2 (not_2_out, in_1[30]);
  not not_3 (not_3_out, in_1[29]);
  not not_4 (not_4_out, in_1[28]);
  not not_5 (not_5_out, in_1[27]);
  not not_6 (not_6_out, in_1[26]);
  not not_7 (not_7_out, in_1[5]);
  not not_8 (not_8_out, in_1[4]);
  not not_9 (not_9_out, in_1[1]);
  not not_10 (not_10_out, in_1[0]);
  not not_11 (not_11_out, in_1[31]);
  not not_12 (not_12_out, in_1[30]);
  not not_13 (not_13_out, in_1[29]);
  not not_14 (not_14_out, in_1[27]);
  not not_15 (not_15_out, in_1[26]);
  not not_16 (not_16_out, in_1[31]);
  not not_17 (not_17_out, in_1[30]);
  not not_18 (not_18_out, in_1[29]);
  not not_19 (not_19_out, in_1[27]);
  not not_20 (not_20_out, in_1[31]);
  not not_21 (not_21_out, in_1[30]);
  not not_22 (not_22_out, in_1[28]);
  not not_23 (not_23_out, in_1[27]);
  not not_24 (not_24_out, in_1[26]);
  not not_25 (not_25_out, in_1[31]);
  not not_26 (not_26_out, in_1[30]);
  not not_27 (not_27_out, in_1[28]);
  not not_28 (not_28_out, in_1[27]);
  not not_29 (not_29_out, in_1[31]);
  not not_30 (not_30_out, in_1[30]);
  not not_31 (not_31_out, in_1[28]);
  not not_32 (not_32_out, in_1[26]);
  not not_33 (not_33_out, in_1[30]);
  not not_34 (not_34_out, in_1[29]);
  not not_35 (not_35_out, in_1[28]);
  not not_36 (not_36_out, in_1[30]);
  not not_37 (not_37_out, in_1[28]);
  not not_38 (not_38_out, in_1[30]);
  not not_39 (not_39_out, in_1[29]);
  not not_40 (not_40_out, in_1[28]);
  not not_41 (not_41_out, in_1[27]);
  not not_42 (not_42_out, in_1[26]);
  not not_43 (not_43_out, in_1[31]);
  not not_44 (not_44_out, in_1[30]);
  not not_45 (not_45_out, in_1[29]);
  not not_46 (not_46_out, in_1[26]);
  not not_47 (not_47_out, in_1[31]);
  not not_48 (not_48_out, in_1[30]);
  not not_49 (not_49_out, in_1[29]);
  not not_50 (not_50_out, in_1[28]);
  not not_51 (not_51_out, in_1[27]);
  not not_52 (not_52_out, in_1[26]);
  not not_53 (not_53_out, in_1[5]);
  not not_54 (not_54_out, in_1[4]);
  not not_55 (not_55_out, in_1[3]);
  not not_56 (not_56_out, in_1[2]);
  not not_57 (not_57_out, in_1[1]);
  not not_58 (not_58_out, in_1[0]);
  not not_59 (not_59_out, in_1[31]);
  not not_60 (not_60_out, in_1[30]);
  not not_61 (not_61_out, in_1[29]);
  not not_62 (not_62_out, in_1[28]);
  not not_63 (not_63_out, in_1[27]);
  not not_64 (not_64_out, in_1[26]);
  not not_65 (not_65_out, in_1[5]);
  not not_66 (not_66_out, in_1[4]);
  not not_67 (not_67_out, in_1[3]);
  not not_68 (not_68_out, in_1[2]);
  not not_69 (not_69_out, in_1[31]);
  not not_70 (not_70_out, in_1[30]);
  not not_71 (not_71_out, in_1[29]);
  not not_72 (not_72_out, in_1[28]);
  not not_73 (not_73_out, in_1[27]);
  not not_74 (not_74_out, in_1[26]);
  not not_75 (not_75_out, in_1[5]);
  not not_76 (not_76_out, in_1[4]);
  not not_77 (not_77_out, in_1[3]);
  not not_78 (not_78_out, in_1[2]);
  not not_79 (not_79_out, in_1[0]);
  not not_80 (not_80_out, in_1[31]);
  not not_81 (not_81_out, in_1[30]);
  not not_82 (not_82_out, in_1[29]);
  not not_83 (not_83_out, in_1[28]);
  not not_84 (not_84_out, in_1[27]);
  not not_85 (not_85_out, in_1[26]);
  not not_86 (not_86_out, in_1[4]);
  not not_87 (not_87_out, in_1[3]);
  not not_88 (not_88_out, in_1[2]);
  not not_89 (not_89_out, in_1[1]);
  not not_90 (not_90_out, in_1[0]);
  not not_91 (not_91_out, in_1[31]);
  not not_92 (not_92_out, in_1[30]);
  not not_93 (not_93_out, in_1[29]);
  not not_94 (not_94_out, in_1[28]);
  not not_95 (not_95_out, in_1[27]);
  not not_96 (not_96_out, in_1[26]);
  not not_97 (not_97_out, in_1[4]);
  not not_98 (not_98_out, in_1[3]);
  not not_99 (not_99_out, in_1[2]);
  not not_100 (not_100_out, in_1[1]);
  not not_101 (not_101_out, in_1[31]);
  not not_102 (not_102_out, in_1[30]);
  not not_103 (not_103_out, in_1[29]);
  not not_104 (not_104_out, in_1[28]);
  not not_105 (not_105_out, in_1[27]);
  not not_106 (not_106_out, in_1[26]);
  not not_107 (not_107_out, in_1[4]);
  not not_108 (not_108_out, in_1[3]);
  not not_109 (not_109_out, in_1[2]);
  not not_110 (not_110_out, in_1[0]);
  not not_111 (not_111_out, in_1[31]);
  not not_112 (not_112_out, in_1[30]);
  not not_113 (not_113_out, in_1[29]);
  not not_114 (not_114_out, in_1[28]);
  not not_115 (not_115_out, in_1[27]);
  not not_116 (not_116_out, in_1[26]);
  not not_117 (not_117_out, in_1[4]);
  not not_118 (not_118_out, in_1[3]);
  not not_119 (not_119_out, in_1[1]);
  not not_120 (not_120_out, in_1[0]);
  not not_121 (not_121_out, in_1[31]);
  not not_122 (not_122_out, in_1[30]);
  not not_123 (not_123_out, in_1[29]);
  not not_124 (not_124_out, in_1[28]);
  not not_125 (not_125_out, in_1[27]);
  not not_126 (not_126_out, in_1[26]);
  not not_127 (not_127_out, in_1[4]);
  not not_128 (not_128_out, in_1[3]);
  not not_129 (not_129_out, in_1[1]);
  not not_130 (not_130_out, in_1[31]);
  not not_131 (not_131_out, in_1[30]);
  not not_132 (not_132_out, in_1[29]);
  not not_133 (not_133_out, in_1[28]);
  not not_134 (not_134_out, in_1[27]);
  not not_135 (not_135_out, in_1[26]);
  not not_136 (not_136_out, in_1[4]);
  not not_137 (not_137_out, in_1[3]);
  not not_138 (not_138_out, in_1[31]);
  not not_139 (not_139_out, in_1[30]);
  not not_140 (not_140_out, in_1[29]);
  not not_141 (not_141_out, in_1[28]);
  not not_142 (not_142_out, in_1[27]);
  not not_143 (not_143_out, in_1[26]);
  not not_144 (not_144_out, in_1[4]);
  not not_145 (not_145_out, in_1[2]);
  not not_146 (not_146_out, in_1[0]);
  not not_147 (not_147_out, in_1[31]);
  not not_148 (not_148_out, in_1[30]);
  not not_149 (not_149_out, in_1[29]);
  not not_150 (not_150_out, in_1[28]);
  not not_151 (not_151_out, in_1[27]);
  not not_152 (not_152_out, in_1[26]);
  not not_153 (not_153_out, in_1[4]);
  not not_154 (not_154_out, in_1[2]);
  not not_155 (not_155_out, in_1[31]);
  not not_156 (not_156_out, in_1[30]);
  not not_157 (not_157_out, in_1[29]);
  not not_158 (not_158_out, in_1[28]);
  not not_159 (not_159_out, in_1[27]);
  not not_160 (not_160_out, in_1[26]);
  not not_161 (not_161_out, in_1[4]);
  not not_162 (not_162_out, in_1[3]);
  not not_163 (not_163_out, in_1[2]);
  not not_164 (not_164_out, in_1[31]);
  not not_165 (not_165_out, in_1[30]);
  not not_166 (not_166_out, in_1[29]);
  not not_167 (not_167_out, in_1[28]);
  and and_6 (SysCall, not_1_out, not_2_out, not_3_out, not_4_out, not_5_out, not_6_out, not_7_out, not_8_out, in_1[3], in_1[2], not_9_out, not_10_out);
  and and_7 (and_7_out, not_11_out, not_12_out, not_13_out, in_1[28], not_14_out, not_15_out);
  and and_8 (and_8_out, not_16_out, not_17_out, not_18_out, in_1[28], not_19_out, in_1[26]);
  and and_9 (and_9_out, not_20_out, not_21_out, in_1[29], not_22_out, not_23_out, not_24_out);
  and and_10 (and_10_out, not_25_out, not_26_out, in_1[29], not_27_out, not_28_out, in_1[26]);
  and and_11 (and_11_out, not_29_out, not_30_out, in_1[29], not_31_out, in_1[27], not_32_out);
  and and_12 (and_12_out, in_1[31], not_33_out, not_34_out, not_35_out, in_1[27], in_1[26]);
  and and_13 (and_13_out, in_1[31], not_36_out, in_1[29], not_37_out, in_1[27], in_1[26]);
  and and_14 (and_14_out, in_1[31], not_38_out, not_39_out, not_40_out, not_41_out, not_42_out);
  and and_15 (and_15_out, not_43_out, not_44_out, not_45_out, in_1[28], in_1[27], not_46_out);
  and and_16 (and_16_out, not_47_out, not_48_out, not_49_out, not_50_out, not_51_out, not_52_out, not_53_out, not_54_out, not_55_out, not_56_out, not_57_out, not_58_out);
  and and_17 (and_17_out, not_59_out, not_60_out, not_61_out, not_62_out, not_63_out, not_64_out, not_65_out, not_66_out, not_67_out, not_68_out, in_1[1], in_1[0]);
  and and_18 (and_18_out, not_69_out, not_70_out, not_71_out, not_72_out, not_73_out, not_74_out, not_75_out, not_76_out, not_77_out, not_78_out, in_1[1], not_79_out);
  and and_19 (and_19_out, not_80_out, not_81_out, not_82_out, not_83_out, not_84_out, not_85_out, in_1[5], not_86_out, not_87_out, not_88_out, not_89_out, not_90_out);
  and and_20 (and_20_out, not_91_out, not_92_out, not_93_out, not_94_out, not_95_out, not_96_out, in_1[5], not_97_out, not_98_out, not_99_out, not_100_out, in_1[0]);
  and and_21 (and_21_out, not_101_out, not_102_out, not_103_out, not_104_out, not_105_out, not_106_out, in_1[5], not_107_out, not_108_out, not_109_out, in_1[1], not_110_out);
  and and_22 (and_22_out, not_111_out, not_112_out, not_113_out, not_114_out, not_115_out, not_116_out, in_1[5], not_117_out, not_118_out, in_1[2], not_119_out, not_120_out);
  and and_23 (and_23_out, not_121_out, not_122_out, not_123_out, not_124_out, not_125_out, not_126_out, in_1[5], not_127_out, not_128_out, in_1[2], not_129_out, in_1[0]);
  and and_24 (and_24_out, not_130_out, not_131_out, not_132_out, not_133_out, not_134_out, not_135_out, in_1[5], not_136_out, not_137_out, in_1[2], in_1[1], in_1[0]);
  and and_25 (and_25_out, not_138_out, not_139_out, not_140_out, not_141_out, not_142_out, not_143_out, in_1[5], not_144_out, in_1[3], not_145_out, in_1[1], not_146_out);
  and and_26 (and_26_out, not_147_out, not_148_out, not_149_out, not_150_out, not_151_out, not_152_out, in_1[5], not_153_out, in_1[3], not_154_out, in_1[1], in_1[0]);
  and and_27 (and_27_out, not_155_out, not_156_out, not_157_out, not_158_out, not_159_out, not_160_out, in_1[5], not_161_out, not_162_out, not_163_out, in_1[1], in_1[0]);
  and and_28 (JAL, not_164_out, not_165_out, not_166_out, not_167_out, in_1[27], in_1[26]);
  or or_2 (SignedExt, and_7_out, and_8_out, and_9_out, and_10_out, and_11_out, and_12_out, and_13_out, and_14_out, and_15_out);
  or or_3 (RegDst, and_16_out, and_17_out, and_18_out, and_19_out, and_20_out, and_21_out, MTC0, and_22_out, and_23_out, and_24_out, and_25_out, and_26_out, and_27_out);

  assign shamt = in_1[10:6];

  // Notes on the sheet:
  //   rs
  //   rt
  //   rd
  //   OP
  //   Func
endmodule

module \重定向锁存器2  (
  input  [3:0] Din32,
  input  [31:0] Din32_2,
  input  Din32_3,
  input  [2:0] Din32_4,
  input  Din32_5,
  input  Din32_6,
  input  [31:0] Din32_7,
  input  [19:0] Din32_8,
  input  [31:0] Din32_9,
  input  [31:0] Din32_10,
  input  [31:0] Din32_11,
  input  [31:0] Din32_12,
  input  CLK,
  input  \同步清零_气泡_高电平有效 ,
  input  \使能端_低电平有效_stall_高电平有效 ,
  output [3:0] Dout32,
  output [31:0] Dout32_2,
  output Dout32_3,
  output [2:0] Dout32_4,
  output Dout32_5,
  output Dout32_6,
  output [31:0] Dout32_7,
  output [19:0] Dout32_8,
  output [31:0] Dout32_9,
  output [31:0] Dout32_10,
  output [31:0] Dout32_11,
  output [31:0] Dout32_12
);

  wire multiplexer_3_out, multiplexer_5_out, multiplexer_6_out, not_1_out;
  wire [2:0] multiplexer_4_out;
  wire [3:0] multiplexer_1_out;
  wire [19:0] multiplexer_8_out;
  wire [31:0] multiplexer_2_out, multiplexer_7_out, multiplexer_9_out, multiplexer_10_out,
       multiplexer_11_out, multiplexer_12_out;

  Multiplexer #(.width(4), .enable("false")) multiplexer_1 (
    .in0(Din32), .in1(4'b0000), .out(multiplexer_1_out), .sel(\同步清零_气泡_高电平有效 ));
  Multiplexer #(.width(32), .enable("false")) multiplexer_2 (
    .in0(Din32_2), .in1({32{1'b0}}), .out(multiplexer_2_out), .sel(\同步清零_气泡_高电平有效 ));
  Multiplexer #(.enable("false")) multiplexer_3 (
    .in0(Din32_3), .in1(1'b0), .out(multiplexer_3_out), .sel(\同步清零_气泡_高电平有效 ));
  Multiplexer #(.width(3), .enable("false")) multiplexer_4 (
    .in0(Din32_4), .in1(3'b000), .out(multiplexer_4_out), .sel(\同步清零_气泡_高电平有效 ));
  Multiplexer #(.enable("false")) multiplexer_5 (
    .in0(Din32_5), .in1(1'b0), .out(multiplexer_5_out), .sel(\同步清零_气泡_高电平有效 ));
  Multiplexer #(.enable("false")) multiplexer_6 (
    .in0(Din32_6), .in1(1'b0), .out(multiplexer_6_out), .sel(\同步清零_气泡_高电平有效 ));
  Multiplexer #(.width(32), .enable("false")) multiplexer_7 (
    .in0(Din32_7), .in1({32{1'b0}}), .out(multiplexer_7_out), .sel(\同步清零_气泡_高电平有效 ));
  Multiplexer #(.width(20), .enable("false")) multiplexer_8 (
    .in0(Din32_8), .in1({20{1'b0}}), .out(multiplexer_8_out), .sel(\同步清零_气泡_高电平有效 ));
  Multiplexer #(.width(32), .enable("false")) multiplexer_9 (
    .in0(Din32_9), .in1({32{1'b0}}), .out(multiplexer_9_out), .sel(\同步清零_气泡_高电平有效 ));
  Multiplexer #(.width(32), .enable("false")) multiplexer_10 (
    .in0(Din32_10), .in1({32{1'b0}}), .out(multiplexer_10_out), .sel(\同步清零_气泡_高电平有效 ));
  Multiplexer #(.width(32), .enable("false")) multiplexer_11 (
    .in0(Din32_11), .in1({32{1'b0}}), .out(multiplexer_11_out), .sel(\同步清零_气泡_高电平有效 ));
  Multiplexer #(.width(32), .enable("false")) multiplexer_12 (
    .in0(Din32_12), .in1({32{1'b0}}), .out(multiplexer_12_out), .sel(\同步清零_气泡_高电平有效 ));
  Pull_Resistor pull_resistor_1 (.node(\同步清零_气泡_高电平有效 ));
  not not_1 (not_1_out, \使能端_低电平有效_stall_高电平有效 );
  Register #(.width(4)) register_1 (.D(multiplexer_1_out), .en(not_1_out), .Q(Dout32), .clk(CLK));  // open: clr
  Register #(.width(32)) register_2 (.D(multiplexer_2_out), .en(not_1_out), .Q(Dout32_2), .clk(CLK));  // open: clr
  Register #(.width(1)) register_3 (.D(multiplexer_3_out), .en(not_1_out), .Q(Dout32_3), .clk(CLK));  // open: clr
  Register #(.width(3)) register_4 (.D(multiplexer_4_out), .en(not_1_out), .Q(Dout32_4), .clk(CLK));  // open: clr
  Register #(.width(1)) register_5 (.D(multiplexer_5_out), .en(not_1_out), .Q(Dout32_5), .clk(CLK));  // open: clr
  Register #(.width(1)) register_6 (.D(multiplexer_6_out), .en(not_1_out), .Q(Dout32_6), .clk(CLK));  // open: clr
  Register #(.width(32)) register_7 (.D(multiplexer_7_out), .en(not_1_out), .Q(Dout32_7), .clk(CLK));  // open: clr
  Register #(.width(20)) register_8 (.D(multiplexer_8_out), .en(not_1_out), .Q(Dout32_8), .clk(CLK));  // open: clr
  Register #(.width(32)) register_9 (.D(multiplexer_9_out), .en(not_1_out), .Q(Dout32_9), .clk(CLK));  // open: clr
  Register #(.width(32)) register_10 (.D(multiplexer_10_out), .en(not_1_out), .Q(Dout32_10), .clk(CLK));  // open: clr
  Register #(.width(32)) register_11 (.D(multiplexer_11_out), .en(not_1_out), .Q(Dout32_11), .clk(CLK));  // open: clr
  Register #(.width(32)) register_12 (.D(multiplexer_12_out), .en(not_1_out), .Q(Dout32_12), .clk(CLK));  // open: clr
  Pull_Resistor pull_resistor_2 (.node(not_1_out));
endmodule

module \重定向锁存器3  (
  input  [31:0] Din32,
  input  [31:0] Din32_2,
  input  [8:0] Din32_3,
  input  [31:0] Din32_4,
  input  [31:0] Din32_5,
  input  \传输状态In_表明当前传输数据有效 ,
  input  CLK,
  input  \同步清零_气泡_高电平有效 ,
  input  \使能端_低电平有效_stall_高电平有效 ,
  output [31:0] Dout32,
  output [31:0] Dout32_2,
  output [8:0] Dout32_3,
  output [31:0] Dout32_4,
  output [31:0] Dout32_5,
  output \传输状态Out_表明当前传输数据有效 
);

  wire multiplexer_6_out, pull_resistor_2_node;
  wire [8:0] multiplexer_3_out;
  wire [31:0] multiplexer_1_out, multiplexer_2_out, multiplexer_4_out, multiplexer_5_out;

  Multiplexer #(.width(32), .enable("false")) multiplexer_1 (
    .in0(Din32), .in1({32{1'b0}}), .out(multiplexer_1_out), .sel(\同步清零_气泡_高电平有效 ));
  Multiplexer #(.width(32), .enable("false")) multiplexer_2 (
    .in0(Din32_2), .in1({32{1'b0}}), .out(multiplexer_2_out), .sel(\同步清零_气泡_高电平有效 ));
  Multiplexer #(.width(9), .enable("false")) multiplexer_3 (
    .in0(Din32_3), .in1({9{1'b0}}), .out(multiplexer_3_out), .sel(\同步清零_气泡_高电平有效 ));
  Multiplexer #(.width(32), .enable("false")) multiplexer_4 (
    .in0(Din32_4), .in1({32{1'b0}}), .out(multiplexer_4_out), .sel(\同步清零_气泡_高电平有效 ));
  Multiplexer #(.width(32), .enable("false")) multiplexer_5 (
    .in0(Din32_5), .in1({32{1'b0}}), .out(multiplexer_5_out), .sel(\同步清零_气泡_高电平有效 ));
  Multiplexer #(.enable("false")) multiplexer_6 (
    .in0(\传输状态In_表明当前传输数据有效 ), .in1(1'b0), .out(multiplexer_6_out), .sel(\同步清零_气泡_高电平有效 ));
  Pull_Resistor pull_resistor_1 (.node(\同步清零_气泡_高电平有效 ));
  Pull_Resistor pull_resistor_2 (.node(pull_resistor_2_node));
  not not_1 (pull_resistor_2_node, \使能端_低电平有效_stall_高电平有效 );
  Register #(.width(32)) register_1 (
    .D(multiplexer_1_out), .en(pull_resistor_2_node), .Q(Dout32), .clk(CLK));  // open: clr
  Register #(.width(32)) register_2 (
    .D(multiplexer_2_out), .en(pull_resistor_2_node), .Q(Dout32_2), .clk(CLK));  // open: clr
  Register #(.width(9)) register_3 (
    .D(multiplexer_3_out), .en(pull_resistor_2_node), .Q(Dout32_3), .clk(CLK));  // open: clr
  Register #(.width(32)) register_4 (
    .D(multiplexer_4_out), .en(pull_resistor_2_node), .Q(Dout32_4), .clk(CLK));  // open: clr
  Register #(.width(32)) register_5 (
    .D(multiplexer_5_out), .en(pull_resistor_2_node), .Q(Dout32_5), .clk(CLK));  // open: clr
  Register #(.width(1)) register_6 (
    .D(multiplexer_6_out), .en(pull_resistor_2_node), .Q(\传输状态Out_表明当前传输数据有效 ), .clk(CLK));  // open: clr
endmodule

module \重定向锁存器4  (
  input  [31:0] Din32,
  input  [31:0] Din32_2,
  input  [6:0] Din32_3,
  input  [31:0] Din32_4,
  input  \传输状态In_表明当前传输数据有效 ,
  input  CLK,
  input  \同步清零_气泡_高电平有效 ,
  input  \使能端_低电平有效_stall_高电平有效 ,
  output [31:0] Dout32,
  output [31:0] Dout32_2,
  output [6:0] Dout32_3,
  output [31:0] Dout32_4,
  output \传输状态Out_表明当前传输数据有效 
);

  wire multiplexer_5_out, pull_resistor_2_node;
  wire [6:0] multiplexer_3_out;
  wire [31:0] multiplexer_1_out, multiplexer_2_out, multiplexer_4_out;

  Multiplexer #(.width(32), .enable("false")) multiplexer_1 (
    .in0(Din32), .in1({32{1'b0}}), .out(multiplexer_1_out), .sel(\同步清零_气泡_高电平有效 ));
  Multiplexer #(.width(32), .enable("false")) multiplexer_2 (
    .in0(Din32_2), .in1({32{1'b0}}), .out(multiplexer_2_out), .sel(\同步清零_气泡_高电平有效 ));
  Multiplexer #(.width(7), .enable("false")) multiplexer_3 (
    .in0(Din32_3), .in1({7{1'b0}}), .out(multiplexer_3_out), .sel(\同步清零_气泡_高电平有效 ));
  Multiplexer #(.width(32), .enable("false")) multiplexer_4 (
    .in0(Din32_4), .in1({32{1'b0}}), .out(multiplexer_4_out), .sel(\同步清零_气泡_高电平有效 ));
  Multiplexer #(.enable("false")) multiplexer_5 (
    .in0(\传输状态In_表明当前传输数据有效 ), .in1(1'b0), .out(multiplexer_5_out), .sel(\同步清零_气泡_高电平有效 ));
  Pull_Resistor pull_resistor_1 (.node(\同步清零_气泡_高电平有效 ));
  Pull_Resistor pull_resistor_2 (.node(pull_resistor_2_node));
  not not_1 (pull_resistor_2_node, \使能端_低电平有效_stall_高电平有效 );
  Register #(.width(32)) register_1 (
    .D(multiplexer_1_out), .en(pull_resistor_2_node), .Q(Dout32), .clk(CLK));  // open: clr
  Register #(.width(32)) register_2 (
    .D(multiplexer_2_out), .en(pull_resistor_2_node), .Q(Dout32_2), .clk(CLK));  // open: clr
  Register #(.width(7)) register_3 (
    .D(multiplexer_3_out), .en(pull_resistor_2_node), .Q(Dout32_3), .clk(CLK));  // open: clr
  Register #(.width(32)) register_4 (
    .D(multiplexer_4_out), .en(pull_resistor_2_node), .Q(Dout32_4), .clk(CLK));  // open: clr
  Register #(.width(1)) register_5 (
    .D(multiplexer_5_out), .en(pull_resistor_2_node), .Q(\传输状态Out_表明当前传输数据有效 ), .clk(CLK));  // open: clr
endmodule

module \重定向选择信号  (
  input  ExRegWrite,
  input  [4:0] ExR,
  input  [31:0] IP,
  input  MemRegWrite,
  input  [4:0] MemR,
  input  MemMemToReg,
  input  ExMemToReg,
  output [1:0] R1Select,
  output [1:0] R2Select,
  output \气泡 
);

  wire and_1_out, and_2_out, and_3_out, and_4_out, and_5_out, and_6_out, and_7_out, and_8_out, and_9_out,
       and_10_out, and_11_out, and_12_out, and_13_out, and_14_out, and_15_out, and_16_out, and_21_out,
       and_22_out, comparator_1_eq, comparator_2_eq, comparator_3_eq, comparator_4_eq, comparator_5_eq,
       comparator_6_eq, nor_1_out, nor_2_out, not_1_out, not_2_out, not_3_out, not_4_out, not_5_out,
       not_6_out, not_7_out, not_8_out, not_9_out, not_10_out, not_11_out, not_12_out, not_13_out,
       not_14_out, not_15_out, not_16_out, not_17_out, not_18_out, not_19_out, not_20_out, not_21_out,
       not_22_out, not_23_out, not_24_out, not_25_out, not_26_out, not_27_out, not_28_out, not_29_out,
       not_30_out, not_31_out, not_32_out, not_33_out, not_34_out, not_35_out, not_36_out, not_37_out,
       not_38_out, not_39_out, not_40_out, not_41_out, not_42_out, not_43_out, not_44_out, not_45_out,
       not_46_out, not_47_out, not_48_out, not_49_out, not_50_out, not_51_out, not_52_out, not_53_out,
       not_54_out, not_55_out, not_56_out, not_57_out, not_58_out, not_59_out, not_60_out, not_61_out,
       not_62_out, not_63_out, not_64_out, not_65_out, not_66_out, not_67_out, not_68_out, not_69_out,
       not_70_out, not_71_out, not_72_out, not_73_out, not_74_out, not_75_out, not_76_out, not_77_out,
       not_78_out, not_79_out, not_80_out, not_81_out, not_82_out, not_83_out, not_84_out, not_85_out,
       not_86_out, not_87_out, not_88_out, not_89_out, or_1_out, or_2_out;
  wire [1:0] and_19_out, and_20_out;
  wire [7:0] multiplexer_2_out;
  wire [9:0] multiplexer_1_out;

  not not_1 (not_1_out, IP[31]);
  not not_2 (not_2_out, IP[30]);
  not not_3 (not_3_out, IP[29]);
  not not_4 (not_4_out, IP[28]);
  not not_5 (not_5_out, IP[27]);
  not not_6 (not_6_out, IP[26]);
  not not_7 (not_7_out, IP[5]);
  not not_8 (not_8_out, IP[4]);
  not not_9 (not_9_out, IP[1]);
  not not_10 (not_10_out, IP[0]);
  not not_11 (not_11_out, IP[31]);
  not not_12 (not_12_out, IP[30]);
  not not_13 (not_13_out, IP[29]);
  not not_14 (not_14_out, IP[28]);
  not not_15 (not_15_out, IP[26]);
  not not_16 (not_16_out, IP[31]);
  not not_17 (not_17_out, IP[30]);
  not not_18 (not_18_out, IP[29]);
  not not_19 (not_19_out, IP[28]);
  not not_20 (not_20_out, IP[31]);
  not not_21 (not_21_out, IP[30]);
  not not_22 (not_22_out, IP[29]);
  not not_23 (not_23_out, IP[28]);
  not not_24 (not_24_out, IP[27]);
  not not_25 (not_25_out, IP[26]);
  not not_26 (not_26_out, IP[5]);
  not not_27 (not_27_out, IP[4]);
  not not_28 (not_28_out, IP[2]);
  not not_29 (not_29_out, IP[1]);
  not not_30 (not_30_out, IP[0]);
  not not_31 (not_31_out, IP[31]);
  not not_32 (not_32_out, IP[30]);
  not not_33 (not_33_out, IP[29]);
  not not_34 (not_34_out, IP[28]);
  not not_35 (not_35_out, IP[26]);
  not not_36 (not_36_out, IP[31]);
  not not_37 (not_37_out, IP[30]);
  not not_38 (not_38_out, IP[29]);
  not not_39 (not_39_out, IP[28]);
  not not_40 (not_40_out, IP[31]);
  not not_41 (not_41_out, IP[30]);
  not not_42 (not_42_out, IP[28]);
  not not_43 (not_43_out, IP[27]);
  not not_44 (not_44_out, IP[26]);
  not not_45 (not_45_out, IP[31]);
  not not_46 (not_46_out, IP[30]);
  not not_47 (not_47_out, IP[27]);
  not not_48 (not_48_out, IP[26]);
  not not_49 (not_49_out, IP[31]);
  not not_50 (not_50_out, IP[30]);
  not not_51 (not_51_out, IP[28]);
  not not_52 (not_52_out, IP[27]);
  not not_53 (not_53_out, IP[31]);
  not not_54 (not_54_out, IP[30]);
  not not_55 (not_55_out, IP[28]);
  not not_56 (not_56_out, IP[26]);
  not not_57 (not_57_out, IP[31]);
  not not_58 (not_58_out, IP[30]);
  not not_59 (not_59_out, IP[27]);
  not not_60 (not_60_out, IP[30]);
  not not_61 (not_61_out, IP[29]);
  not not_62 (not_62_out, IP[28]);
  not not_63 (not_63_out, IP[31]);
  not not_64 (not_64_out, IP[30]);
  not not_65 (not_65_out, IP[26]);
  not not_66 (not_66_out, IP[30]);
  not not_67 (not_67_out, IP[29]);
  not not_68 (not_68_out, IP[28]);
  not not_69 (not_69_out, IP[27]);
  not not_70 (not_70_out, IP[26]);
  not not_71 (not_71_out, IP[31]);
  not not_72 (not_72_out, IP[29]);
  not not_73 (not_73_out, IP[28]);
  not not_74 (not_74_out, IP[27]);
  not not_75 (not_75_out, IP[26]);
  not not_76 (not_76_out, IP[21]);
  not not_77 (not_77_out, IP[22]);
  not not_78 (not_78_out, IP[24]);
  not not_79 (not_79_out, IP[25]);
  not not_80 (not_80_out, IP[31]);
  not not_81 (not_81_out, IP[29]);
  not not_82 (not_82_out, IP[28]);
  not not_83 (not_83_out, IP[27]);
  not not_84 (not_84_out, IP[26]);
  not not_85 (not_85_out, IP[21]);
  not not_86 (not_86_out, IP[22]);
  not not_87 (not_87_out, IP[23]);
  not not_88 (not_88_out, IP[24]);
  not not_89 (not_89_out, IP[25]);
  and and_1 (and_1_out, not_1_out, not_2_out, not_3_out, not_4_out, not_5_out, not_6_out, not_7_out, not_8_out, IP[3], IP[2], not_9_out, not_10_out);
  and and_2 (and_2_out, not_11_out, not_12_out, not_13_out, not_14_out, IP[27], not_15_out);
  and and_3 (and_3_out, not_16_out, not_17_out, not_18_out, not_19_out, IP[27], IP[26]);
  and and_4 (and_4_out, not_20_out, not_21_out, not_22_out, not_23_out, not_24_out, not_25_out, not_26_out, not_27_out, IP[3], not_28_out, not_29_out, not_30_out);
  and and_5 (and_5_out, not_31_out, not_32_out, not_33_out, not_34_out, IP[27], not_35_out);
  and and_6 (and_6_out, not_36_out, not_37_out, not_38_out, not_39_out, IP[27], IP[26]);
  and and_7 (and_7_out, not_40_out, not_41_out, IP[29], not_42_out, not_43_out, not_44_out);
  and and_8 (and_8_out, not_45_out, not_46_out, IP[29], IP[28], not_47_out, not_48_out);
  and and_9 (and_9_out, not_49_out, not_50_out, IP[29], not_51_out, not_52_out, IP[26]);
  and and_10 (and_10_out, not_53_out, not_54_out, IP[29], not_55_out, IP[27], not_56_out);
  and and_11 (and_11_out, not_57_out, not_58_out, IP[29], IP[28], not_59_out, IP[26]);
  and and_12 (and_12_out, IP[31], not_60_out, not_61_out, not_62_out, IP[27], IP[26]);
  and and_13 (and_13_out, not_63_out, not_64_out, IP[29], IP[28], IP[27], not_65_out);
  and and_14 (and_14_out, IP[31], not_66_out, not_67_out, not_68_out, not_69_out, not_70_out);
  and and_15 (and_15_out, not_71_out, IP[30], not_72_out, not_73_out, not_74_out, not_75_out, not_76_out, not_77_out, IP[23], not_78_out, not_79_out);
  nor nor_1 (nor_1_out, and_16_out, and_2_out, and_3_out, and_15_out);
  and and_16 (and_16_out, not_80_out, IP[30], not_81_out, not_82_out, not_83_out, not_84_out, not_85_out, not_86_out, not_87_out, not_88_out, not_89_out);
  nor nor_2 (nor_2_out, and_4_out, and_5_out, and_6_out, and_7_out, and_8_out, and_9_out, and_10_out, and_11_out, and_12_out, and_13_out, and_14_out, and_16_out);
  Multiplexer #(.width(10), .enable("false")) multiplexer_1 (
    .in0({IP[20:16], IP[25:21]}), .in1(10'h44), .out(multiplexer_1_out), .sel(and_1_out));
  Comparator #(.width(5)) comparator_1 (.a(ExR), .b({5{1'b0}}), .eq(comparator_1_eq));  // open: gt, lt
  Comparator #(.width(5)) comparator_2 (.a(multiplexer_1_out[4:0]), .b(ExR), .eq(comparator_2_eq));  // open: gt, lt
  Comparator #(.width(5)) comparator_3 (.a(multiplexer_1_out[9:5]), .b(ExR), .eq(comparator_3_eq));  // open: gt, lt
  Comparator #(.width(5)) comparator_4 (.a(MemR), .b({5{1'b0}}), .eq(comparator_4_eq));  // open: gt, lt
  Comparator #(.width(5)) comparator_5 (.a(multiplexer_1_out[4:0]), .b(MemR), .eq(comparator_5_eq));  // open: gt, lt
  Comparator #(.width(5)) comparator_6 (.a(multiplexer_1_out[9:5]), .b(MemR), .eq(comparator_6_eq));  // open: gt, lt
  and and_17 (and_19_out[1], nor_1_out, ExRegWrite, comparator_2_eq, ~comparator_1_eq);  // AND_Gate
  and and_18 (and_20_out[1], nor_2_out, ExRegWrite, comparator_3_eq, ~comparator_1_eq);  // AND_Gate
  and and_19 (and_19_out[0], nor_1_out, MemRegWrite, comparator_5_eq, ~comparator_4_eq);  // AND_Gate
  and and_20 (and_20_out[0], MemRegWrite, nor_2_out, comparator_6_eq, ~comparator_4_eq);  // AND_Gate
  Multiplexer #(.width(8), .enable("false")) multiplexer_2 (
    .in0(8'h58), .in1(8'ha0), .out(multiplexer_2_out), .sel(\气泡 ));
  or or_1 (or_1_out, and_20_out[1], and_19_out[1]);
  or or_2 (or_2_out, and_19_out[0], and_20_out[0]);
  and and_21 (and_21_out, or_2_out, MemMemToReg);
  and and_22 (and_22_out, or_1_out, ExMemToReg);
  Multiplexer #(.select(2), .width(2), .enable("false")) multiplexer_3 (
    .in0(multiplexer_2_out[1:0]), .in1(multiplexer_2_out[3:2]), .in2(multiplexer_2_out[5:4]),
    .in3(multiplexer_2_out[7:6]), .out(R1Select), .sel(and_19_out));
  Multiplexer #(.select(2), .width(2), .enable("false")) multiplexer_4 (
    .in0(multiplexer_2_out[1:0]), .in1(multiplexer_2_out[3:2]), .in2(multiplexer_2_out[5:4]),
    .in3(multiplexer_2_out[7:6]), .out(R2Select), .sel(and_20_out));
  or or_3 (\气泡 , and_21_out, and_22_out);
endmodule

module \单周期MIPS_单级中断  (
  input  IR1,
  input  IR2,
  input  IR3,
  output RegWrite,
  output MemWrite,
  output [31:0] PC,
  output [31:0] IR,
  output [31:0] RDin,
  output [31:0] MDin,
  output [31:0] LedData
);

  wire and_1_out, and_2_out, and_3_out, and_4_out, and_5_out, and_6_out, BranchJump, CLK, comparator_1_eq,
       demultiplexer_1_out0, demultiplexer_1_out1, demultiplexer_2_out1, demultiplexer_2_out2,
       demultiplexer_2_out3, Go, IE_qn, IR1_t, IR2_t, IR3_t, IRA, IRB, IRC, ITR, JAL, JALJMPJump,
       mips_alu_1_equal, multiplexer_7_out, NormalJump, not_2_out, or_2_out, or_5_out, or_8_out, PCEnable,
       priority_encoder_1_gs, register_1_q, RegJump, RST, SignedExt, Syscall, W1, W2, W3,
       \单周期硬布线控制器_1_alu_src , \单周期硬布线控制器_1_beq , \单周期硬布线控制器_1_blez , \单周期硬布线控制器_1_bne , \单周期硬布线控制器_1_eret ,
       \单周期硬布线控制器_1_jmp , \单周期硬布线控制器_1_mfc0 , \单周期硬布线控制器_1_mtc0 , \单周期硬布线控制器_1_readmode ,
       \单周期硬布线控制器_1_regdst ;
  wire [0:0] IE_q;
  wire [1:0] priority_encoder_1_out, register_4_q, \单周期硬布线控制器_1_memtoreg ;
  wire [2:0] IMW_q;
  wire [3:0] \单周期硬布线控制器_1_alu_op ;
  wire [4:0] multiplexer_2_out, multiplexer_4_out;
  wire [7:0] multiplexer_8_out, ram_1_data, ram_2_data, ram_3_data, ram_4_data;
  wire [9:0] multiplexer_3_out;
  wire [15:0] \总周期数 ;
  wire [27:0] NextPC;
  wire [31:0] bit_extender_1_out, bit_extender_2_out, bit_extender_3_out, bit_extender_4_out, BranchAddr,
       controlled_buffer_1_out, controlled_buffer_2_out, EPC_q, INTFunction, JMPJALAddress,
       mips_alu_1_result, multiplexer_1_out, multiplexer_5_out, multiplexer_6_out, multiplexer_10_out,
       multiplexer_11_out, multiplexer_12_out, R1, shifter_2_out;
  wire [31:28] shifter_1_out;

  Clock clock_1 (.out(CLK));
  Button _1 (.out(IRA));
  Button _2 (.out(IRB));
  Button _3 (.out(IRC));
  Button \u_继续运行  (.out(Go));
  LED led_1 (.in(W1));
  LED led_2 (.in(W2));
  LED led_3 (.in(W3));
  assign controlled_buffer_1_out = ITR ? INTFunction : 32'bz;  // Controlled_Buffer controlled_buffer_1
  Multiplexer #(.width(32), .enable("false")) multiplexer_1 (
    .in0(controlled_buffer_2_out), .in1(controlled_buffer_1_out), .out(multiplexer_1_out), .sel(ITR));
  Hex_Digit_Display hex_digit_display_1 (.value(LedData[31:28]));  // open: dp
  assign controlled_buffer_2_out = \单周期硬布线控制器_1_eret  ? EPC_q : 32'bz;  // Controlled_Buffer controlled_buffer_2
  Register #(.width(32)) u_PC (.D(multiplexer_1_out), .en(PCEnable), .Q(PC), .clk(CLK), .clr(RST));
  Hex_Digit_Display hex_digit_display_2 (.value(LedData[27:24]));  // open: dp
  Hex_Digit_Display hex_digit_display_3 (.value(LedData[23:20]));  // open: dp
  Register #(.width(32)) EPC (.D(controlled_buffer_2_out), .en(ITR), .Q(EPC_q), .clk(CLK));  // open: clr
  Hex_Digit_Display hex_digit_display_4 (.value(LedData[19:16]));  // open: dp
  Hex_Digit_Display hex_digit_display_5 (.value(LedData[15:12]));  // open: dp
  Comparator #(.width(32)) comparator_1 (.a(MDin), .b(32'h22), .eq(comparator_1_eq));  // open: gt, lt
  assign controlled_buffer_2_out = JALJMPJump ? JMPJALAddress : 32'bz;  // Controlled_Buffer controlled_buffer_3
  assign controlled_buffer_2_out = RegJump ? R1 : 32'bz;  // Controlled_Buffer controlled_buffer_4
  assign controlled_buffer_2_out = BranchJump ? BranchAddr : 32'bz;  // Controlled_Buffer controlled_buffer_5
  assign controlled_buffer_2_out = NormalJump ? {JMPJALAddress[31:28], NextPC} : 32'bz;  // Controlled_Buffer controlled_buffer_6
  Adder #(.width(32)) adder_1 (.a(PC), .b(32'h4), .out({JMPJALAddress[31:28], NextPC}));  // open: cin, cout
  Hex_Digit_Display hex_digit_display_6 (.value(LedData[11:8]));  // open: dp
  Hex_Digit_Display hex_digit_display_7 (.value(LedData[7:4]));  // open: dp
  // Probe on \总周期数 
  and and_1 (and_1_out, Syscall, comparator_1_eq);
  and and_2 (and_2_out, Syscall, ~comparator_1_eq);  // AND_Gate
  nor nor_1 (NormalJump, RegJump, JALJMPJump, BranchJump, \单周期硬布线控制器_1_eret );
  Hex_Digit_Display hex_digit_display_8 (.value(LedData[3:0]));  // open: dp
  Register #(.width(1)) register_1 (.D(and_2_out), .en(PCEnable), .Q(register_1_q), .clk(CLK), .clr(or_2_out));
  or or_1 (JALJMPJump, JAL, \单周期硬布线控制器_1_jmp );
  ROM #(.addrWidth(10), .dataWidth(32)) rom_1 (.addr(PC[11:2]), .data(IR));  // open: sel
  Register #(.width(32)) register_2 (.D(R1), .en(and_1_out), .Q(LedData), .clk(CLK), .clr(RST));
  not not_1 (PCEnable, register_1_q);
  or or_2 (or_2_out, Go, RST);
  not not_2 (not_2_out, PCEnable);
  Multiplexer #(.width(5), .enable("false")) multiplexer_2 (
    .in0(IR[20:16]), .in1(IR[15:11]), .out(multiplexer_2_out), .sel(\单周期硬布线控制器_1_regdst ));
  or or_3 (IR1_t, IR1, IRA);
  \单周期硬布线控制器  \u_单周期硬布线控制器_1  (
    .Func(IR[5:0]), .OP(IR[31:26]), .ALU_OP(\单周期硬布线控制器_1_alu_op ), .MemToReg(\单周期硬布线控制器_1_memtoreg [0]),
    .MemWrite(MemWrite), .ALU_SRC(\单周期硬布线控制器_1_alu_src ), .RegWrite(RegWrite), .SysCALL(Syscall),
    .SignedExt(SignedExt), .RegDst(\单周期硬布线控制器_1_regdst ), .JR(RegJump), .JMP(\单周期硬布线控制器_1_jmp ),
    .Beq(\单周期硬布线控制器_1_beq ), .JAL(JAL), .Bne(\单周期硬布线控制器_1_bne ), .\使能端 (not_2_out), .MF(IR[25:21]),
    .MFC0(\单周期硬布线控制器_1_mfc0 ), .MTC0(\单周期硬布线控制器_1_mtc0 ), .ERET(\单周期硬布线控制器_1_eret ),
    .BLEZ(\单周期硬布线控制器_1_blez ), .ReadMode(\单周期硬布线控制器_1_readmode ));
  Multiplexer #(.width(10), .enable("false")) multiplexer_3 (
    .in0({IR[20:16], IR[25:21]}), .in1(10'h44), .out(multiplexer_3_out), .sel(Syscall));
  Multiplexer #(.width(5), .enable("false")) multiplexer_4 (
    .in0(multiplexer_2_out), .in1({5{1'b1}}), .out(multiplexer_4_out), .sel(JAL));
  assign bit_extender_1_out = {{16{1'b0}}, IR[15:0]};  // Bit_Extender bit_extender_1
  assign bit_extender_2_out = {{16{IR[15]}}, IR[15:0]};  // Bit_Extender bit_extender_2
  assign bit_extender_3_out = {{6{IR[25]}}, IR[25:0]};  // Bit_Extender bit_extender_3
  Shifter #(.width(32)) shifter_1 (
    .in(bit_extender_3_out), .\dist (5'b00010), .out({shifter_1_out, JMPJALAddress[27:0]}));
  or or_4 (IR2_t, IR2, IRB);
  or or_5 (or_5_out, mips_alu_1_result[0], mips_alu_1_equal);
  Multiplexer #(.width(32), .enable("false")) multiplexer_5 (
    .in0(bit_extender_1_out), .in1(bit_extender_2_out), .out(multiplexer_5_out), .sel(SignedExt));
  Shifter #(.width(32)) shifter_2 (.in(bit_extender_2_out), .\dist (5'b00010), .out(shifter_2_out));
  and and_3 (and_3_out, or_5_out, \单周期硬布线控制器_1_blez );
  and and_4 (and_4_out, mips_alu_1_equal, \单周期硬布线控制器_1_beq );
  and and_5 (and_5_out, ~mips_alu_1_equal, \单周期硬布线控制器_1_bne );  // AND_Gate
  MIPS_Regifile mips_regifile_1 (
    .Din(RDin), .Clk(CLK), .R1(R1), .R2(MDin), .WE(RegWrite), .W_num(multiplexer_4_out),
    .R1_num(multiplexer_3_out[4:0]), .R2_num(multiplexer_3_out[9:5]));
  Adder #(.width(32)) adder_2 (
    .a({JMPJALAddress[31:28], NextPC}), .b(shifter_2_out), .out(BranchAddr));  // open: cin, cout
  or or_6 (IR3_t, IR3, IRC);
  or or_7 (BranchJump, and_3_out, and_4_out, and_5_out);
  Multiplexer #(.width(32), .enable("false")) multiplexer_6 (
    .in0(MDin), .in1(multiplexer_5_out), .out(multiplexer_6_out), .sel(\单周期硬布线控制器_1_alu_src ));
  Demultiplexer #(.enable("false")) demultiplexer_1 (
    .out0(demultiplexer_1_out0), .out1(demultiplexer_1_out1), .in(\单周期硬布线控制器_1_mtc0 ), .sel(IR[11]));
  MIPS_ALU mips_alu_1 (
    .X(R1), .Y(multiplexer_6_out), .AluOP(\单周期硬布线控制器_1_alu_op ), .Equal(mips_alu_1_equal),
    .Result(mips_alu_1_result), .shamt(IR[10:6]));  // open: Result_2
  or or_8 (or_8_out, demultiplexer_1_out0, \单周期硬布线控制器_1_eret );
  D_Flip_Flop d_ff_1 (.clk(CLK), .D(1'b0), .Q(W1), .preset(IR1_t), .en(demultiplexer_2_out1));  // open: Qn, reset
  D_Flip_Flop d_ff_2 (.clk(CLK), .D(1'b0), .Q(W2), .preset(IR2_t), .en(demultiplexer_2_out2));  // open: Qn, reset
  D_Flip_Flop d_ff_3 (.clk(CLK), .D(1'b0), .Q(W3), .preset(IR3_t), .en(demultiplexer_2_out3));  // open: Qn, reset
  D_Flip_Flop IE (
    .clk(CLK), .D(multiplexer_7_out), .Q(IE_q[0]), .Qn(IE_qn), .preset(ITR), .en(or_8_out));  // open: reset
  Multiplexer #(.enable("false")) multiplexer_7 (
    .in0(MDin[0]), .in1(1'b0), .out(multiplexer_7_out), .sel(\单周期硬布线控制器_1_eret ));
  RAM #(.addrWidth(10), .bus("separate")) ram_1 (
    .addr(mips_alu_1_result[11:2]), .din(MDin[7:0]), .data(ram_1_data), .str(MemWrite), .clk(CLK), .clr(RST));  // open: sel, ld
  RAM #(.addrWidth(10), .bus("separate")) ram_2 (
    .addr(mips_alu_1_result[11:2]), .din(MDin[15:8]), .data(ram_2_data), .str(MemWrite), .clk(CLK), .clr(RST));  // open: sel, ld
  Priority_Encoder #(.select(2)) priority_encoder_1 (
    .in0(1'b0), .in1(W1), .in2(W2), .in3(W3), .out(priority_encoder_1_out), .gs(priority_encoder_1_gs));  // open: en_out, en_in
  Demultiplexer #(.select(2), .enable("false")) demultiplexer_2 (
    .out1(demultiplexer_2_out1), .out2(demultiplexer_2_out2), .out3(demultiplexer_2_out3),
    .in(\单周期硬布线控制器_1_eret ), .sel(register_4_q));  // open: out0
  and and_6 (and_6_out, priority_encoder_1_gs, PCEnable, IE_qn);
  Register #(.width(1), .trigger("falling")) register_3 (.D(and_6_out), .Q(ITR), .clk(CLK));  // open: en, clr
  Register #(.width(2), .trigger("falling")) register_4 (
    .D(priority_encoder_1_out), .en(and_6_out), .Q(register_4_q), .clk(CLK));  // open: clr
  Register #(.width(3)) IMW (.D(MDin[2:0]), .en(demultiplexer_1_out1), .Q(IMW_q), .clk(CLK));  // open: clr
  RAM #(.addrWidth(10), .bus("separate")) ram_3 (
    .addr(mips_alu_1_result[11:2]), .din(MDin[23:16]), .data(ram_3_data), .str(MemWrite), .clk(CLK), .clr(RST));  // open: sel, ld
  RAM #(.addrWidth(10), .bus("separate")) ram_4 (
    .addr(mips_alu_1_result[11:2]), .din(MDin[31:24]), .data(ram_4_data), .str(MemWrite), .clk(CLK), .clr(RST));  // open: sel, ld
  assign bit_extender_4_out = {{24{multiplexer_8_out[7]}}, multiplexer_8_out};  // Bit_Extender bit_extender_4
  Multiplexer #(.select(2), .width(8), .enable("false")) multiplexer_8 (
    .in0(ram_1_data), .in1(ram_2_data), .in2(ram_3_data), .in3(ram_4_data), .out(multiplexer_8_out),
    .sel(mips_alu_1_result[1:0]));
  Button button_1 (.out(RST));
  Multiplexer #(.select(2), .width(32), .enable("false")) multiplexer_9 (
    .in0(32'h30ac), .in1(32'h30ac), .in2(32'h3150), .in3(32'h31f4), .out(INTFunction),
    .sel(priority_encoder_1_out));
  Multiplexer #(.width(32), .enable("false")) multiplexer_10 (
    .in0({{31{1'b0}}, IE_q[0]}), .in1({{29{1'b0}}, IMW_q}), .out(multiplexer_10_out), .sel(IR[11]));
  or or_9 (\单周期硬布线控制器_1_memtoreg [1], \单周期硬布线控制器_1_mfc0 , JAL);
  Multiplexer #(.width(32), .enable("false")) multiplexer_11 (
    .in0({ram_4_data, ram_3_data, ram_2_data, ram_1_data}), .in1(bit_extender_4_out),
    .out(multiplexer_11_out), .sel(\单周期硬布线控制器_1_readmode ));
  Multiplexer #(.width(32), .enable("false")) multiplexer_12 (
    .in0(multiplexer_10_out), .in1({JMPJALAddress[31:28], NextPC}), .out(multiplexer_12_out), .sel(JAL));
  Multiplexer #(.select(2), .width(32), .enable("false")) multiplexer_13 (
    .in0(mips_alu_1_result), .in1(multiplexer_11_out), .in2(multiplexer_12_out), .in3(multiplexer_12_out),
    .out(RDin), .sel(\单周期硬布线控制器_1_memtoreg ));

  // Other names for the same wires on the sheet: Rd = IR[11]; NextPC[31:28] = JMPJALAddress[31:28]; R2[31:0] = MDin

  // Notes on the sheet:
  //   中断源
  //   中断等待指示
  //   总复位信号应将除ROM以外所有存储组件全部清零
  //   数码管输出
  //   数码管输出应该用寄存器锁存，否则显示数据只能一闪而过
  //   指令存储器
  //   rs
  //   指令字
  //   rt
  //   contents of rom_1 (hex, n*v repeats v):
  //   201d07d0 20100001 109fc0 139fc3 8021 2012000c 24160008 26100001 3210000f 20080008 20090001 139900
  //   2709825 132020 20020022 c 1094022 1500fff9 22100001 2018000f 2188024 108700 20080008 20090001 139902
  //   2709825 132021 20020022 c 1094022 1500fff9 108702 2c9b022 12c00001 8000c07 4020 1084027 84400
  //   3508ffff 82021 20020022 c 8000c01 afa20000 23bd0004 afa40000 23bd0004 afb00000 23bd0004 afb30000
  //   23bd0004 afb40000 23bd0004 afb50000 23bd0004 afb60000 23bd0004 20160001 20140003 20150001 168020
  //   108100 2149825 132020 20020022 c 1600fffa 295a022 1680fff7 23bdfffc 8fb60000 23bdfffc 8fb50000
  //   23bdfffc 8fb40000 23bdfffc 8fb30000 23bdfffc 8fb00000 23bdfffc 8fa40000 23bdfffc 8fa20000 42000018
  //   afa20000 23bd0004 afa40000 23bd0004 afb00000 23bd0004 afb30000 23bd0004 afb40000 23bd0004 afb50000
  //   23bd0004 afb60000 23bd0004 20160002 20140003 20150001 168020 108100 2149825 132020 20020022 c
  //   1600fffa 295a022 1680fff7 23bdfffc 8fb60000 23bdfffc 8fb50000 23bdfffc 8fb40000 23bdfffc 8fb30000
  //   23bdfffc 8fb00000 23bdfffc 8fa40000 23bdfffc 8fa20000 42000018 afa20000 23bd0004 afa40000 23bd0004
  //   afb00000 23bd0004 afb30000 23bd0004 afb40000 23bd0004 afb50000 23bd0004 afb60000 23bd0004 20160003
  //   20140003 20150001 168020 108100 2149825 132020 20020022 c 1600fffa 295a022 1680fff7 23bdfffc
  //   8fb60000 23bdfffc 8fb50000 23bdfffc 8fb40000 23bdfffc 8fb30000 23bdfffc 8fb00000 23bdfffc 8fa40000
  //   23bdfffc 8fa20000 42000018
  //   rd
  //   JMP
  //   JR
  //   OP
  //   OP
  //   Func
  //   Func
  //   Beq
  //   Bne
  //   MemToReg
  //   MemWrite
  //   AluOP
  //   AluSrcB
  //   RegWrite
  //   JAL
  //   RegDst
  //   为方便自动评测，需要输出PC，IR，寄存器堆写如数据RDin
  //   RAM写使能MemWrite、RAM写入数据MDin等信号
endmodule

module \单周期MIPS_多级中断  (
  input  IR1,
  input  IR2,
  input  IR3,
  output RegWrite,
  output MemWrite,
  output [31:0] PC,
  output [31:0] IR,
  output [31:0] RDin,
  output [31:0] MDin,
  output [31:0] LedData
);

  wire and_1_out, and_2_out, and_3_out, and_4_out, and_5_out, and_6_out, and_7_out, and_8_out, and_9_out,
       BranchJump, CLK, comparator_1_eq, demultiplexer_1_out0, demultiplexer_1_out1, demultiplexer_2_out1,
       demultiplexer_2_out2, demultiplexer_2_out3, demultiplexer_3_out1, demultiplexer_3_out2,
       demultiplexer_3_out3, Go, IE_qn, IR1_t, IR2_t, IR3_t, IRA, IRB, IRC, ITR, JAL, JALJMPJump,
       mips_alu_1_equal, NormalJump, not_2_out, or_2_out, or_5_out, or_8_out, or_9_out, or_10_out, PCEnable,
       priority_encoder_1_en_out, priority_encoder_1_gs, register_2_q, RegJump, RST, SignedExt, Syscall, W1,
       W2, W3, \单周期硬布线控制器_1_alu_src , \单周期硬布线控制器_1_beq , \单周期硬布线控制器_1_blez , \单周期硬布线控制器_1_bne ,
       \单周期硬布线控制器_1_eret , \单周期硬布线控制器_1_jmp , \单周期硬布线控制器_1_mfc0 , \单周期硬布线控制器_1_mtc0 , \单周期硬布线控制器_1_readmode ,
       \单周期硬布线控制器_1_regdst ;
  wire [0:0] IE_q;
  wire [1:0] multiplexer_9_out, multiplexer_16_out, NewState, NowState, register_6_q, register_7_q,
       register_8_q, \单周期硬布线控制器_1_memtoreg ;
  wire [2:0] multiplexer_7_out;
  wire [3:0] \单周期硬布线控制器_1_alu_op ;
  wire [4:0] multiplexer_2_out, multiplexer_4_out;
  wire [7:0] multiplexer_11_out, ram_1_data, ram_2_data, ram_3_data, ram_4_data;
  wire [9:0] multiplexer_3_out;
  wire [15:0] adder_1_out, \总周期数 ;
  wire [27:0] NextPC;
  wire [31:0] bit_extender_1_out, bit_extender_2_out, bit_extender_3_out, bit_extender_4_out, BranchAddr,
       controlled_buffer_1_out, EPC, INTFunction, JMPJALAddress, mips_alu_1_result, multiplexer_1_out,
       multiplexer_5_out, multiplexer_6_out, multiplexer_8_out, multiplexer_10_out, multiplexer_12_out,
       multiplexer_13_out, NextJumpPC, R1, shifter_2_out;
  wire [31:28] shifter_1_out;

  Clock clock_1 (.out(CLK));
  Button _1 (.out(IRA));
  Button _2 (.out(IRB));
  Button _3 (.out(IRC));
  Button \u_继续运行  (.out(Go));
  LED led_1 (.in(W1));
  LED led_2 (.in(W2));
  LED led_3 (.in(W3));
  Multiplexer #(.width(32), .enable("false")) multiplexer_1 (
    .in0(NextJumpPC), .in1(controlled_buffer_1_out), .out(multiplexer_1_out), .sel(ITR));
  Hex_Digit_Display hex_digit_display_1 (.value(LedData[31:28]));  // open: dp
  Register #(.width(16)) register_1 (.D(adder_1_out), .en(PCEnable), .Q(\总周期数 ), .clk(CLK), .clr(RST));
  assign controlled_buffer_1_out = ITR ? INTFunction : 32'bz;  // Controlled_Buffer controlled_buffer_1
  assign NextJumpPC = \单周期硬布线控制器_1_eret  ? EPC : 32'bz;  // Controlled_Buffer controlled_buffer_2
  Register #(.width(32)) u_PC (.D(multiplexer_1_out), .en(PCEnable), .Q(PC), .clk(CLK), .clr(RST));
  Hex_Digit_Display hex_digit_display_2 (.value(LedData[23:20]));  // open: dp
  Hex_Digit_Display hex_digit_display_3 (.value(LedData[27:24]));  // open: dp
  Adder #(.width(16)) adder_1 (.a(16'h1), .b(\总周期数 ), .out(adder_1_out));  // open: cin, cout
  Hex_Digit_Display hex_digit_display_4 (.value(LedData[19:16]));  // open: dp
  Hex_Digit_Display hex_digit_display_5 (.value(LedData[15:12]));  // open: dp
  Comparator #(.width(32)) comparator_1 (.a(MDin), .b(32'h22), .eq(comparator_1_eq));  // open: gt, lt
  assign NextJumpPC = JALJMPJump ? JMPJALAddress : 32'bz;  // Controlled_Buffer controlled_buffer_3
  assign NextJumpPC = RegJump ? R1 : 32'bz;  // Controlled_Buffer controlled_buffer_4
  assign NextJumpPC = BranchJump ? BranchAddr : 32'bz;  // Controlled_Buffer controlled_buffer_5
  assign NextJumpPC = NormalJump ? {JMPJALAddress[31:28], NextPC} : 32'bz;  // Controlled_Buffer controlled_buffer_6
  Adder #(.width(32)) adder_2 (.a(PC), .b(32'h4), .out({JMPJALAddress[31:28], NextPC}));  // open: cin, cout
  Hex_Digit_Display hex_digit_display_6 (.value(LedData[11:8]));  // open: dp
  Hex_Digit_Display hex_digit_display_7 (.value(LedData[7:4]));  // open: dp
  // Probe on \总周期数 
  Hex_Digit_Display hex_digit_display_8 (.value(LedData[3:0]));  // open: dp
  and and_1 (and_1_out, Syscall, comparator_1_eq);
  and and_2 (and_2_out, Syscall, ~comparator_1_eq);  // AND_Gate
  Register #(.width(1)) register_2 (.D(and_2_out), .en(PCEnable), .Q(register_2_q), .clk(CLK), .clr(or_2_out));
  nor nor_1 (NormalJump, RegJump, JALJMPJump, BranchJump, \单周期硬布线控制器_1_eret );
  or or_1 (JALJMPJump, JAL, \单周期硬布线控制器_1_jmp );
  ROM #(.addrWidth(10), .dataWidth(32)) rom_1 (.addr(PC[11:2]), .data(IR));  // open: sel
  Register #(.width(32)) register_3 (.D(R1), .en(and_1_out), .Q(LedData), .clk(CLK), .clr(RST));
  not not_1 (PCEnable, register_2_q);
  or or_2 (or_2_out, Go, RST);
  not not_2 (not_2_out, PCEnable);
  Multiplexer #(.width(5), .enable("false")) multiplexer_2 (
    .in0(IR[20:16]), .in1(IR[15:11]), .out(multiplexer_2_out), .sel(\单周期硬布线控制器_1_regdst ));
  or or_3 (IR1_t, IR1, IRA);
  Button button_1 (.out(RST));
  \单周期硬布线控制器  \u_单周期硬布线控制器_1  (
    .Func(IR[5:0]), .OP(IR[31:26]), .ALU_OP(\单周期硬布线控制器_1_alu_op ), .MemToReg(\单周期硬布线控制器_1_memtoreg [0]),
    .MemWrite(MemWrite), .ALU_SRC(\单周期硬布线控制器_1_alu_src ), .RegWrite(RegWrite), .SysCALL(Syscall),
    .SignedExt(SignedExt), .RegDst(\单周期硬布线控制器_1_regdst ), .JR(RegJump), .JMP(\单周期硬布线控制器_1_jmp ),
    .Beq(\单周期硬布线控制器_1_beq ), .JAL(JAL), .Bne(\单周期硬布线控制器_1_bne ), .\使能端 (not_2_out), .MF(IR[25:21]),
    .MFC0(\单周期硬布线控制器_1_mfc0 ), .MTC0(\单周期硬布线控制器_1_mtc0 ), .ERET(\单周期硬布线控制器_1_eret ),
    .BLEZ(\单周期硬布线控制器_1_blez ), .ReadMode(\单周期硬布线控制器_1_readmode ));
  Multiplexer #(.width(10), .enable("false")) multiplexer_3 (
    .in0({IR[20:16], IR[25:21]}), .in1(10'h44), .out(multiplexer_3_out), .sel(Syscall));
  Multiplexer #(.width(5), .enable("false")) multiplexer_4 (
    .in0(multiplexer_2_out), .in1({5{1'b1}}), .out(multiplexer_4_out), .sel(JAL));
  assign bit_extender_1_out = {{16{1'b0}}, IR[15:0]};  // Bit_Extender bit_extender_1
  assign bit_extender_2_out = {{16{IR[15]}}, IR[15:0]};  // Bit_Extender bit_extender_2
  assign bit_extender_3_out = {{6{IR[25]}}, IR[25:0]};  // Bit_Extender bit_extender_3
  Shifter #(.width(32)) shifter_1 (
    .in(bit_extender_3_out), .\dist (5'b00010), .out({shifter_1_out, JMPJALAddress[27:0]}));
  or or_4 (IR2_t, IR2, IRB);
  or or_5 (or_5_out, mips_alu_1_result[0], mips_alu_1_equal);
  Multiplexer #(.width(32), .enable("false")) multiplexer_5 (
    .in0(bit_extender_1_out), .in1(bit_extender_2_out), .out(multiplexer_5_out), .sel(SignedExt));
  Shifter #(.width(32)) shifter_2 (.in(bit_extender_2_out), .\dist (5'b00010), .out(shifter_2_out));
  and and_3 (and_3_out, or_5_out, \单周期硬布线控制器_1_blez );
  and and_4 (and_4_out, mips_alu_1_equal, \单周期硬布线控制器_1_beq );
  and and_5 (and_5_out, ~mips_alu_1_equal, \单周期硬布线控制器_1_bne );  // AND_Gate
  MIPS_Regifile mips_regifile_1 (
    .Din(RDin), .Clk(CLK), .R1(R1), .R2(MDin), .WE(RegWrite), .W_num(multiplexer_4_out),
    .R1_num(multiplexer_3_out[4:0]), .R2_num(multiplexer_3_out[9:5]));
  Adder #(.width(32)) adder_3 (
    .a({JMPJALAddress[31:28], NextPC}), .b(shifter_2_out), .out(BranchAddr));  // open: cin, cout
  or or_6 (IR3_t, IR3, IRC);
  or or_7 (BranchJump, and_3_out, and_4_out, and_5_out);
  Multiplexer #(.width(32), .enable("false")) multiplexer_6 (
    .in0(MDin), .in1(multiplexer_5_out), .out(multiplexer_6_out), .sel(\单周期硬布线控制器_1_alu_src ));
  Multiplexer #(.select(2), .width(3), .enable("false")) multiplexer_7 (
    .in0(3'b111), .in1(3'b110), .in2(3'b100), .in3(3'b000), .out(multiplexer_7_out), .sel(NowState));
  Demultiplexer #(.enable("false")) demultiplexer_1 (
    .out0(demultiplexer_1_out0), .out1(demultiplexer_1_out1), .in(\单周期硬布线控制器_1_mtc0 ), .sel(IR[12]));
  MIPS_ALU mips_alu_1 (
    .X(R1), .Y(multiplexer_6_out), .AluOP(\单周期硬布线控制器_1_alu_op ), .Equal(mips_alu_1_equal),
    .Result(mips_alu_1_result), .shamt(IR[10:6]));  // open: Result_2
  D_Flip_Flop d_ff_1 (.clk(CLK), .D(1'b0), .Q(W1), .preset(IR1_t), .en(demultiplexer_2_out1));  // open: Qn, reset
  D_Flip_Flop d_ff_2 (.clk(CLK), .D(1'b0), .Q(W2), .preset(IR2_t), .en(demultiplexer_2_out2));  // open: Qn, reset
  D_Flip_Flop d_ff_3 (.clk(CLK), .D(1'b0), .Q(W3), .preset(IR3_t), .en(demultiplexer_2_out3));  // open: Qn, reset
  and and_6 (and_6_out, multiplexer_7_out[0], W1);
  and and_7 (and_7_out, multiplexer_7_out[1], W2);
  Demultiplexer #(.select(2), .enable("false")) demultiplexer_2 (
    .out1(demultiplexer_2_out1), .out2(demultiplexer_2_out2), .out3(demultiplexer_2_out3),
    .in(\单周期硬布线控制器_1_eret ), .sel(NowState));  // open: out0
  and and_8 (and_8_out, multiplexer_7_out[2], W3);
  Multiplexer #(.width(32), .enable("false")) multiplexer_8 (
    .in0(NextJumpPC), .in1(MDin), .out(multiplexer_8_out), .sel(\单周期硬布线控制器_1_mtc0 ));
  or or_8 (or_8_out, demultiplexer_1_out1, ITR);
  or or_9 (or_9_out, demultiplexer_1_out0, \单周期硬布线控制器_1_eret );
  assign NewState = priority_encoder_1_en_out ? 2'b00 : 2'bz;  // Controlled_Buffer controlled_buffer_7
  Priority_Encoder #(.select(2)) priority_encoder_1 (
    .in0(1'b0), .in1(and_6_out), .in2(and_7_out), .in3(and_8_out), .out(NewState),
    .gs(priority_encoder_1_gs), .en_out(priority_encoder_1_en_out));  // open: en_in
  D_Flip_Flop IE (.clk(CLK), .D(MDin[0]), .Q(IE_q[0]), .Qn(IE_qn), .preset(ITR), .en(or_9_out));  // open: reset
  RAM #(.addrWidth(10), .bus("separate")) ram_1 (
    .addr(mips_alu_1_result[11:2]), .din(MDin[7:0]), .data(ram_1_data), .str(MemWrite), .clk(CLK), .clr(RST));  // open: sel, ld
  RAM #(.addrWidth(10), .bus("separate")) ram_2 (
    .addr(mips_alu_1_result[11:2]), .din(MDin[15:8]), .data(ram_2_data), .str(MemWrite), .clk(CLK), .clr(RST));  // open: sel, ld
  and and_9 (and_9_out, priority_encoder_1_gs, IE_qn, PCEnable);
  Multiplexer #(.width(2), .enable("false")) multiplexer_9 (
    .in0(NewState), .in1(multiplexer_16_out), .out(multiplexer_9_out), .sel(\单周期硬布线控制器_1_eret ));
  Register #(.width(32)) u_EPC (.D(multiplexer_8_out), .en(or_8_out), .Q(EPC), .clk(CLK));  // open: clr
  Demultiplexer #(.select(2), .enable("false")) demultiplexer_3 (
    .out1(demultiplexer_3_out1), .out2(demultiplexer_3_out2), .out3(demultiplexer_3_out3), .in(ITR),
    .sel(NewState));  // open: out0
  or or_10 (or_10_out, ITR, \单周期硬布线控制器_1_eret );
  Multiplexer #(.width(32), .enable("false")) multiplexer_10 (
    .in0({{31{1'b0}}, IE_q[0]}), .in1(EPC), .out(multiplexer_10_out), .sel(IR[12]));
  RAM #(.addrWidth(10), .bus("separate")) ram_3 (
    .addr(mips_alu_1_result[11:2]), .din(MDin[23:16]), .data(ram_3_data), .str(MemWrite), .clk(CLK), .clr(RST));  // open: sel, ld
  RAM #(.addrWidth(10), .bus("separate")) ram_4 (
    .addr(mips_alu_1_result[11:2]), .din(MDin[31:24]), .data(ram_4_data), .str(MemWrite), .clk(CLK), .clr(RST));  // open: sel, ld
  Multiplexer #(.select(2), .width(8), .enable("false")) multiplexer_11 (
    .in0(ram_1_data), .in1(ram_2_data), .in2(ram_3_data), .in3(ram_4_data), .out(multiplexer_11_out),
    .sel(mips_alu_1_result[1:0]));
  Register #(.width(1), .trigger("falling")) register_4 (.D(and_9_out), .Q(ITR), .clk(CLK));  // open: en, clr
  Register #(.width(2)) register_5 (.D(multiplexer_9_out), .en(or_10_out), .Q(NowState), .clk(CLK));  // open: clr
  assign bit_extender_4_out = {{24{multiplexer_11_out[7]}}, multiplexer_11_out};  // Bit_Extender bit_extender_4
  or or_11 (\单周期硬布线控制器_1_memtoreg [1], \单周期硬布线控制器_1_mfc0 , JAL);
  Multiplexer #(.width(32), .enable("false")) multiplexer_12 (
    .in0({ram_4_data, ram_3_data, ram_2_data, ram_1_data}), .in1(bit_extender_4_out),
    .out(multiplexer_12_out), .sel(\单周期硬布线控制器_1_readmode ));
  Multiplexer #(.width(32), .enable("false")) multiplexer_13 (
    .in0(multiplexer_10_out), .in1({JMPJALAddress[31:28], NextPC}), .out(multiplexer_13_out), .sel(JAL));
  Register #(.width(2)) register_6 (.D(NowState), .en(demultiplexer_3_out1), .Q(register_6_q), .clk(CLK));  // open: clr
  Register #(.width(2)) register_7 (.D(NowState), .en(demultiplexer_3_out2), .Q(register_7_q), .clk(CLK));  // open: clr
  Register #(.width(2)) register_8 (.D(NowState), .en(demultiplexer_3_out3), .Q(register_8_q), .clk(CLK));  // open: clr
  Multiplexer #(.select(2), .width(32), .enable("false")) multiplexer_14 (
    .in0(mips_alu_1_result), .in1(multiplexer_12_out), .in2(multiplexer_13_out), .in3(multiplexer_13_out),
    .out(RDin), .sel(\单周期硬布线控制器_1_memtoreg ));
  Multiplexer #(.select(2), .width(32), .enable("false")) multiplexer_15 (
    .in0(32'h30ac), .in1(32'h30ac), .in2(32'h3174), .in3(32'h323c), .out(INTFunction), .sel(NewState));
  Multiplexer #(.select(2), .width(2), .enable("false")) multiplexer_16 (
    .in0(register_6_q), .in1(register_6_q), .in2(register_7_q), .in3(register_8_q), .out(multiplexer_16_out),
    .sel(NowState));

  // Other names for the same wires on the sheet: Rd = IR[12]; NextPC[31:28] = JMPJALAddress[31:28]; R2[31:0] = MDin

  // Notes on the sheet:
  //   中断源
  //   中断等待指示
  //   总复位信号应将除ROM以外所有存储组件全部清零
  //   数码管输出
  //   数码管输出应该用寄存器锁存，否则显示数据只能一闪而过
  //   指令存储器
  //   指令字
  //   contents of rom_1 (hex, n*v repeats v):
  //   201d07d0 20100001 109fc0 139fc3 8021 2012000c 24160008 26100001 3210000f 20080008 20090001 139900
  //   2709825 132020 20020022 c 1094022 1500fff9 22100001 2018000f 2188024 108700 20080008 20090001 139902
  //   2709825 132021 20020022 c 1094022 1500fff9 108702 2c9b022 12c00001 8000c07 4020 1084027 84400
  //   3508ffff 82021 20020022 c 8000c01 afa20000 23bd0004 afa40000 23bd0004 afb00000 23bd0004 afb30000
  //   23bd0004 afb40000 23bd0004 afb50000 23bd0004 afb60000 23bd0004 40167000 afb60000 23bd0004 40806000
  //   20160001 20140003 20150001 168020 108100 2149825 132020 20020022 c 1600fffa 295a022 1680fff7
  //   20160001 40966000 23bdfffc 8fb60000 40967000 23bdfffc 8fb60000 23bdfffc 8fb50000 23bdfffc 8fb40000
  //   23bdfffc 8fb30000 23bdfffc 8fb00000 23bdfffc 8fa40000 23bdfffc 8fa20000 42000018 afa20000 23bd0004
  //   afa40000 23bd0004 afb00000 23bd0004 afb30000 23bd0004 afb40000 23bd0004 afb50000 23bd0004 afb60000
  //   23bd0004 40167000 afb60000 23bd0004 40806000 20160002 20140003 20150001 168020 108100 2149825 132020
  //   20020022 c 1600fffa 295a022 1680fff7 20160001 40966000 23bdfffc 8fb60000 40967000 23bdfffc 8fb60000
  //   23bdfffc 8fb50000 23bdfffc 8fb40000 23bdfffc 8fb30000 23bdfffc 8fb00000 23bdfffc 8fa40000 23bdfffc
  //   8fa20000 42000018 afa20000 23bd0004 afa40000 23bd0004 afb00000 23bd0004 afb30000 23bd0004 afb40000
  //   23bd0004 afb50000 23bd0004 afb60000 23bd0004 40167000 afb60000 23bd0004 40806000 20160003 20140003
  //   20150001 168020 108100 2149825 132020 20020022 c 1600fffa 295a022 1680fff7 20160001 40966000
  //   23bdfffc 8fb60000 40967000 23bdfffc 8fb60000 23bdfffc 8fb50000 23bdfffc 8fb40000 23bdfffc 8fb30000
  //   23bdfffc 8fb00000 23bdfffc 8fa40000 23bdfffc 8fa20000 42000018
  //   JMP
  //   JR
  //   OP
  //   OP
  //   Func
  //   Func
  //   rs
  //   rt
  //   rd
  //   Beq
  //   Bne
  //   AluOP
  //   AluSrcB
  //   RegWrite
  //   JAL
  //   RegDst
  //   MemToReg
  //   MemWrite
  //   为方便自动评测，需要输出PC，IR，寄存器堆写如数据RDin
  //   RAM写使能MemWrite、RAM写入数据MDin等信号
endmodule
